// Logisim project MAINCHIP.circ as structural Verilog: 25 circuits, main circuit main
module TEST (
  input  in_1,
  input  in_2,
  output out_3
);

  and and_1 (out_3, in_1, in_2);
endmodule

module main (
  input  in_1,
  input  in_2,
  input  in_3,
  input  in_4,
  input  in_5,
  input  in_6,
  input  in_7,
  input  in_8,
  input  NOR,
  input  in_10,
  input  in_11,
  input  in_12,
  output out_13,
  output out_14,
  output out_15,
  output out_16,
  output out_17,
  output out_18
);

  wire and_1_out, and_2_out, and_3_out, nand_2_out, nor_2_out, not_1_out, not_2_out, or_2_out, or_3_out;

  // NAND_Gate nand_1 is placed but not wired
  // OR_Gate or_1 is placed but not wired
  // XOR_Gate xor_1 is placed but not wired
  // NOR_Gate nor_1 is placed but not wired
  // XNOR_Gate xnor_1 is placed but not wired
  and and_1 (and_1_out, in_1, in_2);
  not not_1 (not_1_out, in_3);
  not not_2 (not_2_out, in_4);
  or or_2 (or_2_out, in_7, in_8);
  nand nand_2 (nand_2_out, in_7, in_8);
  or or_3 (or_3_out, NOR, in_10);
  and and_2 (and_2_out, in_11, in_12);
  not not_3 (out_13, and_1_out);
  and and_3 (and_3_out, not_1_out, not_2_out);
  and and_4 (out_16, or_2_out, nand_2_out);
  not not_4 (out_17, or_3_out);
  nor nor_2 (nor_2_out, in_11, in_12);
  x16RAM x16ram_1 ();  // open: A65355, in_2, in_3, in_4, in_5, in_6, in_7, in_8, in_9, in_10, in_11, in_12, in_13, in_14, in_15, A1, WRITE, IN7, in_19, in_20, in_21, in_22, in_23, in_24, IN0, OUT0, out_27, out_28, out_29, out_30, out_31, out_32, OUT7
  not not_5 (out_14, and_3_out);
  or or_4 (out_18, nor_2_out, and_2_out);
  D_Flip_Flop d_ff_1 (.D(in_5), .clk(in_6), .Q(out_15));  // open: Qn, preset, reset
  x16ROM x16rom_1 ();  // open: A65355, in_2, in_3, in_4, in_5, in_6, in_7, in_8, in_9, in_10, in_11, in_12, in_13, in_14, in_15, A1, B0, B1, B2
  ADRESSMAP adressmap_1 ();  // open: A65355, in_2, in_3, in_4, in_5, in_6, in_7, in_8, in_9, in_10, in_11, in_12, in_13, in_14, in_15, A1, NEXT_CELL, PREVIOUS_CELL, RESET_TO, UPDATE, B65536, out_22, out_23, out_24, out_25, out_26, out_27, out_28, out_29, out_30, out_31, out_32, out_33, out_34, out_35, B1, OVERFLOW

  // Notes on the sheet:
  //   NAND
  //   OR
  //   XOR
  //   XNOR
endmodule

module ADDER_C (
  input  in_1,
  input  in_2,
  input  carry,
  output sum,
  output carryout
);

  wire and_1_out, and_2_out, xor_1_out;

  xor xor_1 (xor_1_out, in_1, in_2);
  and and_1 (and_1_out, in_1, in_2);
  xor xor_2 (sum, xor_1_out, carry);
  and and_2 (and_2_out, xor_1_out, carry);
  or or_1 (carryout, and_2_out, and_1_out);
endmodule

module b4ADDER (
  input  B8,
  input  in_2,
  input  in_3,
  input  B1,
  input  A8,
  input  in_6,
  input  in_7,
  input  A1,
  input  CARRYIN,
  output C8,
  output out_11,
  output out_12,
  output C1,
  output CARRYOUT
);

  wire adder_c_1_carryout, adder_c_2_carryout, adder_c_3_carryout;

  ADDER_C adder_c_1 (.in_1(B1), .in_2(A1), .carry(CARRYIN), .sum(C1), .carryout(adder_c_1_carryout));
  ADDER_C adder_c_2 (.in_1(in_3), .in_2(in_7), .carry(adder_c_1_carryout), .sum(out_12), .carryout(adder_c_2_carryout));
  ADDER_C adder_c_3 (.in_1(in_2), .in_2(in_6), .carry(adder_c_2_carryout), .sum(out_11), .carryout(adder_c_3_carryout));
  ADDER_C adder_c_4 (.in_1(B8), .in_2(A8), .carry(adder_c_3_carryout), .sum(C8), .carryout(CARRYOUT));
endmodule

module b8PLUS_MINUS (
  input  A128,
  input  in_2,
  input  in_3,
  input  in_4,
  input  in_5,
  input  in_6,
  input  in_7,
  input  A1,
  input  PLUS,
  input  MINUS,
  output OVERFLOW,
  output B128,
  output out_13,
  output out_14,
  output out_15,
  output out_16,
  output out_17,
  output out_18,
  output B1
);

  wire b4adder_1_carryout;

  b4ADDER b4adder_1 (
    .B8(in_5), .in_2(in_6), .in_3(in_7), .B1(A1), .A8(MINUS), .in_6(MINUS), .in_7(MINUS), .A1(MINUS),
    .CARRYIN(PLUS), .C8(out_16), .out_11(out_17), .out_12(out_18), .C1(B1), .CARRYOUT(b4adder_1_carryout));
  b4ADDER b4adder_2 (
    .B8(A128), .in_2(in_2), .in_3(in_3), .B1(in_4), .A8(MINUS), .in_6(MINUS), .in_7(MINUS), .A1(MINUS),
    .CARRYIN(b4adder_1_carryout), .C8(B128), .out_11(out_13), .out_12(out_14), .C1(out_15),
    .CARRYOUT(OVERFLOW));
endmodule

module b16PLUS_MINUS (
  input  A65536,
  input  in_2,
  input  in_3,
  input  in_4,
  input  in_5,
  input  in_6,
  input  in_7,
  input  A256,
  input  A128,
  input  in_10,
  input  in_11,
  input  in_12,
  input  in_13,
  input  in_14,
  input  in_15,
  input  A1,
  input  PLUS,
  input  MINUS,
  output OVERFLOW,
  output b65525,
  output out_21,
  output out_22,
  output out_23,
  output out_24,
  output out_25,
  output out_26,
  output b256,
  output B128,
  output out_29,
  output out_30,
  output out_31,
  output out_32,
  output out_33,
  output out_34,
  output B1
);

  wire b4adder_1_carryout, b4adder_2_carryout, b4adder_3_carryout;

  b4ADDER b4adder_1 (
    .B8(in_13), .in_2(in_14), .in_3(in_15), .B1(A1), .A8(MINUS), .in_6(MINUS), .in_7(MINUS), .A1(MINUS),
    .CARRYIN(PLUS), .C8(out_32), .out_11(out_33), .out_12(out_34), .C1(B1), .CARRYOUT(b4adder_1_carryout));
  b4ADDER b4adder_2 (
    .B8(A128), .in_2(in_10), .in_3(in_11), .B1(in_12), .A8(MINUS), .in_6(MINUS), .in_7(MINUS), .A1(MINUS),
    .CARRYIN(b4adder_1_carryout), .C8(B128), .out_11(out_29), .out_12(out_30), .C1(out_31),
    .CARRYOUT(b4adder_2_carryout));
  b4ADDER b4adder_3 (
    .B8(in_5), .in_2(in_6), .in_3(in_7), .B1(A256), .A8(MINUS), .in_6(MINUS), .in_7(MINUS), .A1(MINUS),
    .CARRYIN(b4adder_2_carryout), .C8(out_24), .out_11(out_25), .out_12(out_26), .C1(b256),
    .CARRYOUT(b4adder_3_carryout));
  b4ADDER b4adder_4 (
    .B8(A65536), .in_2(in_2), .in_3(in_3), .B1(in_4), .A8(MINUS), .in_6(MINUS), .in_7(MINUS), .A1(MINUS),
    .CARRYIN(b4adder_3_carryout), .C8(b65525), .out_11(out_21), .out_12(out_22), .C1(out_23),
    .CARRYOUT(OVERFLOW));
endmodule

module x16COUNTER (
  input  in_1,
  input  in_2,
  input  in_3,
  input  in_4,
  input  in_5,
  input  in_6,
  input  in_7,
  input  in_8,
  input  in_9,
  input  in_10,
  input  in_11,
  input  in_12,
  input  in_13,
  input  in_14,
  input  in_15,
  input  in_16,
  input  RESET,
  output out_18,
  output out_19,
  output out_20,
  output out_21,
  output out_22,
  output out_23,
  output out_24,
  output out_25,
  output out_26,
  output out_27,
  output out_28,
  output out_29,
  output out_30,
  output out_31,
  output out_32,
  output out_33
);

  D_Flip_Flop d_ff_1 (.D(in_1), .clk(RESET), .Q(out_18));  // open: Qn, preset, reset
  D_Flip_Flop d_ff_2 (.D(in_5), .clk(RESET), .Q(out_22));  // open: Qn, preset, reset
  D_Flip_Flop d_ff_3 (.D(in_9), .clk(RESET), .Q(out_26));  // open: Qn, preset, reset
  D_Flip_Flop d_ff_4 (.D(in_13), .clk(RESET), .Q(out_30));  // open: Qn, preset, reset
  D_Flip_Flop d_ff_5 (.D(in_2), .clk(RESET), .Q(out_19));  // open: Qn, preset, reset
  D_Flip_Flop d_ff_6 (.D(in_6), .clk(RESET), .Q(out_23));  // open: Qn, preset, reset
  D_Flip_Flop d_ff_7 (.D(in_10), .clk(RESET), .Q(out_27));  // open: Qn, preset, reset
  D_Flip_Flop d_ff_8 (.D(in_14), .clk(RESET), .Q(out_31));  // open: Qn, preset, reset
  D_Flip_Flop d_ff_9 (.D(in_3), .clk(RESET), .Q(out_20));  // open: Qn, preset, reset
  D_Flip_Flop d_ff_10 (.D(in_7), .clk(RESET), .Q(out_24));  // open: Qn, preset, reset
  D_Flip_Flop d_ff_11 (.D(in_11), .clk(RESET), .Q(out_28));  // open: Qn, preset, reset
  D_Flip_Flop d_ff_12 (.D(in_15), .clk(RESET), .Q(out_32));  // open: Qn, preset, reset
  D_Flip_Flop d_ff_13 (.D(in_4), .clk(RESET), .Q(out_21));  // open: Qn, preset, reset
  D_Flip_Flop d_ff_14 (.D(in_8), .clk(RESET), .Q(out_25));  // open: Qn, preset, reset
  D_Flip_Flop d_ff_15 (.D(in_12), .clk(RESET), .Q(out_29));  // open: Qn, preset, reset
  D_Flip_Flop d_ff_16 (.D(in_16), .clk(RESET), .Q(out_33));  // open: Qn, preset, reset
endmodule

module ADRESSMAP (
  input  A65355,
  input  in_2,
  input  in_3,
  input  in_4,
  input  in_5,
  input  in_6,
  input  in_7,
  input  in_8,
  input  in_9,
  input  in_10,
  input  in_11,
  input  in_12,
  input  in_13,
  input  in_14,
  input  in_15,
  input  A1,
  input  NEXT_CELL,
  input  PREVIOUS_CELL,
  input  RESET_TO,
  input  UPDATE,
  output B65536,
  output out_22,
  output out_23,
  output out_24,
  output out_25,
  output out_26,
  output out_27,
  output out_28,
  output out_29,
  output out_30,
  output out_31,
  output out_32,
  output out_33,
  output out_34,
  output out_35,
  output B1,
  output OVERFLOW
);

  wire and_2_out, and_3_out, and_4_out, and_5_out, and_6_out, and_7_out, and_8_out, and_9_out, and_10_out,
       and_11_out, and_12_out, and_13_out, and_14_out, and_15_out, and_16_out, and_17_out,
       b16plus_minus_1_b1, b16plus_minus_1_b128, b16plus_minus_1_b256, b16plus_minus_1_b65525,
       b16plus_minus_1_out_21, b16plus_minus_1_out_22, b16plus_minus_1_out_23, b16plus_minus_1_out_24,
       b16plus_minus_1_out_25, b16plus_minus_1_out_26, b16plus_minus_1_out_29, b16plus_minus_1_out_30,
       b16plus_minus_1_out_31, b16plus_minus_1_out_32, b16plus_minus_1_out_33, b16plus_minus_1_out_34,
       not_1_out, or_1_out, or_2_out, or_3_out, or_4_out, or_5_out, or_6_out, or_7_out, or_8_out, or_9_out,
       or_10_out, or_11_out, or_12_out, or_13_out, or_14_out, or_15_out, or_16_out;
  wire [15:0] and_1_out, bit_extender_1_out;

  not not_1 (not_1_out, RESET_TO);
  assign bit_extender_1_out = {{15{RESET_TO}}, RESET_TO};  // Bit_Extender bit_extender_1
  assign and_1_out = {A65355, in_2, in_3, in_4, in_5, in_6, in_7, in_8, in_9, in_10, in_11, in_12, in_13, in_14, in_15, A1} & bit_extender_1_out;  // AND_Gate and_1, 16 bits wide
  or or_1 (or_1_out, and_1_out[15], and_2_out);
  or or_2 (or_2_out, and_1_out[14], and_3_out);
  and and_2 (and_2_out, not_1_out, b16plus_minus_1_b65525);
  and and_3 (and_3_out, not_1_out, b16plus_minus_1_out_21);
  or or_3 (or_3_out, and_1_out[13], and_4_out);
  or or_4 (or_4_out, and_1_out[12], and_5_out);
  and and_4 (and_4_out, not_1_out, b16plus_minus_1_out_22);
  or or_5 (or_5_out, and_1_out[11], and_6_out);
  and and_5 (and_5_out, not_1_out, b16plus_minus_1_out_23);
  and and_6 (and_6_out, not_1_out, b16plus_minus_1_out_24);
  or or_6 (or_6_out, and_1_out[10], and_7_out);
  or or_7 (or_7_out, and_1_out[9], and_8_out);
  and and_7 (and_7_out, not_1_out, b16plus_minus_1_out_25);
  or or_8 (or_8_out, and_1_out[8], and_9_out);
  and and_8 (and_8_out, not_1_out, b16plus_minus_1_out_26);
  and and_9 (and_9_out, not_1_out, b16plus_minus_1_b256);
  or or_9 (or_9_out, and_1_out[7], and_10_out);
  or or_10 (or_10_out, and_1_out[6], and_11_out);
  and and_10 (and_10_out, not_1_out, b16plus_minus_1_b128);
  and and_11 (and_11_out, not_1_out, b16plus_minus_1_out_29);
  or or_11 (or_11_out, and_1_out[5], and_12_out);
  or or_12 (or_12_out, and_1_out[4], and_13_out);
  and and_12 (and_12_out, not_1_out, b16plus_minus_1_out_30);
  or or_13 (or_13_out, and_1_out[3], and_14_out);
  and and_13 (and_13_out, not_1_out, b16plus_minus_1_out_31);
  and and_14 (and_14_out, not_1_out, b16plus_minus_1_out_32);
  or or_14 (or_14_out, and_1_out[2], and_15_out);
  or or_15 (or_15_out, and_1_out[1], and_16_out);
  and and_15 (and_15_out, not_1_out, b16plus_minus_1_out_33);
  or or_16 (or_16_out, and_1_out[0], and_17_out);
  and and_16 (and_16_out, not_1_out, b16plus_minus_1_out_34);
  and and_17 (and_17_out, not_1_out, b16plus_minus_1_b1);
  x16COUNTER x16counter_1 (
    .in_1(or_1_out), .in_2(or_2_out), .in_3(or_3_out), .in_4(or_4_out), .in_5(or_5_out), .in_6(or_6_out),
    .in_7(or_7_out), .in_8(or_8_out), .in_9(or_9_out), .in_10(or_10_out), .in_11(or_11_out),
    .in_12(or_12_out), .in_13(or_13_out), .in_14(or_14_out), .in_15(or_15_out), .in_16(or_16_out),
    .RESET(UPDATE), .out_18(B65536), .out_19(out_22), .out_20(out_23), .out_21(out_24), .out_22(out_25),
    .out_23(out_26), .out_24(out_27), .out_25(out_28), .out_26(out_29), .out_27(out_30), .out_28(out_31),
    .out_29(out_32), .out_30(out_33), .out_31(out_34), .out_32(out_35), .out_33(B1));
  b16PLUS_MINUS b16plus_minus_1 (
    .A65536(B65536), .in_2(out_22), .in_3(out_23), .in_4(out_24), .in_5(out_25), .in_6(out_26),
    .in_7(out_27), .A256(out_28), .A128(out_29), .in_10(out_30), .in_11(out_31), .in_12(out_32),
    .in_13(out_33), .in_14(out_34), .in_15(out_35), .A1(B1), .PLUS(NEXT_CELL), .MINUS(PREVIOUS_CELL),
    .OVERFLOW(OVERFLOW), .b65525(b16plus_minus_1_b65525), .out_21(b16plus_minus_1_out_21),
    .out_22(b16plus_minus_1_out_22), .out_23(b16plus_minus_1_out_23), .out_24(b16plus_minus_1_out_24),
    .out_25(b16plus_minus_1_out_25), .out_26(b16plus_minus_1_out_26), .b256(b16plus_minus_1_b256),
    .B128(b16plus_minus_1_b128), .out_29(b16plus_minus_1_out_29), .out_30(b16plus_minus_1_out_30),
    .out_31(b16plus_minus_1_out_31), .out_32(b16plus_minus_1_out_32), .out_33(b16plus_minus_1_out_33),
    .out_34(b16plus_minus_1_out_34), .B1(b16plus_minus_1_b1));
endmodule

module MAINCHIP (
);

  wire button_1_out, button_2_out, clock_1_out, clockdivider8_1_out_3, decod_1_bracketend,
       decod_1_bracketstart, decod_1_get, decod_1_minus, decod_1_nextcell, decod_1_plus,
       decod_1_previouscell, decod_1_print, dipswitch_1_p1, or_1_out, pathdivider_1_bpclock,
       pathdivider_1_minus, pathdivider_1_nextcell, pathdivider_1_plus, pathdivider_1_prevcell,
       pathdivider_1_raminwritemode, pathdivider_1_readmram, pathdivider_1_updateram,
       pathdivider_1_updatereg, ramarchi_1_readed, RESETCELLVALUE_out, RESETPROGRAMMCOUNTER_out,
       RESETRAMCOUNTER_out, RESETSCREEN_out, romarchi_1_ins1, romarchi_1_ins2, romarchi_1_ins3;
  wire [2:0] pathdivider_1_nextrom;
  wire [6:0] ramarchi_1_b1;
  wire [7:0] and_1_out, bit_extender_1_out, clockdivider8_1_out_4, undriven;

  Clock clock_1 (.out(clock_1_out));
  Button button_1 (.out(button_1_out));
  or or_1 (or_1_out, clock_1_out, button_1_out);
  Button RESETPROGRAMMCOUNTER (.out(RESETPROGRAMMCOUNTER_out));
  CLOCKDIVIDER8 clockdivider8_1 (
    .BPclock(pathdivider_1_bpclock), .CLOCK(or_1_out), .out_3(clockdivider8_1_out_3),
    .out_4(clockdivider8_1_out_4[0]), .out_5(clockdivider8_1_out_4[1]), .out_6(clockdivider8_1_out_4[2]),
    .out_7(clockdivider8_1_out_4[3]), .out_8(clockdivider8_1_out_4[4]), .clockBP(clockdivider8_1_out_4[5]),
    .out_10(clockdivider8_1_out_4[6]), .out_11(clockdivider8_1_out_4[7]));
  // DipSwitch #(.number(2)) dipswitch_1: pin names not known; wires that end beside it: dipswitch_1_p1
  ROMARCHi romarchi_1 (
    .READY(1'b1), .NEXTINS(pathdivider_1_nextrom[0]), .PREVIOUSINS(pathdivider_1_nextrom[1]),
    .UPDATE(pathdivider_1_nextrom[2]), .RESETTO0(RESETPROGRAMMCOUNTER_out), .INS1(romarchi_1_ins1),
    .INS2(romarchi_1_ins2), .INS3(romarchi_1_ins3));  // open: BRACKETON, FORWARD, BACKWARD
  assign bit_extender_1_out = {{7{dipswitch_1_p1}}, dipswitch_1_p1};  // Bit_Extender bit_extender_1
  assign and_1_out = bit_extender_1_out & clockdivider8_1_out_4;  // AND_Gate and_1, 8 bits wide
  DECOD decod_1 (
    .INS1(romarchi_1_ins3), .INS2(romarchi_1_ins2), .INS3(romarchi_1_ins1), .PLUS(decod_1_plus),
    .MINUS(decod_1_minus), .NEXTCELL(decod_1_nextcell), .PREVIOUSCELL(decod_1_previouscell),
    .PRINT(decod_1_print), .GET(decod_1_get), .BRACKETSTART(decod_1_bracketstart),
    .BRACKETEND(decod_1_bracketend));
  LED led_1 (.in(and_1_out[0]));
  LED led_2 (.in(and_1_out[1]));
  LED led_3 (.in(and_1_out[2]));
  LED led_4 (.in(and_1_out[3]));
  LED led_5 (.in(and_1_out[4]));
  LED led_6 (.in(and_1_out[5]));
  LED led_7 (.in(and_1_out[6]));
  LED led_8 (.in(and_1_out[7]));
  LED led_9 (.in(decod_1_plus));
  LED led_10 (.in(decod_1_minus));
  LED led_11 (.in(decod_1_nextcell));
  LED led_12 (.in(decod_1_previouscell));
  LED led_13 (.in(decod_1_print));
  LED led_14 (.in(decod_1_get));
  LED led_15 (.in(decod_1_bracketstart));
  LED led_16 (.in(decod_1_bracketend));
  // DipSwitch dipswitch_2: pin names not known
  Button button_2 (.out(button_2_out));
  PATHDIVIDER pathdivider_1 (
    .clockBP(clockdivider8_1_out_3), .BYPASS(and_1_out[0]), .in_3(and_1_out[1]), .INS1(and_1_out[2]),
    .INS2(and_1_out[3]), .INS3(and_1_out[4]), .INS4(and_1_out[5]), .NEXTROMONE(and_1_out[6]),
    .ROMUPDATE(and_1_out[7]), .rom7(decod_1_plus), .in_11(decod_1_minus), .in_12(decod_1_nextcell),
    .in_13(decod_1_previouscell), .in_14(decod_1_print), .in_15(decod_1_get), .in_16(decod_1_bracketstart),
    .rom0(decod_1_bracketend), .BUTTONPRESSED(button_2_out), .BPclock(pathdivider_1_bpclock),
    .NEXTROM(pathdivider_1_nextrom[0]), .PREVIOUSROM(pathdivider_1_nextrom[1]),
    .UPDATEROM(pathdivider_1_nextrom[2]), .READMRAM(pathdivider_1_readmram),
    .NEXTCELL(pathdivider_1_nextcell), .PREVCELL(pathdivider_1_prevcell),
    .UPDATEREG(pathdivider_1_updatereg), .UPDATERAM(pathdivider_1_updateram),
    .RAMINWRITEMODE(pathdivider_1_raminwritemode), .PLUS(pathdivider_1_plus), .MINUS(pathdivider_1_minus));
  Button RESETRAMCOUNTER (.out(RESETRAMCOUNTER_out));
  Button RESETCELLVALUE (.out(RESETCELLVALUE_out));
  RAMARCHI ramarchi_1 (
    .READ(pathdivider_1_readmram), .NEXTCELL(pathdivider_1_nextcell), .PREVCELL(pathdivider_1_prevcell),
    .RESETTONULL(RESETRAMCOUNTER_out), .UPDATEREGS(pathdivider_1_updatereg),
    .UPDATERAM(pathdivider_1_updateram), .RESETTO0(RESETCELLVALUE_out), .A65355(undriven[7]),
    .in_9(undriven[6]), .in_10(undriven[5]), .in_11(undriven[4]), .in_12(undriven[3]), .in_13(undriven[2]),
    .in_14(undriven[1]), .A1(undriven[0]), .PLUS(pathdivider_1_plus), .MINUS(pathdivider_1_minus),
    .WRITE(pathdivider_1_raminwritemode), .out_20(ramarchi_1_b1[6]), .out_21(ramarchi_1_b1[5]),
    .out_22(ramarchi_1_b1[4]), .out_23(ramarchi_1_b1[3]), .out_24(ramarchi_1_b1[2]),
    .out_25(ramarchi_1_b1[1]), .B1(ramarchi_1_b1[0]), .READED(ramarchi_1_readed));  // open: B128
  TTY tty_1 (.data(ramarchi_1_b1), .clk(ramarchi_1_readed), .we(1'b1), .clr(RESETSCREEN_out));
  Button RESETSCREEN (.out(RESETSCREEN_out));

  // Notes on the sheet:
  //   000
  //   +
  //   001
  //   -
  //   010
  //   >
  //   011
  //   <
  //   .
  //   100
  //   ,
  //   101
  //   [
  //   110
  //   ]
  //   111
  //   INPUT
  //   OUTPUT
endmodule

module x16RAM (
  input  A65355,
  input  in_2,
  input  in_3,
  input  in_4,
  input  in_5,
  input  in_6,
  input  in_7,
  input  in_8,
  input  in_9,
  input  in_10,
  input  in_11,
  input  in_12,
  input  in_13,
  input  in_14,
  input  in_15,
  input  A1,
  input  WRITE,
  input  IN7,
  input  in_19,
  input  in_20,
  input  in_21,
  input  in_22,
  input  in_23,
  input  in_24,
  input  IN0,
  output OUT0,
  output out_27,
  output out_28,
  output out_29,
  output out_30,
  output out_31,
  output out_32,
  output OUT7
);

  RAM #(.addrWidth(16), .trigger("high"), .\type ("nonvolatile")) ram_1 (
    .addr({A65355, in_2, in_3, in_4, in_5, in_6, in_7, in_8, in_9, in_10, in_11, in_12, in_13, in_14, in_15, A1}),
    .we(WRITE), .din({IN7, in_19, in_20, in_21, in_22, in_23, in_24, IN0}),
    .dout({OUT7, out_32, out_31, out_30, out_29, out_28, out_27, OUT0}));  // open: oe
endmodule

module x16ROM (
  input  A65355,
  input  in_2,
  input  in_3,
  input  in_4,
  input  in_5,
  input  in_6,
  input  in_7,
  input  in_8,
  input  in_9,
  input  in_10,
  input  in_11,
  input  in_12,
  input  in_13,
  input  in_14,
  input  in_15,
  input  A1,
  output B0,
  output B1,
  output B2
);

  ROM #(.addrWidth(16), .dataWidth(3)) rom_1 (
    .addr({A65355, in_2, in_3, in_4, in_5, in_6, in_7, in_8, in_9, in_10, in_11, in_12, in_13, in_14, in_15, A1}),
    .data({B2, B1, B0}));

  // Notes on the sheet:
  //   contents of rom_1 (hex, n*v repeats v):
  //   8*0 6 2 8*0 3 1 7 2 0 4 0 4 0 4 0 4 0 4
endmodule

module x8COUNTER (
  input  in_1,
  input  in_2,
  input  in_3,
  input  in_4,
  input  in_5,
  input  in_6,
  input  in_7,
  input  in_8,
  input  UPDATE,
  output out_10,
  output out_11,
  output out_12,
  output out_13,
  output out_14,
  output out_15,
  output out_16,
  output out_17
);

  D_Flip_Flop d_ff_1 (.D(in_1), .clk(UPDATE), .Q(out_10));  // open: Qn, preset, reset
  D_Flip_Flop d_ff_2 (.D(in_3), .clk(UPDATE), .Q(out_12));  // open: Qn, preset, reset
  D_Flip_Flop d_ff_3 (.D(in_5), .clk(UPDATE), .Q(out_14));  // open: Qn, preset, reset
  D_Flip_Flop d_ff_4 (.D(in_7), .clk(UPDATE), .Q(out_16));  // open: Qn, preset, reset
  D_Flip_Flop d_ff_5 (.D(in_2), .clk(UPDATE), .Q(out_11));  // open: Qn, preset, reset
  D_Flip_Flop d_ff_6 (.D(in_4), .clk(UPDATE), .Q(out_13));  // open: Qn, preset, reset
  D_Flip_Flop d_ff_7 (.D(in_6), .clk(UPDATE), .Q(out_15));  // open: Qn, preset, reset
  D_Flip_Flop d_ff_8 (.D(in_8), .clk(UPDATE), .Q(out_17));  // open: Qn, preset, reset
endmodule

module BRACKETCOUNT (
  input  RESET,
  input  MORE,
  input  LESS,
  input  UPDATE,
  output B128,
  output out_6,
  output out_7,
  output out_8,
  output out_9,
  output out_10,
  output out_11,
  output B1,
  output OVERFLOW
);

  wire b8plus_minus_1_b1, b8plus_minus_1_b128, b8plus_minus_1_out_13, b8plus_minus_1_out_14,
       b8plus_minus_1_out_15, b8plus_minus_1_out_16, b8plus_minus_1_out_17, b8plus_minus_1_out_18;

  x8COUNTER x8counter_1 (
    .in_1(b8plus_minus_1_b128), .in_2(b8plus_minus_1_out_13), .in_3(b8plus_minus_1_out_14),
    .in_4(b8plus_minus_1_out_15), .in_5(b8plus_minus_1_out_16), .in_6(b8plus_minus_1_out_17),
    .in_7(b8plus_minus_1_out_18), .in_8(b8plus_minus_1_b1), .UPDATE(UPDATE), .out_10(B128), .out_11(out_6),
    .out_12(out_7), .out_13(out_8), .out_14(out_9), .out_15(out_10), .out_16(out_11), .out_17(B1));
  b8PLUS_MINUS b8plus_minus_1 (
    .A128(B128), .in_2(out_6), .in_3(out_7), .in_4(out_8), .in_5(out_9), .in_6(out_10), .in_7(out_11),
    .A1(B1), .PLUS(MORE), .MINUS(LESS), .OVERFLOW(OVERFLOW), .B128(b8plus_minus_1_b128),
    .out_13(b8plus_minus_1_out_13), .out_14(b8plus_minus_1_out_14), .out_15(b8plus_minus_1_out_15),
    .out_16(b8plus_minus_1_out_16), .out_17(b8plus_minus_1_out_17), .out_18(b8plus_minus_1_out_18),
    .B1(b8plus_minus_1_b1));
endmodule

module BRACKETCHECK (
  input  A128,
  input  in_2,
  input  in_3,
  input  in_4,
  input  in_5,
  input  in_6,
  input  in_7,
  input  A1,
  input  FORWARD_if1,
  output YES,
  output SKIP
);

  wire not_1_out, or_1_out, or_2_out, or_3_out, or_4_out, or_5_out, or_6_out, or_7_out;

  or or_1 (or_1_out, A128, in_2);
  or or_2 (or_2_out, in_3, in_4);
  or or_3 (or_3_out, in_5, in_6);
  or or_4 (or_4_out, in_7, A1);
  or or_5 (or_5_out, or_1_out, or_2_out);
  or or_6 (or_6_out, or_3_out, or_4_out);
  not not_1 (not_1_out, FORWARD_if1);
  or or_7 (or_7_out, or_5_out, or_6_out);
  xnor xnor_1 (YES, or_7_out, not_1_out);
  not not_2 (SKIP, YES);
endmodule

module ROMARCHi (
  input  READY,
  input  BRACKETON,
  input  NEXTINS,
  input  PREVIOUSINS,
  input  UPDATE,
  input  RESETTO0,
  output INS1,
  output INS2,
  output INS3,
  output FORWARD,
  output BACKWARD
);

  wire adressmap_1_b1, adressmap_1_b65536, adressmap_1_out_22, adressmap_1_out_23, adressmap_1_out_24,
       adressmap_1_out_25, adressmap_1_out_26, adressmap_1_out_27, adressmap_1_out_28, adressmap_1_out_29,
       adressmap_1_out_30, adressmap_1_out_31, adressmap_1_out_32, adressmap_1_out_33, adressmap_1_out_34,
       adressmap_1_out_35, and_4_out, and_5_out, and_6_out, not_1_out, not_2_out, x16rom_1_b0, x16rom_1_b1,
       x16rom_1_b2;

  not not_1 (not_1_out, RESETTO0);
  ADRESSMAP adressmap_1 (
    .A65355(not_1_out), .in_2(not_1_out), .in_3(not_1_out), .in_4(not_1_out), .in_5(not_1_out),
    .in_6(not_1_out), .in_7(not_1_out), .in_8(not_1_out), .in_9(not_1_out), .in_10(not_1_out),
    .in_11(not_1_out), .in_12(not_1_out), .in_13(not_1_out), .in_14(not_1_out), .in_15(not_1_out),
    .A1(not_1_out), .NEXT_CELL(NEXTINS), .PREVIOUS_CELL(PREVIOUSINS), .RESET_TO(RESETTO0), .UPDATE(UPDATE),
    .B65536(adressmap_1_b65536), .out_22(adressmap_1_out_22), .out_23(adressmap_1_out_23),
    .out_24(adressmap_1_out_24), .out_25(adressmap_1_out_25), .out_26(adressmap_1_out_26),
    .out_27(adressmap_1_out_27), .out_28(adressmap_1_out_28), .out_29(adressmap_1_out_29),
    .out_30(adressmap_1_out_30), .out_31(adressmap_1_out_31), .out_32(adressmap_1_out_32),
    .out_33(adressmap_1_out_33), .out_34(adressmap_1_out_34), .out_35(adressmap_1_out_35), .B1(adressmap_1_b1));  // open: OVERFLOW
  x16ROM x16rom_1 (
    .A65355(adressmap_1_b65536), .in_2(adressmap_1_out_22), .in_3(adressmap_1_out_23),
    .in_4(adressmap_1_out_24), .in_5(adressmap_1_out_25), .in_6(adressmap_1_out_26),
    .in_7(adressmap_1_out_27), .in_8(adressmap_1_out_28), .in_9(adressmap_1_out_29),
    .in_10(adressmap_1_out_30), .in_11(adressmap_1_out_31), .in_12(adressmap_1_out_32),
    .in_13(adressmap_1_out_33), .in_14(adressmap_1_out_34), .in_15(adressmap_1_out_35), .A1(adressmap_1_b1),
    .B0(x16rom_1_b0), .B1(x16rom_1_b1), .B2(x16rom_1_b2));
  and and_1 (INS1, READY, x16rom_1_b0);
  and and_2 (INS2, READY, x16rom_1_b1);
  and and_3 (INS3, READY, x16rom_1_b2);
  and and_4 (and_4_out, x16rom_1_b0, x16rom_1_b1);
  not not_2 (not_2_out, x16rom_1_b2);
  and and_5 (and_5_out, x16rom_1_b2, and_4_out);
  and and_6 (and_6_out, not_2_out, and_4_out);
  and and_7 (FORWARD, BRACKETON, and_6_out);
  and and_8 (BACKWARD, BRACKETON, and_5_out);

  // Notes on the sheet:
  //   000
  //   +
  //   001
  //   -
  //   010
  //   >
  //   011
  //   <
  //   .
  //   100
  //   ,
  //   101
  //   [
  //   110
  //   ]
  //   111
endmodule

module DECOD (
  input  INS1,
  input  INS2,
  input  INS3,
  output PLUS,
  output MINUS,
  output NEXTCELL,
  output PREVIOUSCELL,
  output PRINT,
  output GET,
  output BRACKETSTART,
  output BRACKETEND
);

  wire and_1_out, and_2_out, and_3_out, and_4_out, not_1_out, not_2_out, not_3_out;

  not not_1 (not_1_out, INS1);
  not not_2 (not_2_out, INS2);
  not not_3 (not_3_out, INS3);
  and and_1 (and_1_out, INS1, INS2);
  and and_2 (and_2_out, not_1_out, not_2_out);
  and and_3 (and_3_out, not_1_out, INS2);
  and and_4 (and_4_out, INS1, not_2_out);
  and and_5 (PLUS, not_3_out, and_2_out);
  and and_6 (MINUS, INS3, and_2_out);
  and and_7 (NEXTCELL, not_3_out, and_3_out);
  and and_8 (PREVIOUSCELL, INS3, and_3_out);
  and and_9 (PRINT, not_3_out, and_4_out);
  and and_10 (GET, INS3, and_4_out);
  and and_11 (BRACKETSTART, and_1_out, not_3_out);
  and and_12 (BRACKETEND, and_1_out, INS3);

  // Notes on the sheet:
  //   000
  //   +
  //   001
  //   -
  //   010
  //   >
  //   011
  //   <
  //   .
  //   100
  //   ,
  //   101
  //   [
  //   110
  //   ]
  //   111
endmodule

module RAMARCHI (
  input  READ,
  input  NEXTCELL,
  input  PREVCELL,
  input  RESETTONULL,
  input  UPDATEREGS,
  input  UPDATERAM,
  input  RESETTO0,
  input  A65355,
  input  in_9,
  input  in_10,
  input  in_11,
  input  in_12,
  input  in_13,
  input  in_14,
  input  A1,
  input  PLUS,
  input  MINUS,
  input  WRITE,
  output B128,
  output out_20,
  output out_21,
  output out_22,
  output out_23,
  output out_24,
  output out_25,
  output B1,
  output READED
);

  wire adressmap_1_b1, adressmap_1_b65536, adressmap_1_out_22, adressmap_1_out_23, adressmap_1_out_24,
       adressmap_1_out_25, adressmap_1_out_26, adressmap_1_out_27, adressmap_1_out_28, adressmap_1_out_29,
       adressmap_1_out_30, adressmap_1_out_31, adressmap_1_out_32, adressmap_1_out_33, adressmap_1_out_34,
       adressmap_1_out_35, b8plus_minus_1_b1, b8plus_minus_1_b128, b8plus_minus_1_out_13,
       b8plus_minus_1_out_14, b8plus_minus_1_out_15, b8plus_minus_1_out_16, b8plus_minus_1_out_17,
       b8plus_minus_1_out_18, not_1_out, not_3_out, not_4_out, or_1_out;
  wire [7:0] and_1_out, and_2_out, and_3_out, bit_extender_1_out, bit_extender_2_out, bit_extender_3_out,
       not_2_out, or_2_out, x8counter_1_out_10, x16ram_1_out7;

  not not_1 (not_1_out, RESETTONULL);
  or or_1 (or_1_out, UPDATERAM, RESETTO0);
  assign not_2_out = ~bit_extender_1_out;  // NOT_Gate not_2, 8 bits wide
  not not_3 (not_3_out, RESETTO0);
  assign or_2_out = and_1_out | and_2_out;  // OR_Gate or_2, 8 bits wide
  assign and_1_out = {A1, in_14, in_13, in_12, in_11, in_10, in_9, A65355} & not_2_out;  // AND_Gate and_1, 8 bits wide
  assign and_2_out = bit_extender_1_out & x8counter_1_out_10;  // AND_Gate and_2, 8 bits wide
  assign bit_extender_1_out = {{7{not_4_out}}, not_4_out};  // Bit_Extender bit_extender_1
  not not_4 (not_4_out, WRITE);
  assign bit_extender_2_out = {{7{not_3_out}}, not_3_out};  // Bit_Extender bit_extender_2
  ADRESSMAP adressmap_1 (
    .A65355(not_1_out), .in_2(not_1_out), .in_3(not_1_out), .in_4(not_1_out), .in_5(not_1_out),
    .in_6(not_1_out), .in_7(not_1_out), .in_8(not_1_out), .in_9(not_1_out), .in_10(not_1_out),
    .in_11(not_1_out), .in_12(not_1_out), .in_13(not_1_out), .in_14(not_1_out), .in_15(not_1_out),
    .A1(not_1_out), .NEXT_CELL(NEXTCELL), .PREVIOUS_CELL(PREVCELL), .RESET_TO(RESETTONULL),
    .UPDATE(UPDATEREGS), .B65536(adressmap_1_b65536), .out_22(adressmap_1_out_22),
    .out_23(adressmap_1_out_23), .out_24(adressmap_1_out_24), .out_25(adressmap_1_out_25),
    .out_26(adressmap_1_out_26), .out_27(adressmap_1_out_27), .out_28(adressmap_1_out_28),
    .out_29(adressmap_1_out_29), .out_30(adressmap_1_out_30), .out_31(adressmap_1_out_31),
    .out_32(adressmap_1_out_32), .out_33(adressmap_1_out_33), .out_34(adressmap_1_out_34),
    .out_35(adressmap_1_out_35), .B1(adressmap_1_b1));  // open: OVERFLOW
  assign and_3_out = bit_extender_2_out & or_2_out;  // AND_Gate and_3, 8 bits wide
  x16RAM x16ram_1 (
    .A65355(adressmap_1_b65536), .in_2(adressmap_1_out_22), .in_3(adressmap_1_out_23),
    .in_4(adressmap_1_out_24), .in_5(adressmap_1_out_25), .in_6(adressmap_1_out_26),
    .in_7(adressmap_1_out_27), .in_8(adressmap_1_out_28), .in_9(adressmap_1_out_29),
    .in_10(adressmap_1_out_30), .in_11(adressmap_1_out_31), .in_12(adressmap_1_out_32),
    .in_13(adressmap_1_out_33), .in_14(adressmap_1_out_34), .in_15(adressmap_1_out_35), .A1(adressmap_1_b1),
    .WRITE(or_1_out), .IN7(and_3_out[0]), .in_19(and_3_out[1]), .in_20(and_3_out[2]), .in_21(and_3_out[3]),
    .in_22(and_3_out[4]), .in_23(and_3_out[5]), .in_24(and_3_out[6]), .IN0(and_3_out[7]),
    .OUT0(x16ram_1_out7[7]), .out_27(x16ram_1_out7[6]), .out_28(x16ram_1_out7[5]), .out_29(x16ram_1_out7[4]),
    .out_30(x16ram_1_out7[3]), .out_31(x16ram_1_out7[2]), .out_32(x16ram_1_out7[1]), .OUT7(x16ram_1_out7[0]));
  b8PLUS_MINUS b8plus_minus_1 (
    .A128(x16ram_1_out7[0]), .in_2(x16ram_1_out7[1]), .in_3(x16ram_1_out7[2]), .in_4(x16ram_1_out7[3]),
    .in_5(x16ram_1_out7[4]), .in_6(x16ram_1_out7[5]), .in_7(x16ram_1_out7[6]), .A1(x16ram_1_out7[7]),
    .PLUS(PLUS), .MINUS(MINUS), .B128(b8plus_minus_1_b128), .out_13(b8plus_minus_1_out_13),
    .out_14(b8plus_minus_1_out_14), .out_15(b8plus_minus_1_out_15), .out_16(b8plus_minus_1_out_16),
    .out_17(b8plus_minus_1_out_17), .out_18(b8plus_minus_1_out_18), .B1(b8plus_minus_1_b1));  // open: OVERFLOW
  assign bit_extender_3_out = {{7{READ}}, READ};  // Bit_Extender bit_extender_3
  assign {B1, out_25, out_24, out_23, out_22, out_21, out_20, B128} = bit_extender_3_out & x16ram_1_out7;  // AND_Gate and_4, 8 bits wide
  x8COUNTER x8counter_1 (
    .in_1(b8plus_minus_1_b128), .in_2(b8plus_minus_1_out_13), .in_3(b8plus_minus_1_out_14),
    .in_4(b8plus_minus_1_out_15), .in_5(b8plus_minus_1_out_16), .in_6(b8plus_minus_1_out_17),
    .in_7(b8plus_minus_1_out_18), .in_8(b8plus_minus_1_b1), .UPDATE(UPDATEREGS),
    .out_10(x8counter_1_out_10[0]), .out_11(x8counter_1_out_10[1]), .out_12(x8counter_1_out_10[2]),
    .out_13(x8counter_1_out_10[3]), .out_14(x8counter_1_out_10[4]), .out_15(x8counter_1_out_10[5]),
    .out_16(x8counter_1_out_10[6]), .out_17(x8counter_1_out_10[7]));

  assign READED = READ;
endmodule

module x4COUNTER (
  input  in_1,
  input  in_2,
  input  in_3,
  input  in_4,
  input  UPDATE,
  output out_6,
  output out_7,
  output out_8,
  output out_9
);

  D_Flip_Flop d_ff_1 (.D(in_1), .clk(UPDATE), .Q(out_6));  // open: Qn, preset, reset
  D_Flip_Flop d_ff_2 (.D(in_3), .clk(UPDATE), .Q(out_8));  // open: Qn, preset, reset
  D_Flip_Flop d_ff_3 (.D(in_2), .clk(UPDATE), .Q(out_7));  // open: Qn, preset, reset
  D_Flip_Flop d_ff_4 (.D(in_4), .clk(UPDATE), .Q(out_9));  // open: Qn, preset, reset
endmodule

module x2COUNTER (
  input  in_1,
  input  in_2,
  input  UPDATE,
  output out_4,
  output out_5
);

  D_Flip_Flop d_ff_1 (.D(in_1), .clk(UPDATE), .Q(out_4));  // open: Qn, preset, reset
  D_Flip_Flop d_ff_2 (.D(in_2), .clk(UPDATE), .Q(out_5));  // open: Qn, preset, reset
endmodule

module b2ADDER (
  input  B2,
  input  B1,
  input  A2,
  input  A1,
  input  CARRYIN,
  output C2,
  output C1,
  output CARRYOUT
);

  wire adder_c_1_carryout;

  ADDER_C adder_c_1 (.in_1(B1), .in_2(A1), .carry(CARRYIN), .sum(C1), .carryout(adder_c_1_carryout));
  ADDER_C adder_c_2 (.in_1(B2), .in_2(A2), .carry(adder_c_1_carryout), .sum(C2), .carryout(CARRYOUT));
endmodule

module CLOCKDIVIDER (
  input  CLOCK,
  output out_2,
  output out_3,
  output out_4,
  output out_5
);

  wire x2counter_1_out_4, x2counter_1_out_5;
  wire [1:0] b2adder_1_c2;

  x2COUNTER x2counter_1 (
    .in_1(b2adder_1_c2[0]), .in_2(b2adder_1_c2[1]), .UPDATE(CLOCK), .out_4(x2counter_1_out_4),
    .out_5(x2counter_1_out_5));
  b2ADDER b2adder_1 (
    .A2(x2counter_1_out_4), .A1(x2counter_1_out_5), .CARRYIN(1'b1), .C2(b2adder_1_c2[0]),
    .C1(b2adder_1_c2[1]), .CARRYOUT(out_5));  // open: B2, B1
  and and_1 (out_2, b2adder_1_c2[0], b2adder_1_c2[1]);
  xor xor_1 (out_3, out_2, b2adder_1_c2[0]);
  xor xor_2 (out_4, out_2, b2adder_1_c2[1]);
endmodule

module CLOCKDIVIDER8 (
  input  BPclock,
  input  CLOCK,
  output out_3,
  output out_4,
  output out_5,
  output out_6,
  output out_7,
  output out_8,
  output clockBP,
  output out_10,
  output out_11
);

  wire and_1_out, and_3_out, and_4_out, and_5_out, and_6_out, not_1_out, not_2_out, not_3_out, not_4_out,
       x3counter_1_out_5, x3counter_1_out_6, x3counter_1_out_7;
  wire [2:0] b3plus_1_c3;

  not not_1 (not_1_out, BPclock);
  and and_1 (and_1_out, not_1_out, CLOCK);
  and and_2 (clockBP, BPclock, CLOCK);
  x3COUNTER x3counter_1 (
    .in_1(b3plus_1_c3[0]), .in_2(b3plus_1_c3[1]), .in_3(b3plus_1_c3[2]), .UPDATE(and_1_out),
    .out_5(x3counter_1_out_5), .out_6(x3counter_1_out_6), .out_7(x3counter_1_out_7));
  b3PLUS b3plus_1 (
    .A3(x3counter_1_out_5), .in_2(x3counter_1_out_6), .A1(x3counter_1_out_7), .CARRYIN(1'b1),
    .C3(b3plus_1_c3[0]), .out_6(b3plus_1_c3[1]), .C1(b3plus_1_c3[2]));  // open: OVERFLOW
  not not_2 (not_2_out, b3plus_1_c3[0]);
  not not_3 (not_3_out, b3plus_1_c3[1]);
  not not_4 (not_4_out, b3plus_1_c3[2]);
  and and_3 (and_3_out, b3plus_1_c3[0], b3plus_1_c3[1]);
  and and_4 (and_4_out, not_2_out, not_3_out);
  and and_5 (and_5_out, not_2_out, b3plus_1_c3[1]);
  and and_6 (and_6_out, b3plus_1_c3[0], not_3_out);
  and and_7 (out_3, not_4_out, and_4_out);
  and and_8 (out_4, b3plus_1_c3[2], and_4_out);
  and and_9 (out_5, not_4_out, and_5_out);
  and and_10 (out_6, b3plus_1_c3[2], and_5_out);
  and and_11 (out_7, not_4_out, and_6_out);
  and and_12 (out_8, b3plus_1_c3[2], and_6_out);
  and and_13 (out_10, and_3_out, not_4_out);
  and and_14 (out_11, and_3_out, b3plus_1_c3[2]);

  // Notes on the sheet:
  //   ]
  //   111
endmodule

module x3COUNTER (
  input  in_1,
  input  in_2,
  input  in_3,
  input  UPDATE,
  output out_5,
  output out_6,
  output out_7
);

  D_Flip_Flop d_ff_1 (.D(in_1), .clk(UPDATE), .Q(out_5));  // open: Qn, preset, reset
  D_Flip_Flop d_ff_2 (.D(in_2), .clk(UPDATE), .Q(out_6));  // open: Qn, preset, reset
  D_Flip_Flop d_ff_3 (.D(in_3), .clk(UPDATE), .Q(out_7));  // open: Qn, preset, reset
endmodule

module b3PLUS (
  input  A3,
  input  in_2,
  input  A1,
  input  CARRYIN,
  output C3,
  output out_6,
  output C1,
  output OVERFLOW
);

  wire adder_c_1_carryout, adder_c_2_carryout;

  ADDER_C adder_c_1 (.in_2(A1), .carry(CARRYIN), .sum(C1), .carryout(adder_c_1_carryout));  // open: in_1
  ADDER_C adder_c_2 (
    .in_2(in_2), .carry(adder_c_1_carryout), .sum(out_6), .carryout(adder_c_2_carryout));  // open: in_1
  ADDER_C adder_c_3 (.in_2(A3), .carry(adder_c_2_carryout), .sum(C3), .carryout(OVERFLOW));  // open: in_1
endmodule

module PATHDIVIDER (
  input  clockBP,
  input  BYPASS,
  input  in_3,
  input  INS1,
  input  INS2,
  input  INS3,
  input  INS4,
  input  NEXTROMONE,
  input  ROMUPDATE,
  input  rom7,
  input  in_11,
  input  in_12,
  input  in_13,
  input  in_14,
  input  in_15,
  input  in_16,
  input  rom0,
  input  BUTTONPRESSED,
  output BPclock,
  output NEXTROM,
  output PREVIOUSROM,
  output UPDATEROM,
  output READMRAM,
  output NEXTCELL,
  output PREVCELL,
  output UPDATEREG,
  output UPDATERAM,
  output RAMINWRITEMODE,
  output PLUS,
  output MINUS
);

  wire and_1_out, and_6_out, and_7_out, and_11_out, and_12_out, not_1_out, or_1_out, or_2_out, or_3_out,
       or_4_out;

  or or_1 (or_1_out, rom7, in_11);
  not not_1 (not_1_out, BUTTONPRESSED);
  and and_1 (and_1_out, in_15, not_1_out);
  or or_2 (or_2_out, INS3, INS4);
  or or_3 (or_3_out, or_2_out, INS2);
  and and_2 (READMRAM, INS3, in_14);
  or or_4 (or_4_out, in_13, in_12);
  and and_3 (BPclock, BYPASS, and_1_out);
  or or_5 (NEXTROM, NEXTROMONE, ROMUPDATE);
  and and_4 (NEXTCELL, in_12, or_2_out);
  and and_5 (PREVCELL, or_2_out, in_13);
  and and_6 (and_6_out, INS4, or_4_out);
  and and_7 (and_7_out, in_15, INS4);
  and and_8 (RAMINWRITEMODE, or_2_out, in_15);
  and and_9 (PLUS, or_3_out, rom7);
  and and_10 (MINUS, or_3_out, in_11);
  and and_11 (and_11_out, or_1_out, INS3);
  and and_12 (and_12_out, or_1_out, INS4);
  or or_6 (UPDATEREG, and_6_out, and_11_out);
  or or_7 (UPDATERAM, and_7_out, and_12_out);

  assign UPDATEROM = ROMUPDATE;

  // Notes on the sheet:
  //   100
  //   101
  //   000
  //   +
  //   001
  //   -
  //   010
  //   >
  //   011
  //   <
  //   .
  //   ,
  //   [
  //   110
  //   ]
  //   111
endmodule
