// Logisim project V2.circ as structural Verilog
module ADDER_C (
  input  in_1,
  input  in_2,
  input  carry,
  output sum,
  output carryout
);

  wire and_1_out, and_2_out, xor_1_out;

  and and_1 (and_1_out, in_1, in_2);
  xor xor_1 (xor_1_out, in_1, in_2);
  xor xor_2 (sum, xor_1_out, carry);
  or or_1 (carryout, and_1_out, and_2_out);
  and and_2 (and_2_out, xor_1_out, carry);
endmodule

module b4ADDER (
  input  B8,
  input  in_2,
  input  in_3,
  input  B1,
  input  A8,
  input  in_6,
  input  in_7,
  input  A1,
  input  CARRYIN,
  output C8,
  output out_11,
  output out_12,
  output C1,
  output CARRYOUT
);

  wire adder_c_1_carryout, adder_c_2_carryout, adder_c_3_carryout;

  ADDER_C adder_c_1 (.in_1(B1), .in_2(A1), .carry(CARRYIN), .sum(C1), .carryout(adder_c_1_carryout));
  ADDER_C adder_c_2 (.in_1(in_3), .in_2(in_7), .carry(adder_c_1_carryout), .sum(out_12), .carryout(adder_c_2_carryout));
  ADDER_C adder_c_3 (.in_1(in_2), .in_2(in_6), .carry(adder_c_2_carryout), .sum(out_11), .carryout(adder_c_3_carryout));
  ADDER_C adder_c_4 (.in_1(B8), .in_2(A8), .carry(adder_c_3_carryout), .sum(C8), .carryout(CARRYOUT));
endmodule

module b8PLUS_MINUS (
  input  A128,
  input  in_2,
  input  in_3,
  input  in_4,
  input  in_5,
  input  in_6,
  input  in_7,
  input  A1,
  input  PLUS,
  input  MINUS,
  output OVERFLOW,
  output B128,
  output out_13,
  output out_14,
  output out_15,
  output out_16,
  output out_17,
  output out_18,
  output B1
);

  wire b4adder_1_carryout;

  b4ADDER b4adder_1 (
    .B8(in_5), .in_2(in_6), .in_3(in_7), .B1(A1), .A8(MINUS), .in_6(MINUS), .in_7(MINUS), .A1(MINUS),
    .CARRYIN(PLUS), .C8(out_16), .out_11(out_17), .out_12(out_18), .C1(B1), .CARRYOUT(b4adder_1_carryout));
  b4ADDER b4adder_2 (
    .B8(A128), .in_2(in_2), .in_3(in_3), .B1(in_4), .A8(MINUS), .in_6(MINUS), .in_7(MINUS), .A1(MINUS),
    .CARRYIN(b4adder_1_carryout), .C8(B128), .out_11(out_13), .out_12(out_14), .C1(out_15),
    .CARRYOUT(OVERFLOW));
endmodule

module b16PLUS_MINUS (
  input  A65536,
  input  in_2,
  input  in_3,
  input  in_4,
  input  in_5,
  input  in_6,
  input  in_7,
  input  A256,
  input  A128,
  input  in_10,
  input  in_11,
  input  in_12,
  input  in_13,
  input  in_14,
  input  in_15,
  input  A1,
  input  PLUS,
  input  MINUS,
  output OVERFLOW,
  output b65525,
  output out_21,
  output out_22,
  output out_23,
  output out_24,
  output out_25,
  output out_26,
  output b256,
  output B128,
  output out_29,
  output out_30,
  output out_31,
  output out_32,
  output out_33,
  output out_34,
  output B1
);

  wire b4adder_1_carryout, b4adder_2_carryout, b4adder_3_carryout;

  b4ADDER b4adder_1 (
    .B8(in_13), .in_2(in_14), .in_3(in_15), .B1(A1), .A8(MINUS), .in_6(MINUS), .in_7(MINUS), .A1(MINUS),
    .CARRYIN(PLUS), .C8(out_32), .out_11(out_33), .out_12(out_34), .C1(B1), .CARRYOUT(b4adder_1_carryout));
  b4ADDER b4adder_2 (
    .B8(A128), .in_2(in_10), .in_3(in_11), .B1(in_12), .A8(MINUS), .in_6(MINUS), .in_7(MINUS), .A1(MINUS),
    .CARRYIN(b4adder_1_carryout), .C8(B128), .out_11(out_29), .out_12(out_30), .C1(out_31),
    .CARRYOUT(b4adder_2_carryout));
  b4ADDER b4adder_3 (
    .B8(in_5), .in_2(in_6), .in_3(in_7), .B1(A256), .A8(MINUS), .in_6(MINUS), .in_7(MINUS), .A1(MINUS),
    .CARRYIN(b4adder_2_carryout), .C8(out_24), .out_11(out_25), .out_12(out_26), .C1(b256),
    .CARRYOUT(b4adder_3_carryout));
  b4ADDER b4adder_4 (
    .B8(A65536), .in_2(in_2), .in_3(in_3), .B1(in_4), .A8(MINUS), .in_6(MINUS), .in_7(MINUS), .A1(MINUS),
    .CARRYIN(b4adder_3_carryout), .C8(b65525), .out_11(out_21), .out_12(out_22), .C1(out_23),
    .CARRYOUT(OVERFLOW));
endmodule

module x16COUNTER (
  input  RESET
);

  wire d_ff_1_q, d_ff_2_q, d_ff_3_q, d_ff_4_q, d_ff_5_q, d_ff_6_q, d_ff_7_q, d_ff_8_q, d_ff_9_q, d_ff_10_q,
       d_ff_11_q, d_ff_12_q, d_ff_13_q, d_ff_14_q, d_ff_15_q, d_ff_16_q, undriven, undriven_2, undriven_3,
       undriven_4, undriven_5, undriven_6, undriven_7, undriven_8, undriven_9, undriven_10, undriven_11,
       undriven_12, undriven_13, undriven_14, undriven_15, undriven_16;

  D_Flip_Flop d_ff_1 (.D(undriven_13), .clk(RESET), .Q(d_ff_1_q));  // open: Qn, preset, reset
  D_Flip_Flop d_ff_2 (.D(undriven_14), .clk(RESET), .Q(d_ff_2_q));  // open: Qn, preset, reset
  D_Flip_Flop d_ff_3 (.D(undriven_15), .clk(RESET), .Q(d_ff_3_q));  // open: Qn, preset, reset
  D_Flip_Flop d_ff_4 (.D(undriven_16), .clk(RESET), .Q(d_ff_4_q));  // open: Qn, preset, reset
  D_Flip_Flop d_ff_5 (.D(undriven_9), .clk(RESET), .Q(d_ff_5_q));  // open: Qn, preset, reset
  D_Flip_Flop d_ff_6 (.D(undriven_10), .clk(RESET), .Q(d_ff_6_q));  // open: Qn, preset, reset
  D_Flip_Flop d_ff_7 (.D(undriven_11), .clk(RESET), .Q(d_ff_7_q));  // open: Qn, preset, reset
  D_Flip_Flop d_ff_8 (.D(undriven_12), .clk(RESET), .Q(d_ff_8_q));  // open: Qn, preset, reset
  D_Flip_Flop d_ff_9 (.D(undriven_5), .clk(RESET), .Q(d_ff_9_q));  // open: Qn, preset, reset
  D_Flip_Flop d_ff_10 (.D(undriven_6), .clk(RESET), .Q(d_ff_10_q));  // open: Qn, preset, reset
  D_Flip_Flop d_ff_11 (.D(undriven_7), .clk(RESET), .Q(d_ff_11_q));  // open: Qn, preset, reset
  D_Flip_Flop d_ff_12 (.D(undriven_8), .clk(RESET), .Q(d_ff_12_q));  // open: Qn, preset, reset
  D_Flip_Flop d_ff_13 (.D(undriven), .clk(RESET), .Q(d_ff_13_q));  // open: Qn, preset, reset
  D_Flip_Flop d_ff_14 (.D(undriven_2), .clk(RESET), .Q(d_ff_14_q));  // open: Qn, preset, reset
  D_Flip_Flop d_ff_15 (.D(undriven_3), .clk(RESET), .Q(d_ff_15_q));  // open: Qn, preset, reset
  D_Flip_Flop d_ff_16 (.D(undriven_4), .clk(RESET), .Q(d_ff_16_q));  // open: Qn, preset, reset
endmodule

module ADRESSMAP (
  input  A65355,
  input  in_2,
  input  in_3,
  input  in_4,
  input  in_5,
  input  in_6,
  input  in_7,
  input  in_8,
  input  in_9,
  input  in_10,
  input  in_11,
  input  in_12,
  input  in_13,
  input  in_14,
  input  in_15,
  input  A1,
  input  NEXT_CELL,
  input  PREVIOUS_CELL,
  input  RESET_TO,
  input  UPDATE,
  output B65536,
  output out_22,
  output out_23,
  output out_24,
  output out_25,
  output out_26,
  output out_27,
  output out_28,
  output out_29,
  output out_30,
  output out_31,
  output out_32,
  output out_33,
  output out_34,
  output out_35,
  output B1,
  output OVERFLOW
);

  wire and_2_out, and_3_out, and_4_out, and_5_out, and_6_out, and_7_out, and_8_out, and_9_out, and_10_out,
       and_11_out, and_12_out, and_13_out, and_14_out, and_15_out, and_16_out, and_17_out,
       b16plus_minus_1_b1, b16plus_minus_1_b128, b16plus_minus_1_b256, b16plus_minus_1_b65525,
       b16plus_minus_1_out_21, b16plus_minus_1_out_22, b16plus_minus_1_out_23, b16plus_minus_1_out_24,
       b16plus_minus_1_out_25, b16plus_minus_1_out_26, b16plus_minus_1_out_29, b16plus_minus_1_out_30,
       b16plus_minus_1_out_31, b16plus_minus_1_out_32, b16plus_minus_1_out_33, b16plus_minus_1_out_34,
       not_1_out, or_1_out, or_2_out, or_3_out, or_4_out, or_5_out, or_6_out, or_7_out, or_8_out, or_9_out,
       or_10_out, or_11_out, or_12_out, or_13_out, or_14_out, or_15_out, or_16_out;
  wire [15:0] and_1_out, bit_extender_1_out;

  not not_1 (not_1_out, RESET_TO);
  assign bit_extender_1_out = {{15{RESET_TO}}, RESET_TO};  // Bit_Extender bit_extender_1
  assign and_1_out = {A65355, in_2, in_3, in_4, in_5, in_6, in_7, in_8, in_9, in_10, in_11, in_12, in_13, in_14, in_15, A1} & bit_extender_1_out;  // AND_Gate and_1, 16 bits wide
  or or_1 (or_1_out, and_1_out[15], and_2_out);
  or or_2 (or_2_out, and_1_out[14], and_3_out);
  and and_2 (and_2_out, not_1_out, b16plus_minus_1_b65525);
  and and_3 (and_3_out, not_1_out, b16plus_minus_1_out_21);
  or or_3 (or_3_out, and_1_out[13], and_4_out);
  or or_4 (or_4_out, and_1_out[12], and_5_out);
  and and_4 (and_4_out, not_1_out, b16plus_minus_1_out_22);
  or or_5 (or_5_out, and_1_out[11], and_6_out);
  and and_5 (and_5_out, not_1_out, b16plus_minus_1_out_23);
  and and_6 (and_6_out, not_1_out, b16plus_minus_1_out_24);
  or or_6 (or_6_out, and_1_out[10], and_7_out);
  or or_7 (or_7_out, and_1_out[9], and_8_out);
  and and_7 (and_7_out, not_1_out, b16plus_minus_1_out_25);
  or or_8 (or_8_out, and_1_out[8], and_9_out);
  and and_8 (and_8_out, not_1_out, b16plus_minus_1_out_26);
  and and_9 (and_9_out, not_1_out, b16plus_minus_1_b256);
  or or_9 (or_9_out, and_1_out[7], and_10_out);
  or or_10 (or_10_out, and_1_out[6], and_11_out);
  and and_10 (and_10_out, not_1_out, b16plus_minus_1_b128);
  and and_11 (and_11_out, not_1_out, b16plus_minus_1_out_29);
  or or_11 (or_11_out, and_1_out[5], and_12_out);
  or or_12 (or_12_out, and_1_out[4], and_13_out);
  and and_12 (and_12_out, not_1_out, b16plus_minus_1_out_30);
  or or_13 (or_13_out, and_1_out[3], and_14_out);
  and and_13 (and_13_out, not_1_out, b16plus_minus_1_out_31);
  and and_14 (and_14_out, not_1_out, b16plus_minus_1_out_32);
  or or_14 (or_14_out, and_1_out[2], and_15_out);
  or or_15 (or_15_out, and_1_out[1], and_16_out);
  and and_15 (and_15_out, not_1_out, b16plus_minus_1_out_33);
  or or_16 (or_16_out, and_1_out[0], and_17_out);
  and and_16 (and_16_out, not_1_out, b16plus_minus_1_out_34);
  and and_17 (and_17_out, not_1_out, b16plus_minus_1_b1);
  x16COUNTER x16counter_1 (.RESET(B65536));
  b16PLUS_MINUS b16plus_minus_1 (
    .A65536(B65536), .in_2(out_22), .in_3(out_23), .in_4(out_24), .in_5(out_25), .in_6(out_26),
    .in_7(out_27), .A256(out_28), .A128(out_29), .in_10(out_30), .in_11(out_31), .in_12(out_32),
    .in_13(out_33), .in_14(out_34), .in_15(out_35), .A1(B1), .PLUS(NEXT_CELL), .MINUS(PREVIOUS_CELL),
    .OVERFLOW(OVERFLOW), .b65525(b16plus_minus_1_b65525), .out_21(b16plus_minus_1_out_21),
    .out_22(b16plus_minus_1_out_22), .out_23(b16plus_minus_1_out_23), .out_24(b16plus_minus_1_out_24),
    .out_25(b16plus_minus_1_out_25), .out_26(b16plus_minus_1_out_26), .b256(b16plus_minus_1_b256),
    .B128(b16plus_minus_1_b128), .out_29(b16plus_minus_1_out_29), .out_30(b16plus_minus_1_out_30),
    .out_31(b16plus_minus_1_out_31), .out_32(b16plus_minus_1_out_32), .out_33(b16plus_minus_1_out_33),
    .out_34(b16plus_minus_1_out_34), .B1(b16plus_minus_1_b1));
endmodule

module MAINCHIP (
);

  wire and_1_out, bracketcheck_1_yes, button_1_out, clock_1_out, not_1_out, not_2_out, pathdivider3_1_getram,
       pathdivider3_1_minus1, pathdivider3_1_nextreg, pathdivider3_1_plus1, pathdivider3_1_prevreg,
       pathdivider3_1_ramreadytowrite, pathdivider3_1_redirectclock, pathdivider3_1_stopclock,
       pathdivider3_1_updateramreg, pathdivider3_1_updateramvalue, pathdivider3_1_updatescreen,
       RESETCELLVALUE_out, RESETRAMCOUNTER_out, RESETSCREEN_out, romarchi_1_ins1, romarchi_1_ins2,
       romarchi_1_ins3;
  wire [0:0] ramarchi_1_b128;
  wire [2:0] pathdivider3_1_romplus1;
  wire [6:0] ramarchi_1_b1;
  wire [7:0] undriven;

  Clock clock_1 (.out(clock_1_out));
  and and_1 (and_1_out, not_1_out, clock_1_out);
  not not_1 (not_1_out, pathdivider3_1_stopclock);
  ROMARCHi romarchi_1 (
    .NEXTINS(pathdivider3_1_romplus1[0]), .UPDATE(pathdivider3_1_romplus1[1]),
    .PREVIOUSINS(pathdivider3_1_romplus1[2]), .INS1(romarchi_1_ins1), .INS2(romarchi_1_ins2),
    .INS3(romarchi_1_ins3));
  not not_2 (not_2_out, romarchi_1_ins1);
  Button button_1 (.out(button_1_out));
  // DipSwitch dipswitch_1: pin names not known
  PATHDIVIDER3 pathdivider3_1 (
    .BPClock(pathdivider3_1_redirectclock), .CLOCK(and_1_out), .ROM3(romarchi_1_ins1),
    .in_4(romarchi_1_ins2), .ROM1(romarchi_1_ins3), .BUTTON(button_1_out), .VALID(bracketcheck_1_yes),
    .STOPCLOCK(pathdivider3_1_stopclock), .REDIRECTCLOCK(pathdivider3_1_redirectclock),
    .ROMPLUS1(pathdivider3_1_romplus1[0]), .REFRESHROM(pathdivider3_1_romplus1[1]),
    .ROMMINUS1(pathdivider3_1_romplus1[2]), .PLUS1(pathdivider3_1_plus1), .MINUS1(pathdivider3_1_minus1),
    .NEXTREG(pathdivider3_1_nextreg), .PREVREG(pathdivider3_1_prevreg),
    .UPDATERAMREG(pathdivider3_1_updateramreg), .UPDATERAMVALUE(pathdivider3_1_updateramvalue),
    .GETRAM(pathdivider3_1_getram), .UPDATESCREEN(pathdivider3_1_updatescreen),
    .RAMREADYTOWRITE(pathdivider3_1_ramreadytowrite));
  BRACKETCHECK bracketcheck_1 (
    .A128(ramarchi_1_b128[0]), .in_2(ramarchi_1_b1[6]), .in_3(ramarchi_1_b1[5]), .in_4(ramarchi_1_b1[4]),
    .in_5(ramarchi_1_b1[3]), .in_6(ramarchi_1_b1[2]), .in_7(ramarchi_1_b1[1]), .A1(ramarchi_1_b1[0]),
    .FORWARD_if1(not_2_out), .YES(bracketcheck_1_yes));  // open: SKIP
  Button RESETRAMCOUNTER (.out(RESETRAMCOUNTER_out));
  Button RESETCELLVALUE (.out(RESETCELLVALUE_out));
  RAMARCHI ramarchi_1 (
    .READ(pathdivider3_1_getram), .NEXTCELL(pathdivider3_1_nextreg), .PREVCELL(pathdivider3_1_prevreg),
    .RESETTONULL(RESETRAMCOUNTER_out), .UPDATEREGS(pathdivider3_1_updateramreg),
    .UPDATERAM(pathdivider3_1_updateramvalue), .RESETTO0(RESETCELLVALUE_out), .A65355(undriven[7]),
    .in_9(undriven[6]), .in_10(undriven[5]), .in_11(undriven[4]), .in_12(undriven[3]), .in_13(undriven[2]),
    .in_14(undriven[1]), .A1(undriven[0]), .PLUS(pathdivider3_1_plus1), .MINUS(pathdivider3_1_minus1),
    .WRITE(pathdivider3_1_ramreadytowrite), .B128(ramarchi_1_b128[0]), .out_20(ramarchi_1_b1[6]),
    .out_21(ramarchi_1_b1[5]), .out_22(ramarchi_1_b1[4]), .out_23(ramarchi_1_b1[3]),
    .out_24(ramarchi_1_b1[2]), .out_25(ramarchi_1_b1[1]), .B1(ramarchi_1_b1[0]));  // open: READED
  TTY #(.trigger("falling")) tty_1 (
    .data(ramarchi_1_b1), .clk(pathdivider3_1_updatescreen), .we(1'b1), .clr(RESETSCREEN_out));
  Button RESETSCREEN (.out(RESETSCREEN_out));

  // Notes on the sheet:
  //   INPUT
  //   OUTPUT
endmodule

module x16RAM (
  input  A65355,
  input  in_2,
  input  in_3,
  input  in_4,
  input  in_5,
  input  in_6,
  input  in_7,
  input  in_8,
  input  in_9,
  input  in_10,
  input  in_11,
  input  in_12,
  input  in_13,
  input  in_14,
  input  in_15,
  input  A1,
  input  WRITE,
  input  IN7,
  input  in_19,
  input  in_20,
  input  in_21,
  input  in_22,
  input  in_23,
  input  in_24,
  input  IN0,
  output OUT0,
  output out_27,
  output out_28,
  output out_29,
  output out_30,
  output out_31,
  output out_32,
  output OUT7
);

  RAM #(.addrWidth(16), .trigger("high"), .\type ("nonvolatile")) ram_1 (
    .addr({A65355, in_2, in_3, in_4, in_5, in_6, in_7, in_8, in_9, in_10, in_11, in_12, in_13, in_14, in_15, A1}),
    .we(WRITE), .din({IN7, in_19, in_20, in_21, in_22, in_23, in_24, IN0}),
    .dout({OUT7, out_32, out_31, out_30, out_29, out_28, out_27, OUT0}));  // open: oe
endmodule

module x16ROM (
  input  A65355,
  input  in_2,
  input  in_3,
  input  in_4,
  input  in_5,
  input  in_6,
  input  in_7,
  input  in_8,
  input  in_9,
  input  in_10,
  input  in_11,
  input  in_12,
  input  in_13,
  input  in_14,
  input  in_15,
  input  A1,
  output B0,
  output B1,
  output B2
);

  ROM #(.addrWidth(16), .dataWidth(3)) rom_1 (
    .addr({A65355, in_2, in_3, in_4, in_5, in_6, in_7, in_8, in_9, in_10, in_11, in_12, in_13, in_14, in_15, A1}),
    .data({B2, B1, B0}));

  // Notes on the sheet:
  //   contents of rom_1 (hex, n*v repeats v):
  //   8*0 6 2 8*0 3 1 7 2 8*0 4 2 8*0 6 2 12*0 3 1 7 2 5*0 4 7*0 4 4 0 0 0 4 2 8*0 6 2 5*0 3 1 7 2 4*0 4
  //   12*1 4 4*3 15*0 4 2 2 4 0 0 0 4 6*1 4 8*1 4 2 2 0 4 6*2
endmodule

module x8COUNTER (
  input  in_1,
  input  in_2,
  input  in_3,
  input  in_4,
  input  in_5,
  input  in_6,
  input  in_7,
  input  in_8,
  input  UPDATE,
  output out_10,
  output out_11,
  output out_12,
  output out_13,
  output out_14,
  output out_15,
  output out_16,
  output out_17
);

  D_Flip_Flop d_ff_1 (.D(in_1), .clk(UPDATE), .Q(out_10));  // open: Qn, preset, reset
  D_Flip_Flop d_ff_2 (.D(in_3), .clk(UPDATE), .Q(out_12));  // open: Qn, preset, reset
  D_Flip_Flop d_ff_3 (.D(in_5), .clk(UPDATE), .Q(out_14));  // open: Qn, preset, reset
  D_Flip_Flop d_ff_4 (.D(in_7), .clk(UPDATE), .Q(out_16));  // open: Qn, preset, reset
  D_Flip_Flop d_ff_5 (.D(in_2), .clk(UPDATE), .Q(out_11));  // open: Qn, preset, reset
  D_Flip_Flop d_ff_6 (.D(in_4), .clk(UPDATE), .Q(out_13));  // open: Qn, preset, reset
  D_Flip_Flop d_ff_7 (.D(in_6), .clk(UPDATE), .Q(out_15));  // open: Qn, preset, reset
  D_Flip_Flop d_ff_8 (.D(in_8), .clk(UPDATE), .Q(out_17));  // open: Qn, preset, reset
endmodule

module BRACKETCOUNT (
  input  UPDATE,
  input  MORE,
  input  LESS,
  output B128,
  output out_5,
  output out_6,
  output out_7,
  output out_8,
  output out_9,
  output out_10,
  output B1,
  output OVERFLOW
);

  wire [7:0] b8plus_minus_1_b128;

  x8COUNTER x8counter_1 (
    .in_1(b8plus_minus_1_b128[0]), .in_2(b8plus_minus_1_b128[1]), .in_3(b8plus_minus_1_b128[2]),
    .in_4(b8plus_minus_1_b128[3]), .in_5(b8plus_minus_1_b128[4]), .in_6(b8plus_minus_1_b128[5]),
    .in_7(b8plus_minus_1_b128[6]), .in_8(b8plus_minus_1_b128[7]), .UPDATE(UPDATE), .out_10(B128),
    .out_11(out_5), .out_12(out_6), .out_13(out_7), .out_14(out_8), .out_15(out_9), .out_16(out_10),
    .out_17(B1));
  LED led_1 (.in(B128));
  LED led_2 (.in(out_5));
  LED led_3 (.in(out_6));
  LED led_4 (.in(out_7));
  LED led_5 (.in(out_8));
  LED led_6 (.in(out_9));
  LED led_7 (.in(out_10));
  LED led_8 (.in(B1));
  b8PLUS_MINUS b8plus_minus_1 (
    .A128(B128), .in_2(out_5), .in_3(out_6), .in_4(out_7), .in_5(out_8), .in_6(out_9), .in_7(out_10),
    .A1(B1), .PLUS(MORE), .MINUS(LESS), .OVERFLOW(OVERFLOW), .B128(b8plus_minus_1_b128[0]),
    .out_13(b8plus_minus_1_b128[1]), .out_14(b8plus_minus_1_b128[2]), .out_15(b8plus_minus_1_b128[3]),
    .out_16(b8plus_minus_1_b128[4]), .out_17(b8plus_minus_1_b128[5]), .out_18(b8plus_minus_1_b128[6]),
    .B1(b8plus_minus_1_b128[7]));
  LED led_9 (.in(b8plus_minus_1_b128[0]));
  LED led_10 (.in(b8plus_minus_1_b128[1]));
  LED led_11 (.in(b8plus_minus_1_b128[2]));
  LED led_12 (.in(b8plus_minus_1_b128[3]));
  LED led_13 (.in(b8plus_minus_1_b128[4]));
  LED led_14 (.in(b8plus_minus_1_b128[5]));
  LED led_15 (.in(b8plus_minus_1_b128[6]));
  LED led_16 (.in(b8plus_minus_1_b128[7]));
endmodule

module BRACKETCHECK (
  input  A128,
  input  in_2,
  input  in_3,
  input  in_4,
  input  in_5,
  input  in_6,
  input  in_7,
  input  A1,
  input  FORWARD_if1,
  output YES,
  output SKIP
);

  wire not_1_out, or_1_out, or_2_out, or_3_out, or_4_out, or_5_out, or_6_out, or_7_out;

  or or_1 (or_1_out, A128, in_2);
  or or_2 (or_2_out, in_3, in_4);
  or or_3 (or_3_out, in_5, in_6);
  or or_4 (or_4_out, in_7, A1);
  or or_5 (or_5_out, or_1_out, or_2_out);
  or or_6 (or_6_out, or_3_out, or_4_out);
  not not_1 (not_1_out, FORWARD_if1);
  or or_7 (or_7_out, or_5_out, or_6_out);
  xnor xnor_1 (YES, or_7_out, not_1_out);
  not not_2 (SKIP, YES);
endmodule

module ROMARCHi (
  input  NEXTINS,
  input  UPDATE,
  input  PREVIOUSINS,
  output INS1,
  output INS2,
  output INS3
);

  wire [15:0] adressemap2_1_b1;

  ADRESSEMAP2 adressemap2_1 (
    .NEXT_CELL(NEXTINS), .PREVIOUS_CELL(PREVIOUSINS), .UPDATE(UPDATE), .B65536(adressemap2_1_b1[15]),
    .out_5(adressemap2_1_b1[14]), .out_6(adressemap2_1_b1[13]), .out_7(adressemap2_1_b1[12]),
    .out_8(adressemap2_1_b1[11]), .out_9(adressemap2_1_b1[10]), .out_10(adressemap2_1_b1[9]),
    .out_11(adressemap2_1_b1[8]), .out_12(adressemap2_1_b1[7]), .out_13(adressemap2_1_b1[6]),
    .out_14(adressemap2_1_b1[5]), .out_15(adressemap2_1_b1[4]), .out_16(adressemap2_1_b1[3]),
    .out_17(adressemap2_1_b1[2]), .out_18(adressemap2_1_b1[1]), .B1(adressemap2_1_b1[0]));  // open: OVERFLOW
  ROM #(.addrWidth(16), .dataWidth(3)) rom_1 (.addr(adressemap2_1_b1), .data({INS3, INS2, INS1}));

  // Notes on the sheet:
  //   000
  //   +
  //   001
  //   -
  //   010
  //   >
  //   011
  //   <
  //   .
  //   100
  //   ,
  //   101
  //   [
  //   110
  //   ]
  //   111
  //   contents of rom_1 (hex, n*v repeats v):
  //   4 0 6 4 0 7
endmodule

module DECOD (
  input  INS1,
  input  INS2,
  input  INS3,
  output PLUS,
  output MINUS,
  output NEXTCELL,
  output PREVIOUSCELL,
  output PRINT,
  output GET,
  output BRACKETSTART,
  output BRACKETEND
);

  wire and_1_out, and_2_out, and_3_out, and_4_out, not_1_out, not_2_out, not_3_out;

  not not_1 (not_1_out, INS1);
  not not_2 (not_2_out, INS2);
  not not_3 (not_3_out, INS3);
  and and_1 (and_1_out, not_1_out, not_2_out);
  and and_2 (and_2_out, not_1_out, INS2);
  and and_3 (and_3_out, INS1, not_2_out);
  and and_4 (and_4_out, INS1, INS2);
  and and_5 (PLUS, not_3_out, and_1_out);
  and and_6 (MINUS, INS3, and_1_out);
  and and_7 (NEXTCELL, not_3_out, and_2_out);
  and and_8 (PREVIOUSCELL, INS3, and_2_out);
  and and_9 (PRINT, not_3_out, and_3_out);
  and and_10 (GET, INS3, and_3_out);
  and and_11 (BRACKETSTART, and_4_out, not_3_out);
  and and_12 (BRACKETEND, and_4_out, INS3);
endmodule

module RAMARCHI (
  input  READ,
  input  NEXTCELL,
  input  PREVCELL,
  input  RESETTONULL,
  input  UPDATEREGS,
  input  UPDATERAM,
  input  RESETTO0,
  input  A65355,
  input  in_9,
  input  in_10,
  input  in_11,
  input  in_12,
  input  in_13,
  input  in_14,
  input  A1,
  input  PLUS,
  input  MINUS,
  input  WRITE,
  output B128,
  output out_20,
  output out_21,
  output out_22,
  output out_23,
  output out_24,
  output out_25,
  output B1,
  output READED
);

  wire b8plus_minus_1_b1, b8plus_minus_1_b128, b8plus_minus_1_out_13, b8plus_minus_1_out_14,
       b8plus_minus_1_out_15, b8plus_minus_1_out_16, b8plus_minus_1_out_17, b8plus_minus_1_out_18, not_1_out,
       not_2_out, not_4_out, or_1_out;
  wire [7:0] and_1_out, and_2_out, and_3_out, bit_extender_1_out, bit_extender_2_out, bit_extender_3_out,
       not_3_out, or_2_out, ram_1_dout, x8counter_1_out_17;
  wire [15:0] adressemap2_1_b1;

  not not_1 (not_1_out, WRITE);
  not not_2 (not_2_out, RESETTONULL);
  or or_1 (or_1_out, UPDATERAM, RESETTO0);
  assign not_3_out = ~bit_extender_1_out;  // NOT_Gate not_3, 8 bits wide
  not not_4 (not_4_out, RESETTO0);
  assign or_2_out = and_1_out | and_2_out;  // OR_Gate or_2, 8 bits wide
  assign and_1_out = {A65355, in_9, in_10, in_11, in_12, in_13, in_14, A1} & not_3_out;  // AND_Gate and_1, 8 bits wide
  assign and_2_out = bit_extender_1_out & x8counter_1_out_17;  // AND_Gate and_2, 8 bits wide
  assign bit_extender_1_out = {{7{not_1_out}}, not_1_out};  // Bit_Extender bit_extender_1
  assign bit_extender_2_out = {{7{not_4_out}}, not_4_out};  // Bit_Extender bit_extender_2
  assign and_3_out = bit_extender_2_out & or_2_out;  // AND_Gate and_3, 8 bits wide
  ADRESSEMAP2 adressemap2_1 (
    .NEXT_CELL(NEXTCELL), .PREVIOUS_CELL(PREVCELL), .UPDATE(UPDATEREGS), .B65536(adressemap2_1_b1[15]),
    .out_5(adressemap2_1_b1[14]), .out_6(adressemap2_1_b1[13]), .out_7(adressemap2_1_b1[12]),
    .out_8(adressemap2_1_b1[11]), .out_9(adressemap2_1_b1[10]), .out_10(adressemap2_1_b1[9]),
    .out_11(adressemap2_1_b1[8]), .out_12(adressemap2_1_b1[7]), .out_13(adressemap2_1_b1[6]),
    .out_14(adressemap2_1_b1[5]), .out_15(adressemap2_1_b1[4]), .out_16(adressemap2_1_b1[3]),
    .out_17(adressemap2_1_b1[2]), .out_18(adressemap2_1_b1[1]), .B1(adressemap2_1_b1[0]));  // open: OVERFLOW
  b8PLUS_MINUS b8plus_minus_1 (
    .A128(ram_1_dout[7]), .in_2(ram_1_dout[6]), .in_3(ram_1_dout[5]), .in_4(ram_1_dout[4]),
    .in_5(ram_1_dout[3]), .in_6(ram_1_dout[2]), .in_7(ram_1_dout[1]), .A1(ram_1_dout[0]), .PLUS(PLUS),
    .MINUS(MINUS), .B128(b8plus_minus_1_b128), .out_13(b8plus_minus_1_out_13),
    .out_14(b8plus_minus_1_out_14), .out_15(b8plus_minus_1_out_15), .out_16(b8plus_minus_1_out_16),
    .out_17(b8plus_minus_1_out_17), .out_18(b8plus_minus_1_out_18), .B1(b8plus_minus_1_b1));  // open: OVERFLOW
  RAM #(.addrWidth(16), .trigger("high")) ram_1 (
    .addr(adressemap2_1_b1), .we(or_1_out), .din(and_3_out), .dout(ram_1_dout));  // open: oe
  x8COUNTER x8counter_1 (
    .in_1(b8plus_minus_1_b128), .in_2(b8plus_minus_1_out_13), .in_3(b8plus_minus_1_out_14),
    .in_4(b8plus_minus_1_out_15), .in_5(b8plus_minus_1_out_16), .in_6(b8plus_minus_1_out_17),
    .in_7(b8plus_minus_1_out_18), .in_8(b8plus_minus_1_b1), .UPDATE(UPDATEREGS),
    .out_10(x8counter_1_out_17[7]), .out_11(x8counter_1_out_17[6]), .out_12(x8counter_1_out_17[5]),
    .out_13(x8counter_1_out_17[4]), .out_14(x8counter_1_out_17[3]), .out_15(x8counter_1_out_17[2]),
    .out_16(x8counter_1_out_17[1]), .out_17(x8counter_1_out_17[0]));
  assign bit_extender_3_out = {{7{READ}}, READ};  // Bit_Extender bit_extender_3
  assign {B128, out_20, out_21, out_22, out_23, out_24, out_25, B1} = bit_extender_3_out & ram_1_dout;  // AND_Gate and_4, 8 bits wide

  assign READED = READ;
endmodule

module x4COUNTER (
  input  in_1,
  input  in_2,
  input  in_3,
  input  in_4,
  input  UPDATE,
  output out_6,
  output out_7,
  output out_8,
  output out_9
);

  D_Flip_Flop d_ff_1 (.D(in_1), .clk(UPDATE), .Q(out_6));  // open: Qn, preset, reset
  D_Flip_Flop d_ff_2 (.D(in_3), .clk(UPDATE), .Q(out_8));  // open: Qn, preset, reset
  D_Flip_Flop d_ff_3 (.D(in_2), .clk(UPDATE), .Q(out_7));  // open: Qn, preset, reset
  D_Flip_Flop d_ff_4 (.D(in_4), .clk(UPDATE), .Q(out_9));  // open: Qn, preset, reset
endmodule

module x2COUNTER (
  input  in_1,
  input  in_2,
  input  UPDATE,
  output out_4,
  output out_5
);

  D_Flip_Flop d_ff_1 (.D(in_1), .clk(UPDATE), .Q(out_4));  // open: Qn, preset, reset
  D_Flip_Flop d_ff_2 (.D(in_2), .clk(UPDATE), .Q(out_5));  // open: Qn, preset, reset
endmodule

module b2ADDER (
  input  B2,
  input  B1,
  input  A2,
  input  A1,
  input  CARRYIN,
  output C2,
  output C1,
  output CARRYOUT
);

  wire adder_c_1_carryout;

  ADDER_C adder_c_1 (.in_1(B1), .in_2(A1), .carry(CARRYIN), .sum(C1), .carryout(adder_c_1_carryout));
  ADDER_C adder_c_2 (.in_1(B2), .in_2(A2), .carry(adder_c_1_carryout), .sum(C2), .carryout(CARRYOUT));
endmodule

module CLOCKDIVIDER (
  input  CLOCK,
  output out_2,
  output out_3,
  output out_4,
  output out_5
);

  wire x2counter_1_out_4, x2counter_1_out_5;
  wire [1:0] b2adder_1_c2;

  x2COUNTER x2counter_1 (
    .in_1(b2adder_1_c2[0]), .in_2(b2adder_1_c2[1]), .UPDATE(CLOCK), .out_4(x2counter_1_out_4),
    .out_5(x2counter_1_out_5));
  b2ADDER b2adder_1 (
    .A2(x2counter_1_out_4), .A1(x2counter_1_out_5), .CARRYIN(1'b1), .C2(b2adder_1_c2[0]),
    .C1(b2adder_1_c2[1]), .CARRYOUT(out_5));  // open: B2, B1
  and and_1 (out_2, b2adder_1_c2[0], b2adder_1_c2[1]);
  xor xor_1 (out_3, out_2, b2adder_1_c2[0]);
  xor xor_2 (out_4, out_2, b2adder_1_c2[1]);
endmodule

module CLOCKDIVIDER8 (
  input  BPclock,
  input  CLOCK,
  output clockBP,
  output out_4,
  output out_5,
  output out_6,
  output out_7,
  output out_8,
  output out_9,
  output out_10,
  output out_11
);

  wire and_1_out, and_3_out, and_4_out, and_5_out, and_6_out, not_1_out, not_2_out, not_3_out, not_4_out,
       x3counter_1_out_5, x3counter_1_out_6, x3counter_1_out_7;
  wire [2:0] b3plus_1_c3;

  not not_1 (not_1_out, BPclock);
  and and_1 (and_1_out, not_1_out, CLOCK);
  and and_2 (clockBP, BPclock, CLOCK);
  x3COUNTER x3counter_1 (
    .in_1(b3plus_1_c3[0]), .in_2(b3plus_1_c3[1]), .in_3(b3plus_1_c3[2]), .UPDATE(and_1_out),
    .out_5(x3counter_1_out_5), .out_6(x3counter_1_out_6), .out_7(x3counter_1_out_7));
  b3PLUS b3plus_1 (
    .A3(x3counter_1_out_5), .in_2(x3counter_1_out_6), .A1(x3counter_1_out_7), .CARRYIN(1'b1),
    .C3(b3plus_1_c3[0]), .out_6(b3plus_1_c3[1]), .C1(b3plus_1_c3[2]));  // open: OVERFLOW
  not not_2 (not_2_out, b3plus_1_c3[0]);
  not not_3 (not_3_out, b3plus_1_c3[1]);
  not not_4 (not_4_out, b3plus_1_c3[2]);
  and and_3 (and_3_out, b3plus_1_c3[0], b3plus_1_c3[1]);
  and and_4 (and_4_out, not_2_out, not_3_out);
  and and_5 (and_5_out, not_2_out, b3plus_1_c3[1]);
  and and_6 (and_6_out, b3plus_1_c3[0], not_3_out);
  and and_7 (out_4, not_4_out, and_4_out);
  and and_8 (out_5, b3plus_1_c3[2], and_4_out);
  and and_9 (out_6, not_4_out, and_5_out);
  and and_10 (out_7, b3plus_1_c3[2], and_5_out);
  and and_11 (out_8, not_4_out, and_6_out);
  and and_12 (out_9, b3plus_1_c3[2], and_6_out);
  and and_13 (out_10, and_3_out, not_4_out);
  and and_14 (out_11, and_3_out, b3plus_1_c3[2]);

  // Notes on the sheet:
  //   ]
  //   111
endmodule

module x3COUNTER (
  input  in_1,
  input  in_2,
  input  in_3,
  input  UPDATE,
  output out_5,
  output out_6,
  output out_7
);

  D_Flip_Flop d_ff_1 (.D(in_1), .clk(UPDATE), .Q(out_5));  // open: Qn, preset, reset
  D_Flip_Flop d_ff_2 (.D(in_2), .clk(UPDATE), .Q(out_6));  // open: Qn, preset, reset
  D_Flip_Flop d_ff_3 (.D(in_3), .clk(UPDATE), .Q(out_7));  // open: Qn, preset, reset
endmodule

module b3PLUS (
  input  A3,
  input  in_2,
  input  A1,
  input  CARRYIN,
  output C3,
  output out_6,
  output C1,
  output OVERFLOW
);

  wire adder_c_1_carryout, adder_c_2_carryout;

  ADDER_C adder_c_1 (.in_2(A1), .carry(CARRYIN), .sum(C1), .carryout(adder_c_1_carryout));  // open: in_1
  ADDER_C adder_c_2 (
    .in_2(in_2), .carry(adder_c_1_carryout), .sum(out_6), .carryout(adder_c_2_carryout));  // open: in_1
  ADDER_C adder_c_3 (.in_2(A3), .carry(adder_c_2_carryout), .sum(C3), .carryout(OVERFLOW));  // open: in_1
endmodule

module PATHDIVIDER (
  input  clockBP,
  input  BYPASS,
  input  in_3,
  input  INS1,
  input  INS2,
  input  INS3,
  input  INS4,
  input  NEXTROMONE,
  input  ROMUPDATE,
  input  rom7,
  input  in_11,
  input  in_12,
  input  in_13,
  input  in_14,
  input  in_15,
  input  in_16,
  input  rom0,
  input  BUTTONPRESSED,
  input  BRACKET,
  input  BRACKETON,
  input  BRACKETOFF,
  output BPclock,
  output NEXTROM,
  output PREVIOUSROM,
  output UPDATEROM,
  output READMRAM,
  output NEXTCELL,
  output PREVCELL,
  output UPDATEREG,
  output UPDATERAM,
  output RAMINWRITEMODE,
  output PLUS,
  output MINUS,
  output PRINTRAM,
  output forwardif1
);

  wire and_1_out, and_2_out, and_3_out, and_4_out, and_7_out, and_8_out, and_13_out, and_14_out, and_15_out,
       and_16_out, and_17_out, bracketcount_1_p4, bracketcount_1_p5, bracketcount_1_p6, bracketcount_1_p7,
       bracketcount_1_p8, bracketcount_1_p9, bracketcount_1_p10, bracketcount_1_p11, clockdivider_1_out_2,
       clockdivider_1_out_3, clockdivider_1_out_4, clockdivider_1_out_5, d_ff_1_q, d_ff_2_q, is0_1_out_9,
       not_1_out, or_1_out, or_2_out, or_3_out, or_4_out, or_5_out, or_6_out, or_7_out, or_8_out, or_12_out,
       or_15_out;

  or or_1 (or_1_out, in_16, rom0);
  or or_2 (or_2_out, rom7, in_11);
  not not_1 (not_1_out, BUTTONPRESSED);
  and and_1 (and_1_out, in_15, not_1_out);
  or or_3 (or_3_out, in_3, BYPASS);
  or or_4 (or_4_out, INS3, INS4);
  or or_5 (or_5_out, or_4_out, INS2);
  or or_6 (or_6_out, INS3, INS4);
  and and_2 (and_2_out, or_1_out, or_3_out);
  and and_3 (and_3_out, or_6_out, in_14);
  or or_7 (or_7_out, in_13, in_12);
  and and_4 (and_4_out, BYPASS, and_1_out);
  or or_8 (or_8_out, NEXTROMONE, ROMUPDATE);
  or or_9 (READMRAM, and_2_out, and_3_out);
  and and_5 (NEXTCELL, in_12, or_4_out);
  and and_6 (PREVCELL, or_4_out, in_13);
  and and_7 (and_7_out, INS4, or_7_out);
  and and_8 (and_8_out, in_15, INS4);
  and and_9 (RAMINWRITEMODE, or_4_out, in_15);
  and and_10 (PLUS, or_5_out, rom7);
  and and_11 (MINUS, or_5_out, in_11);
  and and_12 (PRINTRAM, INS4, in_14);
  and and_13 (and_13_out, or_2_out, INS3);
  and and_14 (and_14_out, or_2_out, INS4);
  or or_10 (UPDATEREG, and_7_out, and_13_out);
  or or_11 (UPDATERAM, and_8_out, and_14_out);
  or or_12 (or_12_out, in_3, INS4);
  and and_15 (and_15_out, in_3, and_16_out);
  and and_16 (and_16_out, or_1_out, BRACKET);
  or or_13 (BPclock, and_4_out, d_ff_1_q);
  or or_14 (NEXTROM, or_8_out, d_ff_2_q);
  D_Flip_Flop d_ff_1 (.D(and_15_out), .clk(or_15_out), .Q(d_ff_1_q));  // open: Qn, preset, reset
  or or_15 (or_15_out, or_12_out, and_17_out);
  or or_16 (UPDATEROM, ROMUPDATE, clockdivider_1_out_3);
  LED led_1 (.in(clockdivider_1_out_2));
  CLOCKDIVIDER clockdivider_1 (
    .CLOCK(clockBP), .out_2(clockdivider_1_out_2), .out_3(clockdivider_1_out_3),
    .out_4(clockdivider_1_out_4), .out_5(clockdivider_1_out_5));
  LED led_2 (.in(clockdivider_1_out_3));
  LED led_3 (.in(clockdivider_1_out_4));
  LED led_4 (.in(clockdivider_1_out_5));
  D_Flip_Flop d_ff_2 (.D(in_16), .clk(BYPASS), .Q(d_ff_2_q));  // open: Qn, preset, reset
  D_Flip_Flop d_ff_3 (.D(rom0), .clk(BYPASS), .Q(PREVIOUSROM));  // open: Qn, preset, reset
  and and_17 (and_17_out, clockdivider_1_out_2, is0_1_out_9);
  // BRACKETCOUNT bracketcount_1: pin names not known; wires that end beside it: BRACKETOFF, BRACKETON, clockdivider_1_out_4, bracketcount_1_p4, bracketcount_1_p5, bracketcount_1_p6, bracketcount_1_p7, bracketcount_1_p8, bracketcount_1_p9, bracketcount_1_p10, bracketcount_1_p11
  Is0 is0_1 (
    .in_1(bracketcount_1_p4), .in_2(bracketcount_1_p5), .in_3(bracketcount_1_p6), .in_4(bracketcount_1_p7),
    .in_5(bracketcount_1_p8), .in_6(bracketcount_1_p9), .in_7(bracketcount_1_p10), .in_8(bracketcount_1_p11),
    .out_9(is0_1_out_9));

  // Notes on the sheet:
  //   start
  //   end
  //   start
  //   end
  //   ILFAUDRAIT UN BOUTTON RESET QUI MARCHE
endmodule

module b4PLUS_MINUS (
  input  in_1,
  input  in_2,
  input  in_3,
  input  A1,
  input  PLUS,
  input  MINUS,
  output out_7,
  output out_8,
  output out_9,
  output B1,
  output OVERFLOW
);

  b4ADDER b4adder_1 (
    .B8(in_1), .in_2(in_2), .in_3(in_3), .B1(A1), .A8(MINUS), .in_6(MINUS), .in_7(MINUS), .A1(MINUS),
    .CARRYIN(PLUS), .C8(out_7), .out_11(out_8), .out_12(out_9), .C1(B1), .CARRYOUT(OVERFLOW));
endmodule

module Is0 (
  input  in_1,
  input  in_2,
  input  in_3,
  input  in_4,
  input  in_5,
  input  in_6,
  input  in_7,
  input  in_8,
  output out_9
);

  wire or_1_out, or_2_out, or_3_out, or_4_out, or_5_out, or_6_out, or_7_out;

  or or_1 (or_1_out, in_1, in_2);
  or or_2 (or_2_out, in_3, in_4);
  or or_3 (or_3_out, in_5, in_6);
  or or_4 (or_4_out, in_7, in_8);
  or or_5 (or_5_out, or_1_out, or_2_out);
  or or_6 (or_6_out, or_3_out, or_4_out);
  or or_7 (or_7_out, or_5_out, or_6_out);
  not not_1 (out_9, or_7_out);
endmodule

module PATHDIVIDER2 (
  input  clockBP,
  input  BYPASS,
  input  INS1,
  input  INS2,
  input  ROMUPDATE,
  input  ROM3,
  input  in_7,
  input  ROM1,
  input  BUTTON,
  input  VALID,
  output STOPCLOCK,
  output REDIRECTCLOCK,
  output ROMPLUS1,
  output REFRESHROM,
  output ROMMINUS1,
  output PLUS1,
  output MINUS1,
  output NEXTREG,
  output PREVREG,
  output UPDATERAMREG,
  output UPDATERAMVALUE,
  output GETRAM,
  output UPDATESCREEN,
  output RAMREADYTOWRITE
);

  wire and_1_out, and_2_out, and_3_out, and_4_out, and_5_out, and_6_out, and_7_out, and_8_out, and_9_out,
       and_10_out, and_11_out, and_13_out, and_14_out, and_15_out, and_22_out, and_25_out, and_26_out,
       and_27_out, and_28_out, and_29_out, and_30_out, and_31_out, bracketcountis0_1_valid,
       clockdividerbrct_1_c2, clockdividerbrct_1_c3, clockdividerbrct_1_c4, d_ff_1_q, d_ff_2_q, d_ff_3_q,
       d_ff_4_q, nor_1_out, nor_2_out, not_1_out, not_2_out, not_3_out, not_4_out, not_5_out, not_6_out,
       not_7_out, not_8_out, not_9_out, or_1_out, or_2_out, or_3_out, or_4_out, or_5_out, or_6_out, or_7_out,
       or_8_out, or_9_out;

  LED led_1 (.in(BYPASS));
  LED led_2 (.in(INS1));
  LED led_3 (.in(INS2));
  LED led_4 (.in(ROMUPDATE));
  or or_1 (or_1_out, BYPASS, ROMUPDATE);
  or or_2 (or_2_out, INS1, INS2);
  or or_3 (or_3_out, INS2, ROMUPDATE);
  and and_1 (and_1_out, in_7, ROM1);
  or or_4 (or_4_out, INS1, and_30_out);
  not not_1 (not_1_out, ROM3);
  D_Flip_Flop d_ff_1 (.D(VALID), .clk(or_4_out), .Q(d_ff_1_q));  // open: Qn, preset, reset
  and and_2 (and_2_out, not_1_out, and_1_out);
  and and_3 (and_3_out, ROM3, and_1_out);
  D_Flip_Flop d_ff_2 (.D(ROM3), .clk(BYPASS), .Q(d_ff_2_q));  // open: Qn, preset, reset
  D_Flip_Flop d_ff_3 (.D(in_7), .clk(BYPASS), .Q(d_ff_3_q));  // open: Qn, preset, reset
  D_Flip_Flop d_ff_4 (.D(ROM1), .clk(BYPASS), .Q(d_ff_4_q));  // open: Qn, preset, reset
  not not_2 (not_2_out, BUTTON);
  not not_3 (not_3_out, d_ff_3_q);
  and and_4 (and_4_out, d_ff_3_q, not_4_out);
  not not_4 (not_4_out, d_ff_4_q);
  nor nor_1 (nor_1_out, d_ff_2_q, d_ff_3_q);
  and and_5 (and_5_out, d_ff_2_q, not_3_out);
  and and_6 (and_6_out, d_ff_3_q, d_ff_4_q);
  and and_7 (and_7_out, d_ff_1_q, INS1);
  and and_8 (and_8_out, clockBP, and_11_out);
  nor nor_2 (nor_2_out, d_ff_3_q, d_ff_4_q);
  and and_9 (and_9_out, nor_1_out, d_ff_4_q);
  and and_10 (and_10_out, and_5_out, d_ff_4_q);
  and and_11 (and_11_out, and_6_out, d_ff_1_q);
  or or_5 (or_5_out, BYPASS, and_8_out);
  not not_5 (not_5_out, d_ff_2_q);
  not not_6 (not_6_out, d_ff_2_q);
  and and_12 (STOPCLOCK, INS1, and_13_out);
  and and_13 (and_13_out, not_2_out, and_10_out);
  and and_14 (and_14_out, or_2_out, nor_2_out);
  and and_15 (and_15_out, or_2_out, and_4_out);
  or or_6 (or_6_out, and_4_out, nor_2_out);
  or or_7 (or_7_out, nor_2_out, and_10_out);
  or or_8 (or_8_out, or_2_out, BYPASS);
  or or_9 (or_9_out, INS2, ROMUPDATE);
  and and_16 (PLUS1, not_5_out, and_14_out);
  and and_17 (MINUS1, and_14_out, d_ff_2_q);
  and and_18 (NEXTREG, not_6_out, and_15_out);
  and and_19 (PREVREG, and_15_out, d_ff_2_q);
  and and_20 (UPDATERAMREG, or_6_out, INS2);
  and and_21 (UPDATERAMVALUE, or_7_out, ROMUPDATE);
  and and_22 (and_22_out, or_2_out, and_9_out);
  and and_23 (UPDATESCREEN, INS2, and_9_out);
  and and_24 (RAMREADYTOWRITE, or_3_out, and_10_out);
  and and_25 (and_25_out, or_8_out, and_6_out);
  and and_26 (and_26_out, and_6_out, and_7_out);
  CLOCKDIVIDERBRCT clockdividerbrct_1 (
    .CLOCK(or_5_out), .ZERO(or_1_out), .C2(clockdividerbrct_1_c2), .C3(clockdividerbrct_1_c3),
    .C4(clockdividerbrct_1_c4));  // open: C1
  not not_7 (not_7_out, and_11_out);
  or or_10 (GETRAM, and_22_out, and_25_out);
  not not_8 (not_8_out, d_ff_2_q);
  and and_27 (and_27_out, or_9_out, not_7_out);
  and and_28 (and_28_out, and_11_out, not_8_out);
  and and_29 (and_29_out, and_11_out, d_ff_2_q);
  BRACKETCOUNTIS0 bracketcountis0_1 (
    .UPDATE(and_2_out), .MORE(and_3_out), .LESS(clockdividerbrct_1_c2), .VALID(bracketcountis0_1_valid));
  or or_11 (ROMPLUS1, and_28_out, and_27_out);
  and and_30 (and_30_out, bracketcountis0_1_valid, clockdividerbrct_1_c3);
  and and_31 (and_31_out, clockdividerbrct_1_c4, and_11_out);
  not not_9 (not_9_out, and_30_out);
  and and_32 (REDIRECTCLOCK, not_9_out, and_26_out);
  or or_12 (REFRESHROM, and_31_out, ROMUPDATE);
  LED led_5 (.in(STOPCLOCK));
  LED led_6 (.in(REDIRECTCLOCK));
  LED led_7 (.in(ROMPLUS1));
  LED led_8 (.in(REFRESHROM));
  and and_33 (ROMMINUS1, not_9_out, and_29_out);
  LED led_9 (.in(ROMMINUS1));
  LED led_10 (.in(PLUS1));
  LED led_11 (.in(MINUS1));
  LED led_12 (.in(NEXTREG));
  LED led_13 (.in(PREVREG));
  LED led_14 (.in(UPDATERAMREG));
  LED led_15 (.in(UPDATERAMVALUE));
  LED led_16 (.in(GETRAM));
  LED led_17 (.in(UPDATESCREEN));
  LED led_18 (.in(RAMREADYTOWRITE));

  // Notes on the sheet:
  //   il faut que ca reste allumer le tps de la boucle, ajouter un register desactivé par un compar valide
  //   plusminus
  //   compare
  //   update
  //   if compare is true, then two clock cycle or else update is stuck
endmodule

module CLOCKDIVIDER5 (
  input  BPClock,
  input  CLOCK,
  output BP,
  output b1,
  output b2,
  output b3,
  output b4
);

  wire and_2_out, not_1_out, not_2_out, or_1_out, or_2_out;

  not not_1 (not_1_out, BPClock);
  and and_1 (BP, BPClock, CLOCK);
  or or_1 (or_1_out, or_2_out, b1);
  not not_2 (not_2_out, or_1_out);
  and and_2 (and_2_out, not_1_out, CLOCK);
  D_Flip_Flop d_ff_1 (.D(not_2_out), .clk(and_2_out), .Q(b1));  // open: Qn, preset, reset
  or or_2 (or_2_out, b3, b2);
  D_Flip_Flop d_ff_2 (.D(b1), .clk(and_2_out), .Q(b2));  // open: Qn, preset, reset
  D_Flip_Flop d_ff_3 (.D(b2), .clk(and_2_out), .Q(b3));  // open: Qn, preset, reset
  D_Flip_Flop d_ff_4 (.D(b3), .clk(and_2_out), .Q(b4));  // open: Qn, preset, reset
endmodule

module test (
  input  clockBP,
  input  BYPASS,
  input  INS1,
  input  INS2,
  input  ROMUPDATE,
  input  ROM3,
  input  in_7,
  input  ROM1,
  input  BUTTON,
  input  VALID,
  input  in_11,
  input  in_12,
  input  in_13,
  input  in_14,
  input  in_15,
  input  in_16,
  input  in_17,
  input  in_18,
  input  rom7,
  input  in_20,
  input  in_21,
  input  in_22,
  input  in_23,
  input  in_24,
  input  in_25,
  input  rom0,
  input  BUTTONPRESSED,
  input  BRACKET,
  input  BRACKETON,
  input  BRACKETOFF,
  output STOPCLOCK,
  output REDIRECTCLOCK,
  output ROMPLUS1,
  output REFRESHROM,
  output ROMMINUS1,
  output PLUS1,
  output MINUS1,
  output NEXTREG,
  output PREVREG,
  output UPDATERAMREG,
  output UPDATERAMVALUE,
  output GETRAM,
  output UPDATESCREEN,
  output RAMREADYTOWRITE,
  output BPclock,
  output NEXTROM,
  output PREVIOUSROM,
  output UPDATEROM,
  output READMRAM,
  output NEXTCELL,
  output PREVCELL,
  output UPDATEREG,
  output UPDATERAM,
  output RAMINWRITEMODE,
  output PLUS,
  output MINUS,
  output PRINTRAM,
  output forwardif1
);

  wire and_1_out, and_2_out, and_3_out, and_4_out, and_5_out, and_6_out, and_7_out, and_8_out, and_9_out,
       and_10_out, and_11_out, and_12_out, and_13_out, and_14_out, and_15_out, and_17_out, and_18_out,
       and_19_out, and_22_out, and_23_out, and_24_out, and_25_out, and_36_out, and_39_out, and_40_out,
       and_41_out, and_42_out, and_43_out, and_44_out, and_46_out, and_47_out, bracketcount_1_p4,
       bracketcount_1_p5, bracketcount_1_p6, bracketcount_1_p7, bracketcount_1_p8, bracketcount_1_p9,
       bracketcount_1_p10, bracketcount_1_p11, bracketcountis0_1_valid, clockdivider_1_out_2,
       clockdivider_1_out_3, clockdivider_1_out_4, clockdivider_1_out_5, clockdividerbrct_1_c2,
       clockdividerbrct_1_c3, clockdividerbrct_1_c4, d_ff_1_q, d_ff_2_q, d_ff_3_q, d_ff_4_q, d_ff_5_q,
       is0_1_out_9, nor_1_out, nor_2_out, not_1_out, not_2_out, not_3_out, not_4_out, not_5_out, not_6_out,
       not_7_out, not_8_out, not_9_out, not_10_out, or_1_out, or_2_out, or_3_out, or_4_out, or_5_out,
       or_6_out, or_7_out, or_8_out, or_9_out, or_10_out, or_11_out, or_13_out, or_14_out, or_15_out,
       or_19_out, or_23_out;

  LED led_1 (.in(BYPASS));
  LED led_2 (.in(INS1));
  LED led_3 (.in(INS2));
  LED led_4 (.in(ROMUPDATE));
  or or_1 (or_1_out, INS1, INS2);
  or or_2 (or_2_out, INS2, ROMUPDATE);
  and and_1 (and_1_out, in_7, ROM1);
  or or_3 (or_3_out, in_25, rom0);
  not not_1 (not_1_out, ROM3);
  or or_4 (or_4_out, rom7, in_20);
  and and_2 (and_2_out, not_1_out, and_1_out);
  and and_3 (and_3_out, ROM3, and_1_out);
  D_Flip_Flop d_ff_1 (.D(ROM3), .clk(BYPASS), .Q(d_ff_1_q));  // open: Qn, preset, reset
  D_Flip_Flop d_ff_2 (.D(in_7), .clk(BYPASS), .Q(d_ff_2_q));  // open: Qn, preset, reset
  D_Flip_Flop d_ff_3 (.D(ROM1), .clk(BYPASS), .Q(d_ff_3_q));  // open: Qn, preset, reset
  and and_4 (and_4_out, in_24, not_2_out);
  not not_2 (not_2_out, BUTTONPRESSED);
  not not_3 (not_3_out, BUTTON);
  not not_4 (not_4_out, d_ff_2_q);
  or or_5 (or_5_out, in_15, in_16);
  and and_5 (and_5_out, d_ff_2_q, not_5_out);
  not not_5 (not_5_out, d_ff_3_q);
  nor nor_1 (nor_1_out, d_ff_1_q, d_ff_2_q);
  and and_6 (and_6_out, d_ff_1_q, not_4_out);
  and and_7 (and_7_out, d_ff_2_q, d_ff_3_q);
  and and_8 (and_8_out, VALID, INS2);
  or or_6 (or_6_out, in_12, in_11);
  or or_7 (or_7_out, in_15, in_16);
  or or_8 (or_8_out, or_5_out, in_14);
  nor nor_2 (nor_2_out, d_ff_2_q, d_ff_3_q);
  and and_9 (and_9_out, nor_1_out, d_ff_3_q);
  and and_10 (and_10_out, and_6_out, d_ff_3_q);
  and and_11 (and_11_out, and_7_out, VALID);
  and and_12 (and_12_out, or_3_out, or_6_out);
  and and_13 (and_13_out, or_7_out, in_23);
  or or_9 (or_9_out, in_22, in_21);
  and and_14 (and_14_out, clockBP, and_11_out);
  not not_6 (not_6_out, d_ff_1_q);
  not not_7 (not_7_out, d_ff_1_q);
  or or_10 (or_10_out, or_1_out, or_2_out);
  and and_15 (and_15_out, in_11, and_4_out);
  or or_11 (or_11_out, in_17, in_18);
  or or_12 (READMRAM, and_12_out, and_13_out);
  and and_16 (STOPCLOCK, INS1, and_17_out);
  and and_17 (and_17_out, not_3_out, and_10_out);
  and and_18 (and_18_out, or_1_out, nor_2_out);
  and and_19 (and_19_out, or_1_out, and_5_out);
  or or_13 (or_13_out, and_5_out, nor_2_out);
  or or_14 (or_14_out, nor_2_out, and_10_out);
  and and_20 (NEXTCELL, in_21, or_5_out);
  and and_21 (PREVCELL, or_5_out, in_22);
  and and_22 (and_22_out, in_16, or_9_out);
  and and_23 (and_23_out, or_4_out, in_15);
  and and_24 (and_24_out, in_24, in_16);
  and and_25 (and_25_out, or_4_out, in_16);
  and and_26 (RAMINWRITEMODE, or_5_out, in_24);
  and and_27 (PLUS, or_8_out, rom7);
  and and_28 (MINUS, or_8_out, in_20);
  and and_29 (PRINTRAM, in_16, in_23);
  or or_15 (or_15_out, INS2, ROMUPDATE);
  and and_30 (PLUS1, not_6_out, and_18_out);
  and and_31 (MINUS1, and_18_out, d_ff_1_q);
  and and_32 (NEXTREG, not_7_out, and_19_out);
  and and_33 (PREVREG, and_19_out, d_ff_1_q);
  and and_34 (UPDATERAMREG, or_13_out, INS2);
  and and_35 (UPDATERAMVALUE, or_14_out, ROMUPDATE);
  and and_36 (and_36_out, or_1_out, and_9_out);
  and and_37 (UPDATESCREEN, INS2, and_9_out);
  and and_38 (RAMREADYTOWRITE, or_2_out, and_10_out);
  and and_39 (and_39_out, or_10_out, and_7_out);
  and and_40 (and_40_out, and_7_out, and_8_out);
  or or_16 (UPDATEREG, and_22_out, and_23_out);
  or or_17 (UPDATERAM, and_24_out, and_25_out);
  CLOCKDIVIDERBRCT clockdividerbrct_1 (
    .CLOCK(and_14_out), .C2(clockdividerbrct_1_c2), .C3(clockdividerbrct_1_c3), .C4(clockdividerbrct_1_c4));  // open: ZERO, C1
  not not_8 (not_8_out, and_11_out);
  or or_18 (GETRAM, and_36_out, and_39_out);
  or or_19 (or_19_out, in_12, in_16);
  and and_41 (and_41_out, in_12, and_42_out);
  and and_42 (and_42_out, or_3_out, BRACKET);
  not not_9 (not_9_out, d_ff_1_q);
  and and_43 (and_43_out, or_15_out, not_8_out);
  or or_20 (BPclock, and_15_out, d_ff_4_q);
  and and_44 (and_44_out, and_11_out, not_9_out);
  and and_45 (ROMMINUS1, and_11_out, d_ff_1_q);
  or or_21 (NEXTROM, or_11_out, d_ff_5_q);
  or or_22 (UPDATEROM, in_18, clockdivider_1_out_3);
  D_Flip_Flop d_ff_4 (.D(and_41_out), .clk(or_23_out), .Q(d_ff_4_q));  // open: Qn, preset, reset
  or or_23 (or_23_out, or_19_out, and_47_out);
  BRACKETCOUNTIS0 bracketcountis0_1 (
    .UPDATE(and_2_out), .MORE(and_3_out), .LESS(clockdividerbrct_1_c2), .VALID(bracketcountis0_1_valid));
  or or_24 (ROMPLUS1, and_44_out, and_43_out);
  and and_46 (and_46_out, bracketcountis0_1_valid, clockdividerbrct_1_c3);
  LED led_5 (.in(clockdivider_1_out_2));
  CLOCKDIVIDER clockdivider_1 (
    .out_2(clockdivider_1_out_2), .out_3(clockdivider_1_out_3), .out_4(clockdivider_1_out_4),
    .out_5(clockdivider_1_out_5));  // open: CLOCK
  LED led_6 (.in(clockdivider_1_out_3));
  LED led_7 (.in(clockdivider_1_out_4));
  LED led_8 (.in(clockdivider_1_out_5));
  not not_10 (not_10_out, and_46_out);
  or or_25 (REFRESHROM, clockdividerbrct_1_c4, ROMUPDATE);
  and and_47 (and_47_out, clockdivider_1_out_2, is0_1_out_9);
  LED led_9 (.in(STOPCLOCK));
  and and_48 (REDIRECTCLOCK, not_10_out, and_40_out);
  LED led_10 (.in(REDIRECTCLOCK));
  LED led_11 (.in(ROMPLUS1));
  LED led_12 (.in(REFRESHROM));
  LED led_13 (.in(ROMMINUS1));
  LED led_14 (.in(PLUS1));
  LED led_15 (.in(MINUS1));
  LED led_16 (.in(NEXTREG));
  LED led_17 (.in(PREVREG));
  LED led_18 (.in(UPDATERAMREG));
  LED led_19 (.in(UPDATERAMVALUE));
  LED led_20 (.in(GETRAM));
  LED led_21 (.in(UPDATESCREEN));
  LED led_22 (.in(RAMREADYTOWRITE));
  D_Flip_Flop d_ff_5 (.D(in_25), .clk(in_11), .Q(d_ff_5_q));  // open: Qn, preset, reset
  D_Flip_Flop d_ff_6 (.D(rom0), .clk(in_11), .Q(PREVIOUSROM));  // open: Qn, preset, reset
  // BRACKETCOUNT bracketcount_1: pin names not known; wires that end beside it: BRACKETOFF, BRACKETON, clockdivider_1_out_4, bracketcount_1_p4, bracketcount_1_p5, bracketcount_1_p6, bracketcount_1_p7, bracketcount_1_p8, bracketcount_1_p9, bracketcount_1_p10, bracketcount_1_p11
  Is0 is0_1 (
    .in_1(bracketcount_1_p4), .in_2(bracketcount_1_p5), .in_3(bracketcount_1_p6), .in_4(bracketcount_1_p7),
    .in_5(bracketcount_1_p8), .in_6(bracketcount_1_p9), .in_7(bracketcount_1_p10), .in_8(bracketcount_1_p11),
    .out_9(is0_1_out_9));

  // Notes on the sheet:
  //   start
  //   end
  //   plusminus
  //   compare
  //   update
  //   start
  //   end
endmodule

module CLOCKDIVIDERBRCT (
  input  CLOCK,
  input  ZERO,
  output C1,
  output C2,
  output C3,
  output C4
);

  wire and_1_out, and_2_out, and_3_out, not_1_out, not_2_out, or_1_out, or_2_out;

  or or_1 (or_1_out, or_2_out, C1);
  not not_1 (not_1_out, or_1_out);
  D_Flip_Flop d_ff_1 (.D(not_1_out), .clk(CLOCK), .Q(C1));  // open: Qn, preset, reset
  not not_2 (not_2_out, ZERO);
  or or_2 (or_2_out, C3, C2);
  D_Flip_Flop d_ff_2 (.D(and_1_out), .clk(CLOCK), .Q(C2));  // open: Qn, preset, reset
  and and_1 (and_1_out, C1, not_2_out);
  D_Flip_Flop d_ff_3 (.D(and_2_out), .clk(CLOCK), .Q(C3));  // open: Qn, preset, reset
  and and_2 (and_2_out, C2, not_2_out);
  D_Flip_Flop d_ff_4 (.D(and_3_out), .clk(CLOCK), .Q(C4));  // open: Qn, preset, reset
  and and_3 (and_3_out, C3, not_2_out);
endmodule

module BRACKETCOUNTIS0 (
  input  UPDATE,
  input  MORE,
  input  LESS,
  output VALID
);

  wire bracketcount_1_b1, bracketcount_1_b128, bracketcount_1_out_5, bracketcount_1_out_6,
       bracketcount_1_out_7, bracketcount_1_out_8, bracketcount_1_out_9, bracketcount_1_out_10;

  BRACKETCOUNT bracketcount_1 (
    .UPDATE(UPDATE), .MORE(MORE), .LESS(LESS), .B128(bracketcount_1_b128), .out_5(bracketcount_1_out_5),
    .out_6(bracketcount_1_out_6), .out_7(bracketcount_1_out_7), .out_8(bracketcount_1_out_8),
    .out_9(bracketcount_1_out_9), .out_10(bracketcount_1_out_10), .B1(bracketcount_1_b1));  // open: OVERFLOW
  Is0 is0_1 (
    .in_1(bracketcount_1_b128), .in_2(bracketcount_1_out_5), .in_3(bracketcount_1_out_6),
    .in_4(bracketcount_1_out_7), .in_5(bracketcount_1_out_8), .in_6(bracketcount_1_out_9),
    .in_7(bracketcount_1_out_10), .in_8(bracketcount_1_b1), .out_9(VALID));
endmodule

module ADRESSEMAP2 (
  input  NEXT_CELL,
  input  PREVIOUS_CELL,
  input  UPDATE,
  output B65536,
  output out_5,
  output out_6,
  output out_7,
  output out_8,
  output out_9,
  output out_10,
  output out_11,
  output out_12,
  output out_13,
  output out_14,
  output out_15,
  output out_16,
  output out_17,
  output out_18,
  output B1,
  output OVERFLOW
);

  wire [15:0] b16plus_minus_1_b65525;

  x16COUNTER x16counter_1 (.RESET(B65536));
  LED led_1 (.in(B65536));
  LED led_2 (.in(out_5));
  LED led_3 (.in(out_6));
  LED led_4 (.in(out_7));
  LED led_5 (.in(out_8));
  LED led_6 (.in(out_9));
  LED led_7 (.in(out_10));
  LED led_8 (.in(out_11));
  LED led_9 (.in(out_12));
  LED led_10 (.in(out_13));
  LED led_11 (.in(out_14));
  LED led_12 (.in(out_15));
  LED led_13 (.in(out_16));
  LED led_14 (.in(out_17));
  LED led_15 (.in(out_18));
  LED led_16 (.in(B1));
  b16PLUS_MINUS b16plus_minus_1 (
    .A65536(B65536), .in_2(out_5), .in_3(out_6), .in_4(out_7), .in_5(out_8), .in_6(out_9), .in_7(out_10),
    .A256(out_11), .A128(out_12), .in_10(out_13), .in_11(out_14), .in_12(out_15), .in_13(out_16),
    .in_14(out_17), .in_15(out_18), .A1(B1), .PLUS(NEXT_CELL), .MINUS(PREVIOUS_CELL), .OVERFLOW(OVERFLOW),
    .b65525(b16plus_minus_1_b65525[0]), .out_21(b16plus_minus_1_b65525[1]),
    .out_22(b16plus_minus_1_b65525[2]), .out_23(b16plus_minus_1_b65525[3]),
    .out_24(b16plus_minus_1_b65525[4]), .out_25(b16plus_minus_1_b65525[5]),
    .out_26(b16plus_minus_1_b65525[6]), .b256(b16plus_minus_1_b65525[7]), .B128(b16plus_minus_1_b65525[8]),
    .out_29(b16plus_minus_1_b65525[9]), .out_30(b16plus_minus_1_b65525[10]),
    .out_31(b16plus_minus_1_b65525[11]), .out_32(b16plus_minus_1_b65525[12]),
    .out_33(b16plus_minus_1_b65525[13]), .out_34(b16plus_minus_1_b65525[14]), .B1(b16plus_minus_1_b65525[15]));
  LED led_17 (.in(b16plus_minus_1_b65525[0]));
  LED led_18 (.in(b16plus_minus_1_b65525[1]));
  LED led_19 (.in(b16plus_minus_1_b65525[2]));
  LED led_20 (.in(b16plus_minus_1_b65525[3]));
  LED led_21 (.in(b16plus_minus_1_b65525[4]));
  LED led_22 (.in(b16plus_minus_1_b65525[5]));
  LED led_23 (.in(b16plus_minus_1_b65525[6]));
  LED led_24 (.in(b16plus_minus_1_b65525[7]));
  LED led_25 (.in(b16plus_minus_1_b65525[8]));
  LED led_26 (.in(b16plus_minus_1_b65525[9]));
  LED led_27 (.in(b16plus_minus_1_b65525[10]));
  LED led_28 (.in(b16plus_minus_1_b65525[11]));
  LED led_29 (.in(b16plus_minus_1_b65525[12]));
  LED led_30 (.in(b16plus_minus_1_b65525[13]));
  LED led_31 (.in(b16plus_minus_1_b65525[14]));
  LED led_32 (.in(b16plus_minus_1_b65525[15]));
endmodule

module PATHDIVIDER3 (
  input  BPClock,
  input  CLOCK,
  input  ROM3,
  input  in_4,
  input  ROM1,
  input  BUTTON,
  input  VALID,
  output STOPCLOCK,
  output REDIRECTCLOCK,
  output ROMPLUS1,
  output REFRESHROM,
  output ROMMINUS1,
  output PLUS1,
  output MINUS1,
  output NEXTREG,
  output PREVREG,
  output UPDATERAMREG,
  output UPDATERAMVALUE,
  output GETRAM,
  output UPDATESCREEN,
  output RAMREADYTOWRITE
);

  wire and_1_out, and_2_out, and_3_out, and_4_out, and_5_out, and_6_out, and_7_out, and_8_out, and_9_out,
       and_10_out, and_11_out, and_12_out, and_13_out, and_14_out, and_15_out, and_16_out, and_17_out,
       and_18_out, and_19_out, and_21_out, and_28_out, and_31_out, and_32_out, and_33_out, and_34_out,
       and_35_out, and_36_out, bracketcountis0_1_valid, d_ff_1_q, d_ff_2_q, d_ff_3_q, d_ff_4_q, d_ff_5_q,
       d_ff_6_q, d_ff_7_q, d_ff_8_q, d_ff_9_q, d_ff_10_q, d_ff_11_q, d_ff_12_q, nor_1_out, nor_2_out,
       not_1_out, not_2_out, not_3_out, not_4_out, not_5_out, not_6_out, not_7_out, not_8_out, not_9_out,
       not_10_out, not_11_out, not_12_out, not_13_out, or_1_out, or_2_out, or_3_out, or_4_out, or_5_out,
       or_6_out, or_7_out, or_8_out, or_9_out, or_10_out, or_11_out, or_12_out, or_13_out;

  or or_1 (or_1_out, or_2_out, d_ff_1_q);
  not not_1 (not_1_out, or_1_out);
  D_Flip_Flop d_ff_1 (.D(not_1_out), .clk(and_1_out), .Q(d_ff_1_q));  // open: Qn, preset, reset
  and and_1 (and_1_out, not_2_out, CLOCK);
  not not_2 (not_2_out, BPClock);
  or or_2 (or_2_out, d_ff_3_q, d_ff_2_q);
  D_Flip_Flop d_ff_2 (.D(d_ff_1_q), .clk(and_1_out), .Q(d_ff_2_q));  // open: Qn, preset, reset
  and and_2 (and_2_out, CLOCK, BPClock);
  D_Flip_Flop d_ff_3 (.D(d_ff_2_q), .clk(and_1_out), .Q(d_ff_3_q));  // open: Qn, preset, reset
  and and_3 (and_3_out, and_2_out, and_16_out);
  and and_4 (and_4_out, in_4, ROM1);
  D_Flip_Flop d_ff_4 (.D(d_ff_3_q), .clk(and_1_out), .Q(d_ff_4_q));  // open: Qn, preset, reset
  or or_3 (or_3_out, or_9_out, d_ff_5_q);
  not not_3 (not_3_out, or_3_out);
  D_Flip_Flop d_ff_5 (.D(not_3_out), .clk(or_4_out), .Q(d_ff_5_q));  // open: Qn, preset, reset
  or or_4 (or_4_out, d_ff_1_q, and_3_out);
  or or_5 (or_5_out, d_ff_1_q, d_ff_4_q);
  or or_6 (or_6_out, d_ff_2_q, d_ff_3_q);
  or or_7 (or_7_out, d_ff_3_q, d_ff_4_q);
  or or_8 (or_8_out, d_ff_2_q, and_34_out);
  or or_9 (or_9_out, d_ff_11_q, d_ff_7_q);
  LED led_1 (.in(d_ff_5_q));
  not not_4 (not_4_out, or_5_out);
  not not_5 (not_5_out, ROM3);
  D_Flip_Flop d_ff_6 (.D(VALID), .clk(or_8_out), .Q(d_ff_6_q));  // open: Qn, preset, reset
  D_Flip_Flop d_ff_7 (.D(and_5_out), .clk(or_4_out), .Q(d_ff_7_q));  // open: Qn, preset, reset
  and and_5 (and_5_out, d_ff_5_q, not_4_out);
  and and_6 (and_6_out, not_5_out, and_4_out);
  and and_7 (and_7_out, ROM3, and_4_out);
  D_Flip_Flop d_ff_8 (.D(ROM3), .clk(d_ff_1_q), .Q(d_ff_8_q));  // open: Qn, preset, reset
  D_Flip_Flop d_ff_9 (.D(in_4), .clk(d_ff_1_q), .Q(d_ff_9_q));  // open: Qn, preset, reset
  D_Flip_Flop d_ff_10 (.D(ROM1), .clk(d_ff_1_q), .Q(d_ff_10_q));  // open: Qn, preset, reset
  D_Flip_Flop d_ff_11 (.D(and_8_out), .clk(or_4_out), .Q(d_ff_11_q));  // open: Qn, preset, reset
  and and_8 (and_8_out, d_ff_7_q, not_4_out);
  not not_6 (not_6_out, d_ff_10_q);
  nor nor_1 (nor_1_out, d_ff_8_q, d_ff_9_q);
  not not_7 (not_7_out, BUTTON);
  not not_8 (not_8_out, d_ff_9_q);
  nor nor_2 (nor_2_out, d_ff_9_q, d_ff_10_q);
  and and_9 (and_9_out, d_ff_9_q, not_6_out);
  and and_10 (and_10_out, nor_1_out, d_ff_10_q);
  and and_11 (and_11_out, d_ff_8_q, not_8_out);
  and and_12 (and_12_out, d_ff_9_q, d_ff_10_q);
  and and_13 (and_13_out, d_ff_6_q, d_ff_2_q);
  D_Flip_Flop d_ff_12 (.D(and_14_out), .clk(or_4_out), .Q(d_ff_12_q));  // open: Qn, preset, reset
  and and_14 (and_14_out, d_ff_11_q, not_4_out);
  and and_15 (and_15_out, and_11_out, d_ff_10_q);
  and and_16 (and_16_out, and_12_out, d_ff_6_q);
  LED led_2 (.in(d_ff_7_q));
  LED led_3 (.in(d_ff_11_q));
  LED led_4 (.in(d_ff_12_q));
  and and_17 (and_17_out, not_7_out, and_15_out);
  not not_9 (not_9_out, d_ff_8_q);
  not not_10 (not_10_out, d_ff_8_q);
  and and_18 (and_18_out, or_6_out, nor_2_out);
  not not_11 (not_11_out, d_ff_8_q);
  and and_19 (and_19_out, or_6_out, and_9_out);
  or or_10 (or_10_out, and_9_out, nor_2_out);
  or or_11 (or_11_out, nor_2_out, and_15_out);
  and and_20 (STOPCLOCK, d_ff_2_q, and_17_out);
  and and_21 (and_21_out, and_16_out, not_9_out);
  and and_22 (PLUS1, not_10_out, and_18_out);
  and and_23 (MINUS1, and_18_out, d_ff_8_q);
  and and_24 (NEXTREG, not_11_out, and_19_out);
  and and_25 (PREVREG, and_19_out, d_ff_8_q);
  and and_26 (UPDATERAMREG, or_10_out, d_ff_3_q);
  and and_27 (UPDATERAMVALUE, or_11_out, d_ff_4_q);
  and and_28 (and_28_out, or_6_out, and_10_out);
  and and_29 (UPDATESCREEN, d_ff_3_q, and_10_out);
  and and_30 (RAMREADYTOWRITE, or_7_out, and_15_out);
  or or_12 (or_12_out, or_6_out, d_ff_1_q);
  and and_31 (and_31_out, or_12_out, and_12_out);
  and and_32 (and_32_out, and_12_out, and_13_out);
  or or_13 (or_13_out, d_ff_3_q, d_ff_4_q);
  not not_12 (not_12_out, and_16_out);
  or or_14 (GETRAM, and_28_out, and_31_out);
  or or_15 (ROMPLUS1, and_21_out, and_33_out);
  and and_33 (and_33_out, or_13_out, not_12_out);
  BRACKETCOUNTIS0 bracketcountis0_1 (
    .UPDATE(d_ff_7_q), .MORE(and_6_out), .LESS(and_7_out), .VALID(bracketcountis0_1_valid));
  and and_34 (and_34_out, d_ff_11_q, bracketcountis0_1_valid);
  and and_35 (and_35_out, d_ff_12_q, and_16_out);
  and and_36 (and_36_out, and_16_out, d_ff_8_q);
  not not_13 (not_13_out, and_34_out);
  or or_16 (REFRESHROM, and_35_out, d_ff_4_q);
  LED led_5 (.in(STOPCLOCK));
  and and_37 (REDIRECTCLOCK, not_13_out, and_32_out);
  LED led_6 (.in(REDIRECTCLOCK));
  LED led_7 (.in(ROMPLUS1));
  LED led_8 (.in(REFRESHROM));
  and and_38 (ROMMINUS1, not_13_out, and_36_out);
  LED led_9 (.in(ROMMINUS1));
  LED led_10 (.in(PLUS1));
  LED led_11 (.in(MINUS1));
  LED led_12 (.in(NEXTREG));
  LED led_13 (.in(PREVREG));
  LED led_14 (.in(UPDATERAMREG));
  LED led_15 (.in(UPDATERAMVALUE));
  LED led_16 (.in(GETRAM));
  LED led_17 (.in(UPDATESCREEN));
  LED led_18 (.in(RAMREADYTOWRITE));
endmodule

module V3 (
);

  wire and_1_out, button_1_out, clock_1_out, not_1_out, not_2_out, pathdivider3_1_getram,
       pathdivider3_1_minus1, pathdivider3_1_nextreg, pathdivider3_1_plus1, pathdivider3_1_prevreg,
       pathdivider3_1_ramreadytowrite, pathdivider3_1_redirectclock, pathdivider3_1_stopclock,
       pathdivider3_1_updateramreg, pathdivider3_1_updateramvalue, pathdivider3_1_updatescreen,
       ramarchi2_1_yes, romarchi_1_ins1, romarchi_1_ins2, romarchi_1_ins3;
  wire [2:0] pathdivider3_1_romplus1;

  Clock clock_1 (.out(clock_1_out));
  and and_1 (and_1_out, not_1_out, clock_1_out);
  not not_1 (not_1_out, pathdivider3_1_stopclock);
  ROMARCHi romarchi_1 (
    .NEXTINS(pathdivider3_1_romplus1[0]), .UPDATE(pathdivider3_1_romplus1[1]),
    .PREVIOUSINS(pathdivider3_1_romplus1[2]), .INS1(romarchi_1_ins1), .INS2(romarchi_1_ins2),
    .INS3(romarchi_1_ins3));
  not not_2 (not_2_out, romarchi_1_ins1);
  Button button_1 (.out(button_1_out));
  PATHDIVIDER3 pathdivider3_1 (
    .BPClock(pathdivider3_1_redirectclock), .CLOCK(and_1_out), .ROM3(romarchi_1_ins1),
    .in_4(romarchi_1_ins2), .ROM1(romarchi_1_ins3), .BUTTON(button_1_out), .VALID(ramarchi2_1_yes),
    .STOPCLOCK(pathdivider3_1_stopclock), .REDIRECTCLOCK(pathdivider3_1_redirectclock),
    .ROMPLUS1(pathdivider3_1_romplus1[0]), .REFRESHROM(pathdivider3_1_romplus1[1]),
    .ROMMINUS1(pathdivider3_1_romplus1[2]), .PLUS1(pathdivider3_1_plus1), .MINUS1(pathdivider3_1_minus1),
    .NEXTREG(pathdivider3_1_nextreg), .PREVREG(pathdivider3_1_prevreg),
    .UPDATERAMREG(pathdivider3_1_updateramreg), .UPDATERAMVALUE(pathdivider3_1_updateramvalue),
    .GETRAM(pathdivider3_1_getram), .UPDATESCREEN(pathdivider3_1_updatescreen),
    .RAMREADYTOWRITE(pathdivider3_1_ramreadytowrite));
  RAMARCHI2 ramarchi2_1 (
    .PLUS(pathdivider3_1_plus1), .MINUS(pathdivider3_1_minus1), .pls(pathdivider3_1_nextreg),
    .min(pathdivider3_1_prevreg), .UPDATEREGS(pathdivider3_1_updateramreg),
    .UPDATERAM(pathdivider3_1_updateramvalue), .READ(pathdivider3_1_getram),
    .screen(pathdivider3_1_ramreadytowrite), .WRITE(not_2_out), .FORWARD_if1(not_2_out), .YES(ramarchi2_1_yes));
endmodule

module RAMARCHI2 (
  input  PLUS,
  input  MINUS,
  input  pls,
  input  min,
  input  UPDATEREGS,
  input  UPDATERAM,
  input  READ,
  input  screen,
  input  WRITE,
  input  FORWARD_if1,
  output YES
);

  wire and_3_out, and_4_out, and_5_out, and_6_out, and_7_out, and_8_out, and_9_out, and_10_out, and_11_out,
       and_12_out, and_13_out, and_14_out, and_15_out, and_16_out, and_17_out, and_18_out, and_19_out,
       and_20_out, and_21_out, and_22_out, and_23_out, and_24_out, and_25_out, and_26_out, and_27_out,
       and_28_out, and_29_out, and_30_out, and_31_out, and_32_out, and_33_out, and_34_out, and_35_out,
       and_36_out, and_37_out, and_38_out, and_39_out, and_40_out, and_41_out, and_42_out, and_43_out,
       and_44_out, and_45_out, and_46_out, and_48_out, and_49_out, and_50_out, and_51_out, not_1_out,
       not_3_out, or_2_out, or_3_out, or_4_out, or_5_out, or_6_out, or_7_out, or_8_out, or_9_out, or_10_out,
       or_11_out, or_12_out, or_13_out, or_14_out, or_15_out, or_16_out, or_17_out, or_18_out, or_19_out,
       or_20_out, or_21_out, or_22_out, or_23_out, or_24_out, or_25_out, or_26_out, or_27_out, or_28_out,
       or_29_out, or_30_out, or_31_out, or_32_out, xor_1_out, xor_2_out, xor_3_out, xor_4_out, xor_5_out,
       xor_6_out, xor_7_out, xor_8_out, xor_9_out, xor_10_out, xor_11_out, xor_12_out, xor_13_out,
       xor_14_out, xor_15_out, xor_16_out, xor_17_out, xor_18_out, xor_19_out, xor_20_out, xor_21_out,
       xor_22_out, xor_23_out, xor_24_out, xor_25_out, xor_26_out, xor_27_out, xor_28_out, xor_29_out,
       xor_30_out, xor_31_out, xor_32_out, xor_33_out, xor_34_out, xor_35_out, xor_36_out, xor_37_out,
       xor_38_out, xor_39_out, xor_40_out, xor_41_out, xor_42_out, xor_43_out, xor_44_out, xor_45_out,
       xor_46_out, xor_47_out, xor_48_out;
  wire [7:0] and_1_out, and_2_out, and_47_out, bit_extender_1_out, bit_extender_2_out, d_ff_9_q, not_2_out,
       or_1_out, ram_1_dout, undriven;
  wire [15:0] d_ff_4_q;

  D_Flip_Flop d_ff_1 (.D(xor_9_out), .clk(UPDATEREGS), .Q(d_ff_4_q[3]));  // open: Qn, preset, reset
  D_Flip_Flop d_ff_2 (.D(xor_10_out), .clk(UPDATEREGS), .Q(d_ff_4_q[2]));  // open: Qn, preset, reset
  D_Flip_Flop d_ff_3 (.D(xor_11_out), .clk(UPDATEREGS), .Q(d_ff_4_q[1]));  // open: Qn, preset, reset
  D_Flip_Flop d_ff_4 (.D(xor_12_out), .clk(UPDATEREGS), .Q(d_ff_4_q[0]));  // open: Qn, preset, reset
  // DipSwitch dipswitch_1: pin names not known
  not not_1 (not_1_out, WRITE);
  D_Flip_Flop d_ff_5 (.D(xor_26_out), .clk(UPDATEREGS), .Q(d_ff_4_q[6]));  // open: Qn, preset, reset
  D_Flip_Flop d_ff_6 (.D(xor_27_out), .clk(UPDATEREGS), .Q(d_ff_4_q[5]));  // open: Qn, preset, reset
  D_Flip_Flop d_ff_7 (.D(xor_28_out), .clk(UPDATEREGS), .Q(d_ff_4_q[4]));  // open: Qn, preset, reset
  assign or_1_out = and_1_out | and_2_out;  // OR_Gate or_1, 8 bits wide
  assign and_1_out = undriven & not_2_out;  // AND_Gate and_1, 8 bits wide
  assign not_2_out = ~bit_extender_1_out;  // NOT_Gate not_2, 8 bits wide
  assign bit_extender_1_out = {{7{not_1_out}}, not_1_out};  // Bit_Extender bit_extender_1
  D_Flip_Flop d_ff_8 (.D(xor_25_out), .clk(UPDATEREGS), .Q(d_ff_4_q[7]));  // open: Qn, preset, reset
  assign and_2_out = bit_extender_1_out & d_ff_9_q;  // AND_Gate and_2, 8 bits wide
  D_Flip_Flop d_ff_9 (.D(xor_16_out), .clk(UPDATEREGS), .Q(d_ff_9_q[0]));  // open: Qn, preset, reset
  D_Flip_Flop d_ff_10 (.D(xor_37_out), .clk(UPDATEREGS), .Q(d_ff_4_q[11]));  // open: Qn, preset, reset
  D_Flip_Flop d_ff_11 (.D(xor_38_out), .clk(UPDATEREGS), .Q(d_ff_4_q[10]));  // open: Qn, preset, reset
  D_Flip_Flop d_ff_12 (.D(xor_39_out), .clk(UPDATEREGS), .Q(d_ff_4_q[9]));  // open: Qn, preset, reset
  D_Flip_Flop d_ff_13 (.D(xor_40_out), .clk(UPDATEREGS), .Q(d_ff_4_q[8]));  // open: Qn, preset, reset
  D_Flip_Flop d_ff_14 (.D(xor_13_out), .clk(UPDATEREGS), .Q(d_ff_9_q[3]));  // open: Qn, preset, reset
  D_Flip_Flop d_ff_15 (.D(xor_14_out), .clk(UPDATEREGS), .Q(d_ff_9_q[2]));  // open: Qn, preset, reset
  D_Flip_Flop d_ff_16 (.D(xor_15_out), .clk(UPDATEREGS), .Q(d_ff_9_q[1]));  // open: Qn, preset, reset
  D_Flip_Flop d_ff_17 (.D(xor_46_out), .clk(UPDATEREGS), .Q(d_ff_4_q[14]));  // open: Qn, preset, reset
  D_Flip_Flop d_ff_18 (.D(xor_47_out), .clk(UPDATEREGS), .Q(d_ff_4_q[13]));  // open: Qn, preset, reset
  D_Flip_Flop d_ff_19 (.D(xor_48_out), .clk(UPDATEREGS), .Q(d_ff_4_q[12]));  // open: Qn, preset, reset
  D_Flip_Flop d_ff_20 (.D(xor_29_out), .clk(UPDATEREGS), .Q(d_ff_9_q[7]));  // open: Qn, preset, reset
  D_Flip_Flop d_ff_21 (.D(xor_30_out), .clk(UPDATEREGS), .Q(d_ff_9_q[6]));  // open: Qn, preset, reset
  D_Flip_Flop d_ff_22 (.D(xor_31_out), .clk(UPDATEREGS), .Q(d_ff_9_q[5]));  // open: Qn, preset, reset
  D_Flip_Flop d_ff_23 (.D(xor_32_out), .clk(UPDATEREGS), .Q(d_ff_9_q[4]));  // open: Qn, preset, reset
  D_Flip_Flop d_ff_24 (.D(xor_45_out), .clk(UPDATEREGS), .Q(d_ff_4_q[15]));  // open: Qn, preset, reset
  and and_3 (and_3_out, d_ff_4_q[3], min);
  xor xor_1 (xor_1_out, d_ff_4_q[3], min);
  and and_4 (and_4_out, d_ff_4_q[2], min);
  xor xor_2 (xor_2_out, d_ff_4_q[2], min);
  and and_5 (and_5_out, d_ff_4_q[1], min);
  xor xor_3 (xor_3_out, d_ff_4_q[1], min);
  and and_6 (and_6_out, d_ff_4_q[0], min);
  xor xor_4 (xor_4_out, d_ff_4_q[0], min);
  and and_7 (and_7_out, ram_1_dout[3], MINUS);
  xor xor_5 (xor_5_out, ram_1_dout[3], MINUS);
  and and_8 (and_8_out, ram_1_dout[2], MINUS);
  xor xor_6 (xor_6_out, ram_1_dout[2], MINUS);
  and and_9 (and_9_out, ram_1_dout[1], MINUS);
  xor xor_7 (xor_7_out, ram_1_dout[1], MINUS);
  and and_10 (and_10_out, ram_1_dout[0], MINUS);
  xor xor_8 (xor_8_out, ram_1_dout[0], MINUS);
  xor xor_9 (xor_9_out, xor_1_out, or_3_out);
  and and_11 (and_11_out, xor_1_out, or_3_out);
  xor xor_10 (xor_10_out, xor_2_out, or_4_out);
  and and_12 (and_12_out, xor_2_out, or_4_out);
  xor xor_11 (xor_11_out, xor_3_out, or_5_out);
  and and_13 (and_13_out, xor_3_out, or_5_out);
  xor xor_12 (xor_12_out, xor_4_out, pls);
  and and_14 (and_14_out, xor_4_out, pls);
  xor xor_13 (xor_13_out, xor_5_out, or_7_out);
  and and_15 (and_15_out, xor_5_out, or_7_out);
  xor xor_14 (xor_14_out, xor_6_out, or_8_out);
  and and_16 (and_16_out, xor_6_out, or_8_out);
  xor xor_15 (xor_15_out, xor_7_out, or_9_out);
  and and_17 (and_17_out, xor_7_out, or_9_out);
  xor xor_16 (xor_16_out, xor_8_out, PLUS);
  and and_18 (and_18_out, xor_8_out, PLUS);
  or or_2 (or_2_out, and_3_out, and_11_out);
  or or_3 (or_3_out, and_4_out, and_12_out);
  or or_4 (or_4_out, and_5_out, and_13_out);
  or or_5 (or_5_out, and_6_out, and_14_out);
  or or_6 (or_6_out, and_7_out, and_15_out);
  or or_7 (or_7_out, and_8_out, and_16_out);
  or or_8 (or_8_out, and_9_out, and_17_out);
  or or_9 (or_9_out, and_10_out, and_18_out);
  and and_19 (and_19_out, d_ff_4_q[7], min);
  xor xor_17 (xor_17_out, d_ff_4_q[7], min);
  and and_20 (and_20_out, d_ff_4_q[6], min);
  xor xor_18 (xor_18_out, d_ff_4_q[6], min);
  and and_21 (and_21_out, d_ff_4_q[5], min);
  xor xor_19 (xor_19_out, d_ff_4_q[5], min);
  and and_22 (and_22_out, d_ff_4_q[4], min);
  xor xor_20 (xor_20_out, d_ff_4_q[4], min);
  and and_23 (and_23_out, ram_1_dout[7], MINUS);
  xor xor_21 (xor_21_out, ram_1_dout[7], MINUS);
  and and_24 (and_24_out, ram_1_dout[6], MINUS);
  xor xor_22 (xor_22_out, ram_1_dout[6], MINUS);
  and and_25 (and_25_out, ram_1_dout[5], MINUS);
  xor xor_23 (xor_23_out, ram_1_dout[5], MINUS);
  and and_26 (and_26_out, ram_1_dout[4], MINUS);
  xor xor_24 (xor_24_out, ram_1_dout[4], MINUS);
  xor xor_25 (xor_25_out, xor_17_out, or_11_out);
  and and_27 (and_27_out, xor_17_out, or_11_out);
  xor xor_26 (xor_26_out, xor_18_out, or_12_out);
  and and_28 (and_28_out, xor_18_out, or_12_out);
  xor xor_27 (xor_27_out, xor_19_out, or_13_out);
  and and_29 (and_29_out, xor_19_out, or_13_out);
  xor xor_28 (xor_28_out, xor_20_out, or_2_out);
  and and_30 (and_30_out, xor_20_out, or_2_out);
  xor xor_29 (xor_29_out, xor_21_out, or_15_out);
  and and_31 (and_31_out, xor_21_out, or_15_out);
  xor xor_30 (xor_30_out, xor_22_out, or_16_out);
  and and_32 (and_32_out, xor_22_out, or_16_out);
  xor xor_31 (xor_31_out, xor_23_out, or_17_out);
  and and_33 (and_33_out, xor_23_out, or_17_out);
  xor xor_32 (xor_32_out, xor_24_out, or_6_out);
  and and_34 (and_34_out, xor_24_out, or_6_out);
  or or_10 (or_10_out, and_19_out, and_27_out);
  or or_11 (or_11_out, and_20_out, and_28_out);
  or or_12 (or_12_out, and_21_out, and_29_out);
  or or_13 (or_13_out, and_22_out, and_30_out);
  or or_14 (or_14_out, and_23_out, and_31_out);
  or or_15 (or_15_out, and_24_out, and_32_out);
  or or_16 (or_16_out, and_25_out, and_33_out);
  or or_17 (or_17_out, and_26_out, and_34_out);
  RAM #(.addrWidth(16), .trigger("high")) ram_1 (
    .addr(d_ff_4_q), .we(UPDATERAM), .din(or_1_out), .dout(ram_1_dout));  // open: oe
  and and_35 (and_35_out, d_ff_4_q[11], min);
  xor xor_33 (xor_33_out, d_ff_4_q[11], min);
  and and_36 (and_36_out, d_ff_4_q[10], min);
  xor xor_34 (xor_34_out, d_ff_4_q[10], min);
  and and_37 (and_37_out, d_ff_4_q[9], min);
  xor xor_35 (xor_35_out, d_ff_4_q[9], min);
  and and_38 (and_38_out, d_ff_4_q[8], min);
  xor xor_36 (xor_36_out, d_ff_4_q[8], min);
  xor xor_37 (xor_37_out, xor_33_out, or_19_out);
  xor xor_38 (xor_38_out, xor_34_out, or_20_out);
  xor xor_39 (xor_39_out, xor_35_out, or_21_out);
  xor xor_40 (xor_40_out, xor_36_out, or_10_out);
  or or_18 (or_18_out, and_35_out, and_39_out);
  and and_39 (and_39_out, xor_33_out, or_19_out);
  or or_19 (or_19_out, and_36_out, and_40_out);
  and and_40 (and_40_out, xor_34_out, or_20_out);
  or or_20 (or_20_out, and_37_out, and_41_out);
  and and_41 (and_41_out, xor_35_out, or_21_out);
  or or_21 (or_21_out, and_38_out, and_42_out);
  and and_42 (and_42_out, xor_36_out, or_10_out);
  assign bit_extender_2_out = {{7{READ}}, READ};  // Bit_Extender bit_extender_2
  and and_43 (and_43_out, d_ff_4_q[15], min);
  xor xor_41 (xor_41_out, d_ff_4_q[15], min);
  and and_44 (and_44_out, d_ff_4_q[14], min);
  xor xor_42 (xor_42_out, d_ff_4_q[14], min);
  and and_45 (and_45_out, d_ff_4_q[13], min);
  xor xor_43 (xor_43_out, d_ff_4_q[13], min);
  and and_46 (and_46_out, d_ff_4_q[12], min);
  xor xor_44 (xor_44_out, d_ff_4_q[12], min);
  assign and_47_out = bit_extender_2_out & ram_1_dout;  // AND_Gate and_47, 8 bits wide
  TTY #(.trigger("falling")) tty_1 (.data(and_47_out[6:0]), .clk(screen), .we(1'b1));  // open: clr
  or or_22 (or_22_out, and_47_out[2], and_47_out[3]);
  or or_23 (or_23_out, and_47_out[4], and_47_out[5]);
  or or_24 (or_24_out, and_47_out[6], and_47_out[7]);
  not not_3 (not_3_out, FORWARD_if1);
  xor xor_45 (xor_45_out, xor_41_out, or_26_out);
  or or_25 (or_25_out, and_43_out, and_48_out);
  and and_48 (and_48_out, xor_41_out, or_26_out);
  xor xor_46 (xor_46_out, xor_42_out, or_27_out);
  or or_26 (or_26_out, and_44_out, and_49_out);
  and and_49 (and_49_out, xor_42_out, or_27_out);
  xor xor_47 (xor_47_out, xor_43_out, or_28_out);
  or or_27 (or_27_out, and_45_out, and_50_out);
  and and_50 (and_50_out, xor_43_out, or_28_out);
  xor xor_48 (xor_48_out, xor_44_out, or_18_out);
  or or_28 (or_28_out, and_46_out, and_51_out);
  and and_51 (and_51_out, xor_44_out, or_18_out);
  or or_29 (or_29_out, and_47_out[0], and_47_out[1]);
  or or_30 (or_30_out, or_29_out, or_22_out);
  or or_31 (or_31_out, or_23_out, or_24_out);
  or or_32 (or_32_out, or_30_out, or_31_out);
  xnor xnor_1 (YES, or_32_out, not_3_out);
endmodule

module b4adder2 (
  input  plus,
  input  minus
);

  wire and_1_out, and_2_out, and_3_out, and_4_out, and_5_out, and_6_out, and_7_out, and_8_out, and_9_out,
       and_10_out, and_11_out, and_12_out, and_13_out, and_14_out, and_15_out, and_16_out, and_17_out,
       and_18_out, and_19_out, and_20_out, and_21_out, and_22_out, and_23_out, and_24_out, and_25_out,
       and_26_out, and_27_out, and_28_out, and_29_out, and_30_out, and_31_out, and_32_out, or_1_out,
       or_2_out, or_3_out, or_4_out, or_5_out, or_6_out, or_7_out, or_8_out, or_9_out, or_10_out, or_11_out,
       or_12_out, or_13_out, or_14_out, or_15_out, or_16_out, undriven, undriven_2, undriven_3, undriven_4,
       undriven_5, undriven_6, undriven_7, undriven_8, undriven_9, undriven_10, undriven_11, undriven_12,
       undriven_13, undriven_14, undriven_15, undriven_16, undriven_17, xor_1_out, xor_2_out, xor_3_out,
       xor_4_out, xor_5_out, xor_6_out, xor_7_out, xor_8_out, xor_9_out, xor_10_out, xor_11_out, xor_12_out,
       xor_13_out, xor_14_out, xor_15_out, xor_16_out, xor_17_out, xor_18_out, xor_19_out, xor_20_out,
       xor_21_out, xor_22_out, xor_23_out, xor_24_out, xor_25_out, xor_26_out, xor_27_out, xor_28_out,
       xor_29_out, xor_30_out, xor_31_out, xor_32_out;

  and and_1 (and_1_out, undriven_8, minus);
  xor xor_1 (xor_1_out, undriven_8, minus);
  and and_2 (and_2_out, undriven_7, minus);
  xor xor_2 (xor_2_out, undriven_7, minus);
  and and_3 (and_3_out, undriven_6, minus);
  xor xor_3 (xor_3_out, undriven_6, minus);
  and and_4 (and_4_out, undriven_5, minus);
  xor xor_4 (xor_4_out, undriven_5, minus);
  xor xor_5 (xor_5_out, xor_1_out, or_2_out);
  and and_5 (and_5_out, xor_1_out, or_2_out);
  xor xor_6 (xor_6_out, xor_2_out, or_3_out);
  and and_6 (and_6_out, xor_2_out, or_3_out);
  xor xor_7 (xor_7_out, xor_3_out, or_4_out);
  and and_7 (and_7_out, xor_3_out, or_4_out);
  xor xor_8 (xor_8_out, xor_4_out, plus);
  and and_8 (and_8_out, xor_4_out, plus);
  or or_1 (or_1_out, and_1_out, and_5_out);
  or or_2 (or_2_out, and_2_out, and_6_out);
  or or_3 (or_3_out, and_3_out, and_7_out);
  or or_4 (or_4_out, and_4_out, and_8_out);
  and and_9 (and_9_out, undriven_12, minus);
  xor xor_9 (xor_9_out, undriven_12, minus);
  and and_10 (and_10_out, undriven_11, minus);
  xor xor_10 (xor_10_out, undriven_11, minus);
  and and_11 (and_11_out, undriven_10, minus);
  xor xor_11 (xor_11_out, undriven_10, minus);
  and and_12 (and_12_out, undriven_9, minus);
  xor xor_12 (xor_12_out, undriven_9, minus);
  xor xor_13 (xor_13_out, xor_9_out, or_6_out);
  and and_13 (and_13_out, xor_9_out, or_6_out);
  xor xor_14 (xor_14_out, xor_10_out, or_7_out);
  and and_14 (and_14_out, xor_10_out, or_7_out);
  xor xor_15 (xor_15_out, xor_11_out, or_8_out);
  and and_15 (and_15_out, xor_11_out, or_8_out);
  xor xor_16 (xor_16_out, xor_12_out, or_1_out);
  and and_16 (and_16_out, xor_12_out, or_1_out);
  or or_5 (or_5_out, and_9_out, and_13_out);
  or or_6 (or_6_out, and_10_out, and_14_out);
  or or_7 (or_7_out, and_11_out, and_15_out);
  or or_8 (or_8_out, and_12_out, and_16_out);
  and and_17 (and_17_out, undriven_16, or_5_out);
  xor xor_17 (xor_17_out, undriven_16, or_5_out);
  and and_18 (and_18_out, undriven_15, or_5_out);
  xor xor_18 (xor_18_out, undriven_15, or_5_out);
  and and_19 (and_19_out, undriven_14, or_5_out);
  xor xor_19 (xor_19_out, undriven_14, or_5_out);
  and and_20 (and_20_out, undriven_13, or_5_out);
  xor xor_20 (xor_20_out, undriven_13, or_5_out);
  xor xor_21 (xor_21_out, xor_17_out, or_10_out);
  and and_21 (and_21_out, xor_17_out, or_10_out);
  xor xor_22 (xor_22_out, xor_18_out, or_11_out);
  and and_22 (and_22_out, xor_18_out, or_11_out);
  xor xor_23 (xor_23_out, xor_19_out, or_12_out);
  and and_23 (and_23_out, xor_19_out, or_12_out);
  xor xor_24 (xor_24_out, xor_20_out, undriven_17);
  and and_24 (and_24_out, xor_20_out, undriven_17);
  or or_9 (or_9_out, and_17_out, and_21_out);
  or or_10 (or_10_out, and_18_out, and_22_out);
  or or_11 (or_11_out, and_19_out, and_23_out);
  or or_12 (or_12_out, and_20_out, and_24_out);
  and and_25 (and_25_out, undriven, or_5_out);
  xor xor_25 (xor_25_out, undriven, or_5_out);
  and and_26 (and_26_out, undriven_2, or_5_out);
  xor xor_26 (xor_26_out, undriven_2, or_5_out);
  and and_27 (and_27_out, undriven_3, or_5_out);
  xor xor_27 (xor_27_out, undriven_3, or_5_out);
  and and_28 (and_28_out, undriven_4, or_5_out);
  xor xor_28 (xor_28_out, undriven_4, or_5_out);
  xor xor_29 (xor_29_out, xor_25_out, or_14_out);
  xor xor_30 (xor_30_out, xor_26_out, or_15_out);
  xor xor_31 (xor_31_out, xor_27_out, or_16_out);
  xor xor_32 (xor_32_out, xor_28_out, or_9_out);
  or or_13 (or_13_out, and_25_out, and_29_out);
  and and_29 (and_29_out, xor_25_out, or_14_out);
  or or_14 (or_14_out, and_26_out, and_30_out);
  and and_30 (and_30_out, xor_26_out, or_15_out);
  or or_15 (or_15_out, and_27_out, and_31_out);
  and and_31 (and_31_out, xor_27_out, or_16_out);
  or or_16 (or_16_out, and_28_out, and_32_out);
  and and_32 (and_32_out, xor_28_out, or_9_out);
endmodule

module b2adder3 (
  input  RESET,
  input  PLUS,
  input  minus
);

  wire and_1_out, and_2_out, and_3_out, and_4_out, and_5_out, and_6_out, and_7_out, and_8_out, and_9_out,
       and_10_out, and_11_out, and_12_out, and_13_out, and_14_out, and_15_out, and_16_out, d_ff_1_q,
       d_ff_2_q, d_ff_3_q, d_ff_4_q, d_ff_5_q, d_ff_6_q, d_ff_7_q, d_ff_8_q, or_1_out, or_2_out, or_3_out,
       or_4_out, or_5_out, or_6_out, or_7_out, or_8_out, xor_1_out, xor_2_out, xor_3_out, xor_4_out,
       xor_5_out, xor_6_out, xor_7_out, xor_8_out, xor_9_out, xor_10_out, xor_11_out, xor_12_out, xor_13_out,
       xor_14_out, xor_15_out, xor_16_out;

  D_Flip_Flop d_ff_1 (.D(xor_6_out), .clk(RESET), .Q(d_ff_1_q));  // open: Qn, preset, reset
  D_Flip_Flop d_ff_2 (.D(xor_7_out), .clk(RESET), .Q(d_ff_2_q));  // open: Qn, preset, reset
  D_Flip_Flop d_ff_3 (.D(xor_8_out), .clk(RESET), .Q(d_ff_3_q));  // open: Qn, preset, reset
  D_Flip_Flop d_ff_4 (.D(xor_5_out), .clk(RESET), .Q(d_ff_4_q));  // open: Qn, preset, reset
  D_Flip_Flop d_ff_5 (.D(xor_13_out), .clk(RESET), .Q(d_ff_5_q));  // open: Qn, preset, reset
  D_Flip_Flop d_ff_6 (.D(xor_14_out), .clk(RESET), .Q(d_ff_6_q));  // open: Qn, preset, reset
  D_Flip_Flop d_ff_7 (.D(xor_15_out), .clk(RESET), .Q(d_ff_7_q));  // open: Qn, preset, reset
  D_Flip_Flop d_ff_8 (.D(xor_16_out), .clk(RESET), .Q(d_ff_8_q));  // open: Qn, preset, reset
  and and_1 (and_1_out, d_ff_4_q, minus);
  and and_2 (and_2_out, d_ff_1_q, minus);
  and and_3 (and_3_out, d_ff_2_q, minus);
  and and_4 (and_4_out, d_ff_3_q, minus);
  xor xor_1 (xor_1_out, d_ff_4_q, minus);
  xor xor_2 (xor_2_out, d_ff_1_q, minus);
  xor xor_3 (xor_3_out, d_ff_2_q, minus);
  xor xor_4 (xor_4_out, d_ff_3_q, minus);
  xor xor_5 (xor_5_out, xor_1_out, or_2_out);
  and and_5 (and_5_out, xor_1_out, or_2_out);
  xor xor_6 (xor_6_out, xor_2_out, or_3_out);
  and and_6 (and_6_out, xor_2_out, or_3_out);
  xor xor_7 (xor_7_out, xor_3_out, or_4_out);
  and and_7 (and_7_out, xor_3_out, or_4_out);
  xor xor_8 (xor_8_out, xor_4_out, PLUS);
  and and_8 (and_8_out, xor_4_out, PLUS);
  or or_1 (or_1_out, and_1_out, and_5_out);
  or or_2 (or_2_out, and_2_out, and_6_out);
  or or_3 (or_3_out, and_3_out, and_7_out);
  or or_4 (or_4_out, and_4_out, and_8_out);
  and and_9 (and_9_out, d_ff_5_q, minus);
  xor xor_9 (xor_9_out, d_ff_5_q, minus);
  and and_10 (and_10_out, d_ff_6_q, minus);
  xor xor_10 (xor_10_out, d_ff_6_q, minus);
  and and_11 (and_11_out, d_ff_7_q, minus);
  xor xor_11 (xor_11_out, d_ff_7_q, minus);
  and and_12 (and_12_out, d_ff_8_q, minus);
  xor xor_12 (xor_12_out, d_ff_8_q, minus);
  xor xor_13 (xor_13_out, xor_9_out, or_6_out);
  and and_13 (and_13_out, xor_9_out, or_6_out);
  xor xor_14 (xor_14_out, xor_10_out, or_7_out);
  and and_14 (and_14_out, xor_10_out, or_7_out);
  xor xor_15 (xor_15_out, xor_11_out, or_8_out);
  and and_15 (and_15_out, xor_11_out, or_8_out);
  xor xor_16 (xor_16_out, xor_12_out, or_1_out);
  and and_16 (and_16_out, xor_12_out, or_1_out);
  or or_5 (or_5_out, and_9_out, and_13_out);
  or or_6 (or_6_out, and_10_out, and_14_out);
  or or_7 (or_7_out, and_11_out, and_15_out);
  or or_8 (or_8_out, and_12_out, and_16_out);
endmodule
module V4 (
  input  BUTTON,
  input  FORWARD_if1,
  output ROMPLUS1
);

  wire and_1_out, and_2_out, and_3_out, and_4_out, and_5_out, and_6_out, and_7_out, and_8_out, and_9_out,
       and_10_out, and_11_out, and_12_out, and_13_out, and_14_out, and_15_out, and_16_out, and_17_out,
       and_18_out, and_19_out, and_20_out, and_21_out, and_22_out, and_23_out, and_24_out, and_25_out,
       and_26_out, and_27_out, and_28_out, and_29_out, and_30_out, and_31_out, and_32_out, and_33_out,
       and_34_out, and_35_out, and_36_out, and_37_out, and_38_out, and_39_out, and_40_out, and_41_out,
       and_42_out, and_43_out, and_44_out, and_45_out, and_46_out, and_47_out, and_48_out, and_49_out,
       and_50_out, and_51_out, and_52_out, and_53_out, and_54_out, and_55_out, and_56_out, and_57_out,
       and_58_out, and_59_out, and_60_out, and_61_out, and_62_out, and_63_out, and_64_out, and_65_out,
       and_66_out, and_67_out, and_68_out, and_69_out, and_70_out, and_71_out, and_72_out, and_73_out,
       and_74_out, and_75_out, and_76_out, and_77_out, and_78_out, and_79_out, and_80_out, and_81_out,
       and_82_out, and_83_out, and_84_out, and_85_out, and_86_out, and_87_out, and_90_out, and_91_out,
       and_92_out, and_93_out, and_94_out, and_95_out, and_96_out, and_97_out, and_98_out, and_99_out,
       and_100_out, and_101_out, and_102_out, and_103_out, and_104_out, and_105_out, and_106_out,
       and_107_out, and_108_out, and_109_out, and_110_out, and_111_out, and_112_out, and_113_out,
       and_114_out, and_115_out, and_116_out, and_117_out, and_118_out, and_119_out, and_120_out,
       and_121_out, and_122_out, and_123_out, and_124_out, and_125_out, and_126_out, and_127_out,
       and_128_out, and_129_out, and_131_out, and_132_out, and_133_out, and_134_out, and_135_out,
       and_136_out, and_137_out, and_138_out, clock_1_out, d_ff_17_q, d_ff_18_q, d_ff_19_q, d_ff_20_q,
       d_ff_21_q, d_ff_22_q, d_ff_23_q, d_ff_24_q, d_ff_25_q, d_ff_26_q, d_ff_27_q, d_ff_27_qn, d_ff_28_q,
       d_ff_29_q, d_ff_30_q, d_ff_31_q, d_ff_32_q, d_ff_33_q, d_ff_34_q, d_ff_35_q, d_ff_36_q, nor_1_out,
       nor_2_out, not_1_out, not_2_out, not_3_out, not_4_out, not_5_out, not_6_out, not_7_out, not_8_out,
       not_9_out, not_10_out, not_11_out, not_12_out, not_13_out, not_14_out, not_15_out, not_16_out,
       not_18_out, or_1_out, or_2_out, or_3_out, or_4_out, or_5_out, or_6_out, or_7_out, or_8_out, or_9_out,
       or_10_out, or_11_out, or_12_out, or_13_out, or_14_out, or_15_out, or_16_out, or_17_out, or_18_out,
       or_19_out, or_20_out, or_21_out, or_22_out, or_23_out, or_24_out, or_26_out, or_27_out, or_28_out,
       or_29_out, or_30_out, or_31_out, or_32_out, or_33_out, or_34_out, or_35_out, or_36_out, or_37_out,
       or_38_out, or_39_out, or_40_out, or_41_out, or_42_out, or_43_out, or_44_out, or_45_out, or_46_out,
       or_47_out, or_49_out, or_50_out, or_51_out, or_52_out, or_53_out, or_54_out, or_55_out, or_56_out,
       or_57_out, or_58_out, or_59_out, or_60_out, or_61_out, or_62_out, or_63_out, or_64_out, or_65_out,
       or_66_out, or_67_out, or_68_out, or_69_out, or_70_out, or_71_out, or_72_out, or_73_out, or_74_out,
       or_75_out, or_76_out, or_77_out, or_78_out, or_79_out, undriven, xor_1_out, xor_2_out, xor_3_out,
       xor_4_out, xor_5_out, xor_6_out, xor_7_out, xor_8_out, xor_9_out, xor_10_out, xor_11_out, xor_12_out,
       xor_13_out, xor_14_out, xor_15_out, xor_16_out, xor_17_out, xor_18_out, xor_19_out, xor_20_out,
       xor_21_out, xor_22_out, xor_23_out, xor_24_out, xor_25_out, xor_26_out, xor_27_out, xor_28_out,
       xor_29_out, xor_30_out, xor_31_out, xor_32_out, xor_33_out, xor_34_out, xor_35_out, xor_36_out,
       xor_37_out, xor_38_out, xor_39_out, xor_40_out, xor_41_out, xor_42_out, xor_43_out, xor_44_out,
       xor_45_out, xor_46_out, xor_47_out, xor_48_out, xor_49_out, xor_50_out, xor_51_out, xor_52_out,
       xor_53_out, xor_54_out, xor_55_out, xor_56_out, xor_57_out, xor_58_out, xor_59_out, xor_60_out,
       xor_61_out, xor_62_out, xor_63_out, xor_64_out, xor_65_out, xor_66_out, xor_67_out, xor_68_out,
       xor_69_out, xor_70_out, xor_71_out, xor_72_out, xor_73_out, xor_74_out, xor_75_out, xor_76_out,
       xor_77_out, xor_78_out, xor_79_out, xor_80_out, xor_81_out, xor_82_out, xor_83_out, xor_84_out,
       xor_85_out, xor_86_out, xor_87_out, xor_88_out, xor_89_out, xor_90_out, xor_91_out, xor_92_out,
       xor_93_out, xor_94_out, xor_95_out, xor_96_out, xor_97_out;
  wire [2:0] rom_1_data;
  wire [7:0] and_88_out, and_89_out, and_130_out, bit_extender_1_out, bit_extender_2_out, d_ff_52_q,
       not_17_out, or_48_out, ram_1_dout, undriven_2;
  wire [15:0] d_ff_4_q, d_ff_40_q;

  D_Flip_Flop d_ff_1 (.D(xor_5_out), .clk(undriven), .Q(d_ff_4_q[3]));  // open: Qn, preset, reset
  D_Flip_Flop d_ff_2 (.D(xor_6_out), .clk(undriven), .Q(d_ff_4_q[2]));  // open: Qn, preset, reset
  D_Flip_Flop d_ff_3 (.D(xor_7_out), .clk(undriven), .Q(d_ff_4_q[1]));  // open: Qn, preset, reset
  D_Flip_Flop d_ff_4 (.D(xor_8_out), .clk(undriven), .Q(d_ff_4_q[0]));  // open: Qn, preset, reset
  D_Flip_Flop d_ff_5 (.D(xor_16_out), .clk(undriven), .Q(d_ff_4_q[4]));  // open: Qn, preset, reset
  ROM #(.addrWidth(16), .dataWidth(3)) rom_1 (.addr(d_ff_4_q), .data(rom_1_data));
  D_Flip_Flop d_ff_6 (.D(xor_13_out), .clk(undriven), .Q(d_ff_4_q[7]));  // open: Qn, preset, reset
  D_Flip_Flop d_ff_7 (.D(xor_14_out), .clk(undriven), .Q(d_ff_4_q[6]));  // open: Qn, preset, reset
  D_Flip_Flop d_ff_8 (.D(xor_15_out), .clk(undriven), .Q(d_ff_4_q[5]));  // open: Qn, preset, reset
  Clock clock_1 (.out(clock_1_out));
  D_Flip_Flop d_ff_9 (.D(xor_25_out), .clk(undriven), .Q(d_ff_4_q[11]));  // open: Qn, preset, reset
  D_Flip_Flop d_ff_10 (.D(xor_26_out), .clk(undriven), .Q(d_ff_4_q[10]));  // open: Qn, preset, reset
  D_Flip_Flop d_ff_11 (.D(xor_27_out), .clk(undriven), .Q(d_ff_4_q[9]));  // open: Qn, preset, reset
  D_Flip_Flop d_ff_12 (.D(xor_28_out), .clk(undriven), .Q(d_ff_4_q[8]));  // open: Qn, preset, reset
  D_Flip_Flop d_ff_13 (.D(xor_44_out), .clk(undriven), .Q(d_ff_4_q[12]));  // open: Qn, preset, reset
  or or_1 (or_1_out, or_2_out, d_ff_17_q);
  not not_1 (not_1_out, or_1_out);
  and and_1 (and_1_out, not_15_out, clock_1_out);
  D_Flip_Flop d_ff_14 (.D(xor_41_out), .clk(undriven), .Q(d_ff_4_q[15]));  // open: Qn, preset, reset
  D_Flip_Flop d_ff_15 (.D(xor_42_out), .clk(undriven), .Q(d_ff_4_q[14]));  // open: Qn, preset, reset
  D_Flip_Flop d_ff_16 (.D(xor_43_out), .clk(undriven), .Q(d_ff_4_q[13]));  // open: Qn, preset, reset
  D_Flip_Flop d_ff_17 (.D(not_1_out), .clk(and_2_out), .Q(d_ff_17_q));  // open: Qn, preset, reset
  and and_2 (and_2_out, not_2_out, and_1_out);
  not not_2 (not_2_out, and_78_out);
  and and_3 (and_3_out, and_1_out, and_78_out);
  or or_2 (or_2_out, d_ff_19_q, d_ff_18_q);
  D_Flip_Flop d_ff_18 (.D(d_ff_17_q), .clk(and_2_out), .Q(d_ff_18_q));  // open: Qn, preset, reset
  D_Flip_Flop d_ff_19 (.D(d_ff_18_q), .clk(and_2_out), .Q(d_ff_19_q));  // open: Qn, preset, reset
  and and_4 (and_4_out, and_3_out, and_28_out);
  or or_3 (or_3_out, d_ff_17_q, d_ff_20_q);
  or or_4 (or_4_out, d_ff_18_q, d_ff_19_q);
  or or_5 (or_5_out, d_ff_19_q, d_ff_20_q);
  and and_5 (and_5_out, rom_1_data[1], rom_1_data[2]);
  and and_6 (and_6_out, d_ff_4_q[3], and_79_out);
  xor xor_1 (xor_1_out, d_ff_4_q[3], and_79_out);
  and and_7 (and_7_out, d_ff_4_q[2], and_79_out);
  xor xor_2 (xor_2_out, d_ff_4_q[2], and_79_out);
  and and_8 (and_8_out, d_ff_4_q[1], and_79_out);
  xor xor_3 (xor_3_out, d_ff_4_q[1], and_79_out);
  and and_9 (and_9_out, d_ff_4_q[0], and_79_out);
  xor xor_4 (xor_4_out, d_ff_4_q[0], and_79_out);
  D_Flip_Flop d_ff_20 (.D(d_ff_19_q), .clk(and_2_out), .Q(d_ff_20_q));  // open: Qn, preset, reset
  or or_6 (or_6_out, or_9_out, d_ff_21_q);
  not not_3 (not_3_out, or_6_out);
  D_Flip_Flop d_ff_21 (.D(not_3_out), .clk(or_7_out), .Q(d_ff_21_q));  // open: Qn, preset, reset
  or or_7 (or_7_out, d_ff_17_q, and_4_out);
  D_Flip_Flop d_ff_22 (.D(xor_81_out), .clk(or_8_out), .Q(d_ff_22_q));  // open: Qn, preset, reset
  or or_8 (or_8_out, d_ff_18_q, and_67_out);
  or or_9 (or_9_out, d_ff_27_q, d_ff_23_q);
  LED led_1 (.in(d_ff_21_q));
  not not_4 (not_4_out, or_3_out);
  not not_5 (not_5_out, rom_1_data[0]);
  xor xor_5 (xor_5_out, xor_1_out, or_11_out);
  or or_10 (or_10_out, and_6_out, and_10_out);
  and and_10 (and_10_out, xor_1_out, or_11_out);
  xor xor_6 (xor_6_out, xor_2_out, or_12_out);
  or or_11 (or_11_out, and_7_out, and_11_out);
  and and_11 (and_11_out, xor_2_out, or_12_out);
  xor xor_7 (xor_7_out, xor_3_out, or_13_out);
  or or_12 (or_12_out, and_8_out, and_12_out);
  and and_12 (and_12_out, xor_3_out, or_13_out);
  xor xor_8 (xor_8_out, xor_4_out, or_35_out);
  or or_13 (or_13_out, and_9_out, and_13_out);
  and and_13 (and_13_out, xor_4_out, or_35_out);
  D_Flip_Flop d_ff_23 (.D(and_14_out), .clk(or_7_out), .Q(d_ff_23_q));  // open: Qn, preset, reset
  and and_14 (and_14_out, d_ff_21_q, not_4_out);
  and and_15 (and_15_out, not_5_out, and_5_out);
  and and_16 (and_16_out, rom_1_data[0], and_5_out);
  D_Flip_Flop d_ff_24 (.D(rom_1_data[0]), .clk(d_ff_17_q), .Q(d_ff_24_q));  // open: Qn, preset, reset
  D_Flip_Flop d_ff_25 (.D(rom_1_data[1]), .clk(d_ff_17_q), .Q(d_ff_25_q));  // open: Qn, preset, reset
  D_Flip_Flop d_ff_26 (.D(rom_1_data[2]), .clk(d_ff_17_q), .Q(d_ff_26_q));  // open: Qn, preset, reset
  and and_17 (and_17_out, d_ff_4_q[7], and_79_out);
  and and_18 (and_18_out, d_ff_4_q[6], and_79_out);
  and and_19 (and_19_out, d_ff_4_q[5], and_79_out);
  and and_20 (and_20_out, d_ff_4_q[4], and_79_out);
  D_Flip_Flop d_ff_27 (.D(and_21_out), .clk(or_7_out), .Q(d_ff_27_q), .Qn(d_ff_27_qn));  // open: preset, reset
  and and_21 (and_21_out, d_ff_23_q, not_4_out);
  not not_6 (not_6_out, d_ff_26_q);
  nor nor_1 (nor_1_out, d_ff_24_q, d_ff_25_q);
  not not_7 (not_7_out, BUTTON);
  not not_8 (not_8_out, d_ff_25_q);
  and and_22 (and_22_out, d_ff_25_q, d_ff_26_q);
  and and_23 (and_23_out, d_ff_22_q, d_ff_18_q);
  xor xor_9 (xor_9_out, d_ff_4_q[7], and_79_out);
  xor xor_10 (xor_10_out, d_ff_4_q[6], and_79_out);
  xor xor_11 (xor_11_out, d_ff_4_q[5], and_79_out);
  xor xor_12 (xor_12_out, d_ff_4_q[4], and_79_out);
  D_Flip_Flop d_ff_28 (.D(xor_29_out), .clk(d_ff_23_q), .Q(d_ff_28_q));  // open: Qn, preset, reset
  D_Flip_Flop d_ff_29 (.D(xor_30_out), .clk(d_ff_23_q), .Q(d_ff_29_q));  // open: Qn, preset, reset
  D_Flip_Flop d_ff_30 (.D(xor_31_out), .clk(d_ff_23_q), .Q(d_ff_30_q));  // open: Qn, preset, reset
  D_Flip_Flop d_ff_31 (.D(xor_32_out), .clk(d_ff_23_q), .Q(d_ff_31_q));  // open: Qn, preset, reset
  nor nor_2 (nor_2_out, d_ff_25_q, d_ff_26_q);
  and and_24 (and_24_out, d_ff_25_q, not_6_out);
  and and_25 (and_25_out, nor_1_out, d_ff_26_q);
  and and_26 (and_26_out, d_ff_24_q, not_8_out);
  and and_27 (and_27_out, and_26_out, d_ff_26_q);
  and and_28 (and_28_out, and_22_out, d_ff_22_q);
  xor xor_13 (xor_13_out, xor_9_out, or_15_out);
  and and_29 (and_29_out, xor_9_out, or_15_out);
  xor xor_14 (xor_14_out, xor_10_out, or_16_out);
  and and_30 (and_30_out, xor_10_out, or_16_out);
  xor xor_15 (xor_15_out, xor_11_out, or_17_out);
  and and_31 (and_31_out, xor_11_out, or_17_out);
  xor xor_16 (xor_16_out, xor_12_out, or_10_out);
  and and_32 (and_32_out, xor_12_out, or_10_out);
  D_Flip_Flop d_ff_32 (.D(xor_47_out), .clk(d_ff_23_q), .Q(d_ff_32_q));  // open: Qn, preset, reset
  D_Flip_Flop d_ff_33 (.D(xor_48_out), .clk(d_ff_23_q), .Q(d_ff_33_q));  // open: Qn, preset, reset
  D_Flip_Flop d_ff_34 (.D(and_33_out), .clk(or_7_out), .Q(d_ff_34_q));  // open: Qn, preset, reset
  and and_33 (and_33_out, d_ff_27_q, not_4_out);
  or or_14 (or_14_out, and_17_out, and_29_out);
  or or_15 (or_15_out, and_18_out, and_30_out);
  or or_16 (or_16_out, and_19_out, and_31_out);
  or or_17 (or_17_out, and_20_out, and_32_out);
  D_Flip_Flop d_ff_35 (.D(xor_45_out), .clk(d_ff_23_q), .Q(d_ff_35_q));  // open: Qn, preset, reset
  D_Flip_Flop d_ff_36 (.D(xor_46_out), .clk(d_ff_23_q), .Q(d_ff_36_q));  // open: Qn, preset, reset
  LED led_2 (.in(d_ff_27_q));
  LED led_3 (.in(d_ff_34_q));
  and and_34 (and_34_out, not_7_out, and_27_out);
  not not_9 (not_9_out, d_ff_24_q);
  not not_10 (not_10_out, d_ff_24_q);
  and and_35 (and_35_out, or_4_out, nor_2_out);
  not not_11 (not_11_out, d_ff_24_q);
  and and_36 (and_36_out, or_4_out, and_24_out);
  or or_18 (or_18_out, and_24_out, nor_2_out);
  or or_19 (or_19_out, nor_2_out, and_27_out);
  or or_20 (or_20_out, or_4_out, d_ff_17_q);
  and and_37 (and_37_out, d_ff_18_q, and_34_out);
  and and_38 (and_38_out, and_28_out, not_9_out);
  not not_12 (not_12_out, and_28_out);
  and and_39 (and_39_out, not_10_out, and_35_out);
  and and_40 (and_40_out, and_35_out, d_ff_24_q);
  and and_41 (and_41_out, not_11_out, and_36_out);
  and and_42 (and_42_out, and_36_out, d_ff_24_q);
  and and_43 (and_43_out, or_18_out, d_ff_19_q);
  and and_44 (and_44_out, or_19_out, d_ff_20_q);
  and and_45 (and_45_out, or_4_out, and_25_out);
  and and_46 (and_46_out, d_ff_19_q, and_25_out);
  and and_47 (and_47_out, or_5_out, and_27_out);
  and and_48 (and_48_out, or_20_out, and_22_out);
  and and_49 (and_49_out, and_22_out, and_23_out);
  and and_50 (and_50_out, d_ff_4_q[11], and_79_out);
  xor xor_17 (xor_17_out, d_ff_4_q[11], and_79_out);
  and and_51 (and_51_out, d_ff_4_q[10], and_79_out);
  xor xor_18 (xor_18_out, d_ff_4_q[10], and_79_out);
  and and_52 (and_52_out, d_ff_4_q[9], and_79_out);
  xor xor_19 (xor_19_out, d_ff_4_q[9], and_79_out);
  and and_53 (and_53_out, d_ff_4_q[8], and_79_out);
  xor xor_20 (xor_20_out, d_ff_4_q[8], and_79_out);
  and and_54 (and_54_out, d_ff_28_q, and_16_out);
  xor xor_21 (xor_21_out, d_ff_28_q, and_16_out);
  and and_55 (and_55_out, d_ff_29_q, and_16_out);
  xor xor_22 (xor_22_out, d_ff_29_q, and_16_out);
  and and_56 (and_56_out, d_ff_30_q, and_16_out);
  xor xor_23 (xor_23_out, d_ff_30_q, and_16_out);
  and and_57 (and_57_out, d_ff_31_q, and_16_out);
  xor xor_24 (xor_24_out, d_ff_31_q, and_16_out);
  or or_21 (or_21_out, d_ff_19_q, d_ff_20_q);
  and and_58 (and_58_out, or_21_out, not_12_out);
  or or_22 (or_22_out, and_45_out, and_48_out);
  xor xor_25 (xor_25_out, xor_17_out, or_27_out);
  and and_59 (and_59_out, xor_17_out, or_27_out);
  xor xor_26 (xor_26_out, xor_18_out, or_28_out);
  and and_60 (and_60_out, xor_18_out, or_28_out);
  xor xor_27 (xor_27_out, xor_19_out, or_29_out);
  and and_61 (and_61_out, xor_19_out, or_29_out);
  xor xor_28 (xor_28_out, xor_20_out, or_14_out);
  and and_62 (and_62_out, xor_20_out, or_14_out);
  xor xor_29 (xor_29_out, xor_21_out, or_31_out);
  and and_63 (and_63_out, xor_21_out, or_31_out);
  xor xor_30 (xor_30_out, xor_22_out, or_32_out);
  and and_64 (and_64_out, xor_22_out, or_32_out);
  xor xor_31 (xor_31_out, xor_23_out, or_33_out);
  and and_65 (and_65_out, xor_23_out, or_33_out);
  xor xor_32 (xor_32_out, xor_24_out, and_15_out);
  and and_66 (and_66_out, xor_24_out, and_15_out);
  or or_23 (or_23_out, d_ff_28_q, d_ff_29_q);
  or or_24 (or_24_out, d_ff_30_q, d_ff_31_q);
  or or_25 (ROMPLUS1, and_38_out, and_58_out);
  or or_26 (or_26_out, and_50_out, and_59_out);
  or or_27 (or_27_out, and_51_out, and_60_out);
  or or_28 (or_28_out, and_52_out, and_61_out);
  or or_29 (or_29_out, and_53_out, and_62_out);
  or or_30 (or_30_out, and_54_out, and_63_out);
  or or_31 (or_31_out, and_55_out, and_64_out);
  or or_32 (or_32_out, and_56_out, and_65_out);
  or or_33 (or_33_out, and_57_out, and_66_out);
  or or_34 (or_34_out, or_23_out, or_24_out);
  not not_13 (not_13_out, or_39_out);
  and and_67 (and_67_out, d_ff_27_q, not_13_out);
  and and_68 (and_68_out, d_ff_34_q, and_28_out);
  and and_69 (and_69_out, and_28_out, d_ff_24_q);
  not not_14 (not_14_out, and_67_out);
  or or_35 (or_35_out, and_68_out, d_ff_20_q);
  and and_70 (and_70_out, d_ff_4_q[15], and_79_out);
  xor xor_33 (xor_33_out, d_ff_4_q[15], and_79_out);
  and and_71 (and_71_out, d_ff_4_q[14], and_79_out);
  xor xor_34 (xor_34_out, d_ff_4_q[14], and_79_out);
  and and_72 (and_72_out, d_ff_4_q[13], and_79_out);
  xor xor_35 (xor_35_out, d_ff_4_q[13], and_79_out);
  and and_73 (and_73_out, d_ff_4_q[12], and_79_out);
  xor xor_36 (xor_36_out, d_ff_4_q[12], and_79_out);
  and and_74 (and_74_out, d_ff_35_q, and_16_out);
  xor xor_37 (xor_37_out, d_ff_35_q, and_16_out);
  and and_75 (and_75_out, d_ff_36_q, and_16_out);
  xor xor_38 (xor_38_out, d_ff_36_q, and_16_out);
  and and_76 (and_76_out, d_ff_32_q, and_16_out);
  xor xor_39 (xor_39_out, d_ff_32_q, and_16_out);
  and and_77 (and_77_out, d_ff_33_q, and_16_out);
  xor xor_40 (xor_40_out, d_ff_33_q, and_16_out);
  or or_36 (or_36_out, d_ff_35_q, d_ff_36_q);
  or or_37 (or_37_out, d_ff_32_q, d_ff_33_q);
  LED led_4 (.in(and_37_out));
  and and_78 (and_78_out, not_14_out, and_49_out);
  LED led_5 (.in(and_78_out));
  LED led_6 (.in(ROMPLUS1));
  and and_79 (and_79_out, not_14_out, and_69_out);
  LED led_7 (.in(and_39_out));
  LED led_8 (.in(and_40_out));
  LED led_9 (.in(and_41_out));
  LED led_10 (.in(and_42_out));
  LED led_11 (.in(and_43_out));
  LED led_12 (.in(and_44_out));
  LED led_13 (.in(or_22_out));
  LED led_14 (.in(and_46_out));
  LED led_15 (.in(and_47_out));
  xor xor_41 (xor_41_out, xor_33_out, or_41_out);
  and and_80 (and_80_out, xor_33_out, or_41_out);
  xor xor_42 (xor_42_out, xor_34_out, or_42_out);
  and and_81 (and_81_out, xor_34_out, or_42_out);
  xor xor_43 (xor_43_out, xor_35_out, or_43_out);
  and and_82 (and_82_out, xor_35_out, or_43_out);
  xor xor_44 (xor_44_out, xor_36_out, or_26_out);
  and and_83 (and_83_out, xor_36_out, or_26_out);
  xor xor_45 (xor_45_out, xor_37_out, or_45_out);
  xor xor_46 (xor_46_out, xor_38_out, or_46_out);
  xor xor_47 (xor_47_out, xor_39_out, or_47_out);
  xor xor_48 (xor_48_out, xor_40_out, or_30_out);
  or or_38 (or_38_out, or_36_out, or_37_out);
  or or_39 (or_39_out, or_38_out, or_34_out);
  not not_15 (not_15_out, and_37_out);
  LED led_16 (.in(or_35_out));
  LED led_17 (.in(and_79_out));
  or or_40 (or_40_out, and_70_out, and_80_out);
  or or_41 (or_41_out, and_71_out, and_81_out);
  or or_42 (or_42_out, and_72_out, and_82_out);
  or or_43 (or_43_out, and_73_out, and_83_out);
  or or_44 (or_44_out, and_74_out, and_84_out);
  and and_84 (and_84_out, xor_37_out, or_45_out);
  or or_45 (or_45_out, and_75_out, and_85_out);
  and and_85 (and_85_out, xor_38_out, or_46_out);
  or or_46 (or_46_out, and_76_out, and_86_out);
  and and_86 (and_86_out, xor_39_out, or_47_out);
  or or_47 (or_47_out, and_77_out, and_87_out);
  and and_87 (and_87_out, xor_40_out, or_30_out);
  D_Flip_Flop d_ff_37 (.D(xor_57_out), .clk(and_43_out), .Q(d_ff_40_q[3]));  // open: Qn, preset, reset
  D_Flip_Flop d_ff_38 (.D(xor_58_out), .clk(and_43_out), .Q(d_ff_40_q[2]));  // open: Qn, preset, reset
  D_Flip_Flop d_ff_39 (.D(xor_59_out), .clk(and_43_out), .Q(d_ff_40_q[1]));  // open: Qn, preset, reset
  D_Flip_Flop d_ff_40 (.D(xor_60_out), .clk(and_43_out), .Q(d_ff_40_q[0]));  // open: Qn, preset, reset
  D_Flip_Flop d_ff_41 (.D(xor_80_out), .clk(and_43_out), .Q(d_ff_40_q[4]));  // open: Qn, preset, reset
  // DipSwitch dipswitch_1: pin names not known; wires that end beside it: and_79_out
  assign and_88_out = undriven_2 & not_17_out;  // AND_Gate and_88, 8 bits wide
  assign bit_extender_1_out = {{7{not_16_out}}, not_16_out};  // Bit_Extender bit_extender_1
  not not_16 (not_16_out, and_47_out);
  D_Flip_Flop d_ff_42 (.D(xor_77_out), .clk(and_43_out), .Q(d_ff_40_q[7]));  // open: Qn, preset, reset
  D_Flip_Flop d_ff_43 (.D(xor_78_out), .clk(and_43_out), .Q(d_ff_40_q[6]));  // open: Qn, preset, reset
  D_Flip_Flop d_ff_44 (.D(xor_79_out), .clk(and_43_out), .Q(d_ff_40_q[5]));  // open: Qn, preset, reset
  assign or_48_out = and_88_out | and_89_out;  // OR_Gate or_48, 8 bits wide
  assign and_89_out = bit_extender_1_out & d_ff_52_q;  // AND_Gate and_89, 8 bits wide
  assign not_17_out = ~bit_extender_1_out;  // NOT_Gate not_17, 8 bits wide
  D_Flip_Flop d_ff_45 (.D(xor_86_out), .clk(and_43_out), .Q(d_ff_40_q[11]));  // open: Qn, preset, reset
  D_Flip_Flop d_ff_46 (.D(xor_87_out), .clk(and_43_out), .Q(d_ff_40_q[10]));  // open: Qn, preset, reset
  D_Flip_Flop d_ff_47 (.D(xor_88_out), .clk(and_43_out), .Q(d_ff_40_q[9]));  // open: Qn, preset, reset
  D_Flip_Flop d_ff_48 (.D(xor_89_out), .clk(and_43_out), .Q(d_ff_40_q[8]));  // open: Qn, preset, reset
  D_Flip_Flop d_ff_49 (.D(xor_61_out), .clk(and_43_out), .Q(d_ff_52_q[3]));  // open: Qn, preset, reset
  D_Flip_Flop d_ff_50 (.D(xor_62_out), .clk(and_43_out), .Q(d_ff_52_q[2]));  // open: Qn, preset, reset
  D_Flip_Flop d_ff_51 (.D(xor_63_out), .clk(and_43_out), .Q(d_ff_52_q[1]));  // open: Qn, preset, reset
  D_Flip_Flop d_ff_52 (.D(xor_64_out), .clk(and_43_out), .Q(d_ff_52_q[0]));  // open: Qn, preset, reset
  D_Flip_Flop d_ff_53 (.D(xor_97_out), .clk(and_43_out), .Q(d_ff_40_q[12]));  // open: Qn, preset, reset
  D_Flip_Flop d_ff_54 (.D(xor_74_out), .clk(and_43_out), .Q(d_ff_52_q[6]));  // open: Qn, preset, reset
  D_Flip_Flop d_ff_55 (.D(xor_75_out), .clk(and_43_out), .Q(d_ff_52_q[5]));  // open: Qn, preset, reset
  D_Flip_Flop d_ff_56 (.D(xor_76_out), .clk(and_43_out), .Q(d_ff_52_q[4]));  // open: Qn, preset, reset
  D_Flip_Flop d_ff_57 (.D(xor_94_out), .clk(and_43_out), .Q(d_ff_40_q[15]));  // open: Qn, preset, reset
  D_Flip_Flop d_ff_58 (.D(xor_95_out), .clk(and_43_out), .Q(d_ff_40_q[14]));  // open: Qn, preset, reset
  D_Flip_Flop d_ff_59 (.D(xor_96_out), .clk(and_43_out), .Q(d_ff_40_q[13]));  // open: Qn, preset, reset
  D_Flip_Flop d_ff_60 (.D(xor_73_out), .clk(and_43_out), .Q(d_ff_52_q[7]));  // open: Qn, preset, reset
  and and_90 (and_90_out, d_ff_40_q[3], and_42_out);
  xor xor_49 (xor_49_out, d_ff_40_q[3], and_42_out);
  and and_91 (and_91_out, d_ff_40_q[2], and_42_out);
  xor xor_50 (xor_50_out, d_ff_40_q[2], and_42_out);
  and and_92 (and_92_out, d_ff_40_q[1], and_42_out);
  xor xor_51 (xor_51_out, d_ff_40_q[1], and_42_out);
  and and_93 (and_93_out, d_ff_40_q[0], and_42_out);
  xor xor_52 (xor_52_out, d_ff_40_q[0], and_42_out);
  and and_94 (and_94_out, ram_1_dout[3], and_40_out);
  xor xor_53 (xor_53_out, ram_1_dout[3], and_40_out);
  and and_95 (and_95_out, ram_1_dout[2], and_40_out);
  xor xor_54 (xor_54_out, ram_1_dout[2], and_40_out);
  and and_96 (and_96_out, ram_1_dout[1], and_40_out);
  xor xor_55 (xor_55_out, ram_1_dout[1], and_40_out);
  and and_97 (and_97_out, ram_1_dout[0], and_40_out);
  xor xor_56 (xor_56_out, ram_1_dout[0], and_40_out);
  xor xor_57 (xor_57_out, xor_49_out, or_50_out);
  xor xor_58 (xor_58_out, xor_50_out, or_51_out);
  xor xor_59 (xor_59_out, xor_51_out, or_52_out);
  xor xor_60 (xor_60_out, xor_52_out, and_41_out);
  xor xor_61 (xor_61_out, xor_53_out, or_54_out);
  and and_98 (and_98_out, xor_53_out, or_54_out);
  xor xor_62 (xor_62_out, xor_54_out, or_55_out);
  and and_99 (and_99_out, xor_54_out, or_55_out);
  xor xor_63 (xor_63_out, xor_55_out, or_56_out);
  and and_100 (and_100_out, xor_55_out, or_56_out);
  xor xor_64 (xor_64_out, xor_56_out, and_39_out);
  and and_101 (and_101_out, xor_56_out, and_39_out);
  or or_49 (or_49_out, and_90_out, and_102_out);
  and and_102 (and_102_out, xor_49_out, or_50_out);
  or or_50 (or_50_out, and_91_out, and_103_out);
  and and_103 (and_103_out, xor_50_out, or_51_out);
  or or_51 (or_51_out, and_92_out, and_104_out);
  and and_104 (and_104_out, xor_51_out, or_52_out);
  or or_52 (or_52_out, and_93_out, and_105_out);
  and and_105 (and_105_out, xor_52_out, and_41_out);
  or or_53 (or_53_out, and_94_out, and_98_out);
  or or_54 (or_54_out, and_95_out, and_99_out);
  or or_55 (or_55_out, and_96_out, and_100_out);
  or or_56 (or_56_out, and_97_out, and_101_out);
  and and_106 (and_106_out, d_ff_40_q[7], and_42_out);
  xor xor_65 (xor_65_out, d_ff_40_q[7], and_42_out);
  and and_107 (and_107_out, d_ff_40_q[6], and_42_out);
  xor xor_66 (xor_66_out, d_ff_40_q[6], and_42_out);
  and and_108 (and_108_out, d_ff_40_q[5], and_42_out);
  xor xor_67 (xor_67_out, d_ff_40_q[5], and_42_out);
  and and_109 (and_109_out, d_ff_40_q[4], and_42_out);
  xor xor_68 (xor_68_out, d_ff_40_q[4], and_42_out);
  and and_110 (and_110_out, ram_1_dout[7], and_40_out);
  xor xor_69 (xor_69_out, ram_1_dout[7], and_40_out);
  and and_111 (and_111_out, ram_1_dout[6], and_40_out);
  xor xor_70 (xor_70_out, ram_1_dout[6], and_40_out);
  and and_112 (and_112_out, ram_1_dout[5], and_40_out);
  xor xor_71 (xor_71_out, ram_1_dout[5], and_40_out);
  and and_113 (and_113_out, ram_1_dout[4], and_40_out);
  xor xor_72 (xor_72_out, ram_1_dout[4], and_40_out);
  xor xor_73 (xor_73_out, xor_69_out, or_62_out);
  and and_114 (and_114_out, xor_69_out, or_62_out);
  xor xor_74 (xor_74_out, xor_70_out, or_63_out);
  and and_115 (and_115_out, xor_70_out, or_63_out);
  xor xor_75 (xor_75_out, xor_71_out, or_64_out);
  and and_116 (and_116_out, xor_71_out, or_64_out);
  xor xor_76 (xor_76_out, xor_72_out, or_53_out);
  and and_117 (and_117_out, xor_72_out, or_53_out);
  xor xor_77 (xor_77_out, xor_65_out, or_58_out);
  or or_57 (or_57_out, and_106_out, and_118_out);
  and and_118 (and_118_out, xor_65_out, or_58_out);
  xor xor_78 (xor_78_out, xor_66_out, or_59_out);
  or or_58 (or_58_out, and_107_out, and_119_out);
  and and_119 (and_119_out, xor_66_out, or_59_out);
  xor xor_79 (xor_79_out, xor_67_out, or_60_out);
  or or_59 (or_59_out, and_108_out, and_120_out);
  and and_120 (and_120_out, xor_67_out, or_60_out);
  xor xor_80 (xor_80_out, xor_68_out, or_49_out);
  or or_60 (or_60_out, and_109_out, and_121_out);
  and and_121 (and_121_out, xor_68_out, or_49_out);
  or or_61 (or_61_out, and_110_out, and_114_out);
  or or_62 (or_62_out, and_111_out, and_115_out);
  or or_63 (or_63_out, and_112_out, and_116_out);
  or or_64 (or_64_out, and_113_out, and_117_out);
  xor xor_81 (xor_81_out, not_18_out, or_75_out);
  RAM #(.addrWidth(16), .trigger("high")) ram_1 (
    .addr(d_ff_40_q), .we(and_44_out), .din(or_48_out), .dout(ram_1_dout));  // open: oe
  not not_18 (not_18_out, FORWARD_if1);
  and and_122 (and_122_out, d_ff_40_q[11], and_42_out);
  and and_123 (and_123_out, d_ff_40_q[10], and_42_out);
  and and_124 (and_124_out, d_ff_40_q[9], and_42_out);
  and and_125 (and_125_out, d_ff_40_q[8], and_42_out);
  xor xor_82 (xor_82_out, d_ff_40_q[11], and_42_out);
  xor xor_83 (xor_83_out, d_ff_40_q[10], and_42_out);
  xor xor_84 (xor_84_out, d_ff_40_q[9], and_42_out);
  xor xor_85 (xor_85_out, d_ff_40_q[8], and_42_out);
  xor xor_86 (xor_86_out, xor_82_out, or_66_out);
  and and_126 (and_126_out, xor_82_out, or_66_out);
  xor xor_87 (xor_87_out, xor_83_out, or_67_out);
  and and_127 (and_127_out, xor_83_out, or_67_out);
  xor xor_88 (xor_88_out, xor_84_out, or_68_out);
  and and_128 (and_128_out, xor_84_out, or_68_out);
  xor xor_89 (xor_89_out, xor_85_out, or_57_out);
  and and_129 (and_129_out, xor_85_out, or_57_out);
  or or_65 (or_65_out, and_122_out, and_126_out);
  or or_66 (or_66_out, and_123_out, and_127_out);
  or or_67 (or_67_out, and_124_out, and_128_out);
  or or_68 (or_68_out, and_125_out, and_129_out);
  assign bit_extender_2_out = {{7{or_22_out}}, or_22_out};  // Bit_Extender bit_extender_2
  assign and_130_out = bit_extender_2_out & ram_1_dout;  // AND_Gate and_130, 8 bits wide
  or or_69 (or_69_out, and_130_out[7], and_130_out[6]);
  or or_70 (or_70_out, or_69_out, or_74_out);
  and and_131 (and_131_out, d_ff_40_q[15], and_42_out);
  xor xor_90 (xor_90_out, d_ff_40_q[15], and_42_out);
  and and_132 (and_132_out, d_ff_40_q[14], and_42_out);
  xor xor_91 (xor_91_out, d_ff_40_q[14], and_42_out);
  and and_133 (and_133_out, d_ff_40_q[13], and_42_out);
  xor xor_92 (xor_92_out, d_ff_40_q[13], and_42_out);
  and and_134 (and_134_out, d_ff_40_q[12], and_42_out);
  xor xor_93 (xor_93_out, d_ff_40_q[12], and_42_out);
  or or_71 (or_71_out, and_130_out[1], and_130_out[0]);
  or or_72 (or_72_out, and_130_out[3], and_130_out[2]);
  or or_73 (or_73_out, or_72_out, or_71_out);
  or or_74 (or_74_out, and_130_out[5], and_130_out[4]);
  or or_75 (or_75_out, or_70_out, or_73_out);
  xor xor_94 (xor_94_out, xor_90_out, or_77_out);
  and and_135 (and_135_out, xor_90_out, or_77_out);
  xor xor_95 (xor_95_out, xor_91_out, or_78_out);
  and and_136 (and_136_out, xor_91_out, or_78_out);
  xor xor_96 (xor_96_out, xor_92_out, or_79_out);
  and and_137 (and_137_out, xor_92_out, or_79_out);
  xor xor_97 (xor_97_out, xor_93_out, or_65_out);
  and and_138 (and_138_out, xor_93_out, or_65_out);
  TTY #(.trigger("falling")) tty_1 (.data(and_130_out[6:0]), .clk(and_46_out), .we(1'b1));  // open: clr
  or or_76 (or_76_out, and_131_out, and_135_out);
  or or_77 (or_77_out, and_132_out, and_136_out);
  or or_78 (or_78_out, and_133_out, and_137_out);
  or or_79 (or_79_out, and_134_out, and_138_out);

  // Notes on the sheet:
  //   contents of rom_1 (hex, n*v repeats v):
  //   8*0 6 2 8*0 3 1 7 2 8*0 4 2 8*0 6 2 12*0 3 1 7 2 5*0 4 7*0 4 4 0 0 0 4 2 8*0 6 2 5*0 3 1 7 2 4*0 4
  //   12*1 4 4*3 15*0 4 2 2 4 0 0 0 4 6*1 4 8*1 4 2 2 0 4 6*2
endmodule

module BRACKETCOUNT2 (
  input  in_1,
  input  in_2,
  input  in_3,
  input  in_4,
  input  in_5,
  input  in_6,
  input  in_7,
  input  in_8,
  output out_9
);

  wire and_1_out, and_2_out, and_3_out, and_4_out, and_5_out, and_6_out, and_7_out, and_8_out, and_9_out,
       and_10_out, and_11_out, and_12_out, and_13_out, and_14_out, and_15_out, and_16_out, d_ff_1_q,
       d_ff_2_q, d_ff_3_q, d_ff_4_q, d_ff_5_q, d_ff_6_q, d_ff_7_q, d_ff_8_q, or_1_out, or_2_out, or_3_out,
       or_4_out, or_5_out, or_6_out, or_7_out, or_8_out, or_9_out, or_10_out, or_11_out, or_12_out,
       or_13_out, or_14_out, or_15_out, undriven, undriven_2, undriven_3, xor_1_out, xor_2_out, xor_3_out,
       xor_4_out, xor_5_out, xor_6_out, xor_7_out, xor_8_out, xor_9_out, xor_10_out, xor_11_out, xor_12_out,
       xor_13_out, xor_14_out, xor_15_out, xor_16_out;

  D_Flip_Flop d_ff_1 (.D(xor_8_out), .clk(undriven), .Q(d_ff_1_q));  // open: Qn, preset, reset
  D_Flip_Flop d_ff_2 (.D(xor_5_out), .clk(undriven), .Q(d_ff_2_q));  // open: Qn, preset, reset
  D_Flip_Flop d_ff_3 (.D(xor_6_out), .clk(undriven), .Q(d_ff_3_q));  // open: Qn, preset, reset
  D_Flip_Flop d_ff_4 (.D(xor_7_out), .clk(undriven), .Q(d_ff_4_q));  // open: Qn, preset, reset
  D_Flip_Flop d_ff_5 (.D(xor_13_out), .clk(undriven), .Q(d_ff_5_q));  // open: Qn, preset, reset
  D_Flip_Flop d_ff_6 (.D(xor_14_out), .clk(undriven), .Q(d_ff_6_q));  // open: Qn, preset, reset
  D_Flip_Flop d_ff_7 (.D(xor_15_out), .clk(undriven), .Q(d_ff_7_q));  // open: Qn, preset, reset
  D_Flip_Flop d_ff_8 (.D(xor_16_out), .clk(undriven), .Q(d_ff_8_q));  // open: Qn, preset, reset
  and and_1 (and_1_out, d_ff_2_q, undriven_2);
  xor xor_1 (xor_1_out, d_ff_2_q, undriven_2);
  and and_2 (and_2_out, d_ff_3_q, undriven_2);
  xor xor_2 (xor_2_out, d_ff_3_q, undriven_2);
  and and_3 (and_3_out, d_ff_4_q, undriven_2);
  xor xor_3 (xor_3_out, d_ff_4_q, undriven_2);
  and and_4 (and_4_out, d_ff_1_q, undriven_2);
  xor xor_4 (xor_4_out, d_ff_1_q, undriven_2);
  xor xor_5 (xor_5_out, xor_1_out, or_2_out);
  and and_5 (and_5_out, xor_1_out, or_2_out);
  xor xor_6 (xor_6_out, xor_2_out, or_3_out);
  and and_6 (and_6_out, xor_2_out, or_3_out);
  xor xor_7 (xor_7_out, xor_3_out, or_4_out);
  and and_7 (and_7_out, xor_3_out, or_4_out);
  xor xor_8 (xor_8_out, xor_4_out, undriven_3);
  and and_8 (and_8_out, xor_4_out, undriven_3);
  or or_1 (or_1_out, and_1_out, and_5_out);
  or or_2 (or_2_out, and_2_out, and_6_out);
  or or_3 (or_3_out, and_3_out, and_7_out);
  or or_4 (or_4_out, and_4_out, and_8_out);
  or or_5 (or_5_out, in_1, in_2);
  or or_6 (or_6_out, in_3, in_4);
  or or_7 (or_7_out, in_5, in_6);
  or or_8 (or_8_out, in_7, in_8);
  or or_9 (or_9_out, or_5_out, or_6_out);
  or or_10 (or_10_out, or_7_out, or_8_out);
  and and_9 (and_9_out, d_ff_5_q, undriven_2);
  xor xor_9 (xor_9_out, d_ff_5_q, undriven_2);
  and and_10 (and_10_out, d_ff_6_q, undriven_2);
  xor xor_10 (xor_10_out, d_ff_6_q, undriven_2);
  and and_11 (and_11_out, d_ff_7_q, undriven_2);
  xor xor_11 (xor_11_out, d_ff_7_q, undriven_2);
  and and_12 (and_12_out, d_ff_8_q, undriven_2);
  xor xor_12 (xor_12_out, d_ff_8_q, undriven_2);
  or or_11 (or_11_out, or_9_out, or_10_out);
  xor xor_13 (xor_13_out, xor_9_out, or_13_out);
  and and_13 (and_13_out, xor_9_out, or_13_out);
  xor xor_14 (xor_14_out, xor_10_out, or_14_out);
  and and_14 (and_14_out, xor_10_out, or_14_out);
  xor xor_15 (xor_15_out, xor_11_out, or_15_out);
  and and_15 (and_15_out, xor_11_out, or_15_out);
  xor xor_16 (xor_16_out, xor_12_out, or_1_out);
  and and_16 (and_16_out, xor_12_out, or_1_out);
  not not_1 (out_9, or_11_out);
  or or_12 (or_12_out, and_9_out, and_13_out);
  or or_13 (or_13_out, and_10_out, and_14_out);
  or or_14 (or_14_out, and_11_out, and_15_out);
  or or_15 (or_15_out, and_12_out, and_16_out);
endmodule

module ROMARCHI2 (
  input  plus,
  input  minus,
  input  NEXTINS,
  input  PREVIOUSINS,
  input  UPDATE,
  output INS1,
  output INS2,
  output INS3
);

  wire and_1_out, and_2_out, and_3_out, and_4_out, and_5_out, and_6_out, and_7_out, and_8_out, and_9_out,
       and_10_out, and_11_out, and_12_out, and_13_out, and_14_out, and_15_out, and_16_out, and_17_out,
       and_18_out, and_19_out, and_20_out, and_21_out, and_22_out, and_23_out, and_24_out, and_25_out,
       and_26_out, and_27_out, and_28_out, and_29_out, and_30_out, and_31_out, and_32_out, or_1_out,
       or_2_out, or_3_out, or_4_out, or_5_out, or_6_out, or_7_out, or_8_out, or_9_out, or_10_out, or_11_out,
       or_12_out, or_13_out, or_14_out, or_15_out, or_16_out, undriven, undriven_2, undriven_3, undriven_4,
       undriven_5, undriven_6, undriven_7, undriven_8, undriven_9, undriven_10, undriven_11, undriven_12,
       undriven_13, undriven_14, undriven_15, undriven_16, undriven_17, xor_1_out, xor_2_out, xor_3_out,
       xor_4_out, xor_5_out, xor_6_out, xor_7_out, xor_8_out, xor_9_out, xor_10_out, xor_11_out, xor_12_out,
       xor_13_out, xor_14_out, xor_15_out, xor_16_out, xor_17_out, xor_18_out, xor_19_out, xor_20_out,
       xor_21_out, xor_22_out, xor_23_out, xor_24_out, xor_25_out, xor_26_out, xor_27_out, xor_28_out,
       xor_29_out, xor_30_out, xor_31_out, xor_32_out;
  wire [15:0] adressemap2_1_b1;

  and and_1 (and_1_out, undriven_8, minus);
  xor xor_1 (xor_1_out, undriven_8, minus);
  and and_2 (and_2_out, undriven_7, minus);
  xor xor_2 (xor_2_out, undriven_7, minus);
  and and_3 (and_3_out, undriven_6, minus);
  xor xor_3 (xor_3_out, undriven_6, minus);
  and and_4 (and_4_out, undriven_5, minus);
  xor xor_4 (xor_4_out, undriven_5, minus);
  xor xor_5 (xor_5_out, xor_1_out, or_2_out);
  and and_5 (and_5_out, xor_1_out, or_2_out);
  xor xor_6 (xor_6_out, xor_2_out, or_3_out);
  and and_6 (and_6_out, xor_2_out, or_3_out);
  xor xor_7 (xor_7_out, xor_3_out, or_4_out);
  and and_7 (and_7_out, xor_3_out, or_4_out);
  xor xor_8 (xor_8_out, xor_4_out, plus);
  and and_8 (and_8_out, xor_4_out, plus);
  or or_1 (or_1_out, and_1_out, and_5_out);
  or or_2 (or_2_out, and_2_out, and_6_out);
  or or_3 (or_3_out, and_3_out, and_7_out);
  or or_4 (or_4_out, and_4_out, and_8_out);
  and and_9 (and_9_out, undriven_12, minus);
  xor xor_9 (xor_9_out, undriven_12, minus);
  and and_10 (and_10_out, undriven_11, minus);
  xor xor_10 (xor_10_out, undriven_11, minus);
  and and_11 (and_11_out, undriven_10, minus);
  xor xor_11 (xor_11_out, undriven_10, minus);
  and and_12 (and_12_out, undriven_9, minus);
  xor xor_12 (xor_12_out, undriven_9, minus);
  xor xor_13 (xor_13_out, xor_9_out, or_6_out);
  and and_13 (and_13_out, xor_9_out, or_6_out);
  xor xor_14 (xor_14_out, xor_10_out, or_7_out);
  and and_14 (and_14_out, xor_10_out, or_7_out);
  xor xor_15 (xor_15_out, xor_11_out, or_8_out);
  and and_15 (and_15_out, xor_11_out, or_8_out);
  xor xor_16 (xor_16_out, xor_12_out, or_1_out);
  and and_16 (and_16_out, xor_12_out, or_1_out);
  or or_5 (or_5_out, and_9_out, and_13_out);
  or or_6 (or_6_out, and_10_out, and_14_out);
  or or_7 (or_7_out, and_11_out, and_15_out);
  or or_8 (or_8_out, and_12_out, and_16_out);
  and and_17 (and_17_out, undriven_16, or_5_out);
  xor xor_17 (xor_17_out, undriven_16, or_5_out);
  and and_18 (and_18_out, undriven_15, or_5_out);
  xor xor_18 (xor_18_out, undriven_15, or_5_out);
  and and_19 (and_19_out, undriven_14, or_5_out);
  xor xor_19 (xor_19_out, undriven_14, or_5_out);
  and and_20 (and_20_out, undriven_13, or_5_out);
  xor xor_20 (xor_20_out, undriven_13, or_5_out);
  xor xor_21 (xor_21_out, xor_17_out, or_10_out);
  and and_21 (and_21_out, xor_17_out, or_10_out);
  xor xor_22 (xor_22_out, xor_18_out, or_11_out);
  and and_22 (and_22_out, xor_18_out, or_11_out);
  xor xor_23 (xor_23_out, xor_19_out, or_12_out);
  and and_23 (and_23_out, xor_19_out, or_12_out);
  xor xor_24 (xor_24_out, xor_20_out, undriven_17);
  and and_24 (and_24_out, xor_20_out, undriven_17);
  or or_9 (or_9_out, and_17_out, and_21_out);
  or or_10 (or_10_out, and_18_out, and_22_out);
  or or_11 (or_11_out, and_19_out, and_23_out);
  or or_12 (or_12_out, and_20_out, and_24_out);
  and and_25 (and_25_out, undriven, or_5_out);
  xor xor_25 (xor_25_out, undriven, or_5_out);
  and and_26 (and_26_out, undriven_2, or_5_out);
  xor xor_26 (xor_26_out, undriven_2, or_5_out);
  and and_27 (and_27_out, undriven_3, or_5_out);
  xor xor_27 (xor_27_out, undriven_3, or_5_out);
  and and_28 (and_28_out, undriven_4, or_5_out);
  xor xor_28 (xor_28_out, undriven_4, or_5_out);
  xor xor_29 (xor_29_out, xor_25_out, or_14_out);
  xor xor_30 (xor_30_out, xor_26_out, or_15_out);
  xor xor_31 (xor_31_out, xor_27_out, or_16_out);
  xor xor_32 (xor_32_out, xor_28_out, or_9_out);
  or or_13 (or_13_out, and_25_out, and_29_out);
  and and_29 (and_29_out, xor_25_out, or_14_out);
  or or_14 (or_14_out, and_26_out, and_30_out);
  and and_30 (and_30_out, xor_26_out, or_15_out);
  or or_15 (or_15_out, and_27_out, and_31_out);
  and and_31 (and_31_out, xor_27_out, or_16_out);
  or or_16 (or_16_out, and_28_out, and_32_out);
  and and_32 (and_32_out, xor_28_out, or_9_out);
  ADRESSEMAP2 adressemap2_1 (
    .NEXT_CELL(NEXTINS), .PREVIOUS_CELL(PREVIOUSINS), .UPDATE(UPDATE), .B65536(adressemap2_1_b1[15]),
    .out_5(adressemap2_1_b1[14]), .out_6(adressemap2_1_b1[13]), .out_7(adressemap2_1_b1[12]),
    .out_8(adressemap2_1_b1[11]), .out_9(adressemap2_1_b1[10]), .out_10(adressemap2_1_b1[9]),
    .out_11(adressemap2_1_b1[8]), .out_12(adressemap2_1_b1[7]), .out_13(adressemap2_1_b1[6]),
    .out_14(adressemap2_1_b1[5]), .out_15(adressemap2_1_b1[4]), .out_16(adressemap2_1_b1[3]),
    .out_17(adressemap2_1_b1[2]), .out_18(adressemap2_1_b1[1]), .B1(adressemap2_1_b1[0]));  // open: OVERFLOW
  ROM #(.addrWidth(16), .dataWidth(3)) rom_1 (.addr(adressemap2_1_b1), .data({INS3, INS2, INS1}));

  // Notes on the sheet:
  //   contents of rom_1 (hex, n*v repeats v):
  //   4 0 6 4 0 7
endmodule
